// Digital circuit ALU.dig as structural Verilog
module ALU (
  input  [3:0] ALU_ctrl,
  input  [31:0] A,
  input  [31:0] B,
  output [31:0] Y,
  output Z
);

  wire and_1_out, and_2_out, and_3_out, and_4_out, and_5_out, bit0__30_c_o, C_out, not_1_out, not_3_out,
       or_1_out, or_2_out, over, Result_SLT, xor_1_out;
  wire [30:0] multiplexer_2_out;
  wire [31:0] and_6_out, not_2_out, or_4_out, Reseult_logic, Result_arith, Result_shift, xor_3_out;
  wire [31:1] pulldown_1_out;
  wire [31:31] multiplexer_2_out_2;

  PullDown #(.Bits(31)) pulldown_1 (.out(pulldown_1_out));
  Multiplexer #(.Selector_Bits(2), .Bits(32)) multiplexer_1 (
    .sel(ALU_ctrl[1:0]), .in_0(Result_arith), .in_1(Reseult_logic), .in_2(Result_shift),
    .in_3({pulldown_1_out, Result_SLT}), .out(Y));
  nor nor_1 (Z, Y[15], Y[14], Y[13], Y[12], Y[11], Y[10], Y[9], Y[8], Y[7], Y[6], Y[5], Y[4], Y[3], Y[2], Y[1], Y[0], Y[16], Y[17], Y[18], Y[19], Y[20], Y[21], Y[22], Y[23], Y[24], Y[25], Y[26], Y[27], Y[28], Y[29], Y[30], Y[31]);
  // Probe on Y
  not not_1 (not_1_out, ALU_ctrl[2]);
  and and_1 (and_1_out, ALU_ctrl[0], ALU_ctrl[1]);
  assign not_2_out = ~B;  // Not not_2, 32 bits wide
  or or_1 (or_1_out, ALU_ctrl[2], and_1_out);
  Multiplexer #(.Bits(32)) multiplexer_2 (
    .sel(or_1_out), .in_0(B), .in_1(not_2_out), .out({multiplexer_2_out_2[31], multiplexer_2_out}));
  and and_2 (and_2_out, ALU_ctrl[2], not_3_out);
  not not_3 (not_3_out, C_out);
  xor xor_1 (xor_1_out, Result_arith[31], over);
  and and_3 (and_3_out, not_1_out, xor_1_out);
  Add #(.Bits(31)) bit0__30 (
    .a(A[30:0]), .b(multiplexer_2_out), .c_i(or_1_out), .s(Result_arith[30:0]), .c_o(bit0__30_c_o));
  Add bit31 (.a(A[31]), .b(multiplexer_2_out_2[31]), .c_i(bit0__30_c_o), .s(Result_arith[31]), .c_o(C_out));
  and and_4 (and_4_out, ~Result_arith[31], multiplexer_2_out_2[31], A[31]);  // And
  and and_5 (and_5_out, Result_arith[31], ~multiplexer_2_out_2[31], ~A[31]);  // And
  or or_2 (or_2_out, and_4_out, and_5_out);
  xor xor_2 (over, C_out, bit0__30_c_o);
  or or_3 (Result_SLT, and_2_out, and_3_out);
  ALU_BarrelShifter alu_barrelshifter_1 (.in(A), .op(ALU_ctrl[3:2]), .shamt(B[4:0]), .out(Result_shift));
  assign xor_3_out = A ^ B;  // XOr xor_3, 32 bits wide
  assign or_4_out = A | B;  // Or or_4, 32 bits wide
  assign and_6_out = A & B;  // And and_6, 32 bits wide
  Multiplexer #(.Selector_Bits(2), .Bits(32)) multiplexer_3 (
    .sel(ALU_ctrl[3:2]), .in_0(xor_3_out), .in_1(or_4_out), .in_2(and_6_out), .in_3({32{1'b0}}),
    .out(Reseult_logic));

  // Other names for the same wires on the sheet: op_01[1:0] = ALU_ctrl[1:0]; op_2 = ALU_ctrl[2];
  //   op_23[1:0] = ALU_ctrl[3:2]; Input_A[31:0] = A; Input_B[31:0] = B

  // Notes on the sheet:
  //   Inputs
  //   Output (Result)
  //   Output (Zero-Flag)
  //   ALU-Operation
  //   u0-00   ADD
  //   u1-00   SUB
  //   00-01   XOR
  //   01-01   OR
  //   10-01   AND
  //   u0-11   SLT
  //   u1-11   SLTU
  //   00-10   SLL
  //   10-10   SRL
  //   11-10   SRA
  //   Arithmetic (ADD/SUB)
  //   Comparator (SLT/SLTU)
  //   SLT and SLTU:
  //   ==============
  //   For  unsigned  comparison  of  two  numbers  A  and  B,  we need to perform a subtraction operation, A - B,
  //   and then check whether we have a Carry-Out (Cout) or not. If Carry-Out=0, this means that there was a
  //   borrow when B is subtracted from A and thus A < B. However, if Carry-Out=1 then this implies that there
  //   was no borrow and hence A ≥ B.
  //   Similarly, for comparing signed numbers A and B, we perform the subtraction operation A – B and then
  //   we check both the Sign of the result and the Overflow signal. The Sign of the result is the most
  //   significant bit of the result (i.e. bit 31). If the Sign value is not equal to the Overflow value, then  A < B,
  //   otherwise, A ≥ B. This can be done by XORing the Sign and the Overflow signals. If the result is 1,
  //   this means that A < B.
  //   Overflow:
  //   ========
  //   see also:
  //   https://stackoverflow.com/questions/34534304/calculating-the-overflow-flag-in-an-alu
  //   SLTU
  //   SLT
  //   Shift (SLL/SRL/SRA)
  //   Logic (XOR/OR/AND)
  //   TODO: ist "overflow" überhaupt nötig? wann wird es jemals "1"?
  //   DONE: ja, ist es.
  //   Test: 4 - (-4) = 8 (overflow) .... nutze die obersten 4 bit von a/b
endmodule
