// Digital circuit BasicAdder.dig as structural Verilog
module BasicAdder (
  input  [31:0] A,
  input  [31:0] B,
  output [31:0] Y
);

  Add #(.Bits(32)) add_1 (.a(A), .b(B), .c_i(1'b0), .s(Y));  // open: c_o
endmodule
