// Digital circuit ALU_BarrelShifter.dig as structural Verilog
module ALU_BarrelShifter (
  input  [31:0] in,
  input  [1:0] op,
  input  [4:0] shamt,
  output [31:0] out
);

  wire not_1_out;
  wire [0:0] multiplexer_6_out;
  wire [31:0] multiplexer_1_out, multiplexer_2_out, multiplexer_3_out, multiplexer_4_out, multiplexer_5_out,
       multiplexer_7_out;

  LED led_1 (.in(in[28]));
  LED led_2 (.in(in[29]));
  LED led_3 (.in(in[30]));
  LED led_4 (.in(in[31]));
  LED led_5 (.in(out[31]));
  LED led_6 (.in(out[30]));
  LED led_7 (.in(out[29]));
  LED led_8 (.in(out[28]));
  not not_1 (not_1_out, op[1]);
  LED led_9 (.in(in[24]));
  LED led_10 (.in(in[25]));
  LED led_11 (.in(in[26]));
  LED led_12 (.in(in[27]));
  LED led_13 (.in(out[27]));
  LED led_14 (.in(out[26]));
  LED led_15 (.in(out[25]));
  LED led_16 (.in(out[24]));
  LED right (.in(op[1]));
  LED left (.in(not_1_out));
  LED arithmetic (.in(op[0]));
  Multiplexer multiplexer_1 (.sel(op[0]), .in_0(1'b0), .in_1(in[31]), .out(multiplexer_1_out[31]));
  LED led_17 (.in(in[20]));
  LED led_18 (.in(in[21]));
  LED led_19 (.in(in[22]));
  LED led_20 (.in(in[23]));
  LED led_21 (.in(out[23]));
  LED led_22 (.in(out[22]));
  LED led_23 (.in(out[21]));
  LED led_24 (.in(out[20]));
  Multiplexer #(.Bits(32)) multiplexer_2 (
    .sel(not_1_out), .in_0(in),
    .in_1({in[0], in[1], in[2], in[3], in[4], in[5], in[6], in[7], in[8], in[9], in[10], in[11], in[12], in[13], in[14], in[15], in[16], in[17], in[18], in[19], in[20], in[21], in[22], in[23], in[24], in[25], in[26], in[27], in[28], in[29], in[30], in[31]}),
    .out(multiplexer_2_out));
  LED led_25 (.in(in[16]));
  LED led_26 (.in(in[17]));
  LED led_27 (.in(in[18]));
  LED led_28 (.in(in[19]));
  LED led_29 (.in(out[19]));
  LED led_30 (.in(out[18]));
  LED led_31 (.in(out[17]));
  LED led_32 (.in(out[16]));
  LED led_33 (.in(in[12]));
  LED led_34 (.in(in[13]));
  LED led_35 (.in(in[14]));
  LED led_36 (.in(in[15]));
  LED led_37 (.in(out[15]));
  LED led_38 (.in(out[14]));
  LED led_39 (.in(out[13]));
  LED led_40 (.in(out[12]));
  LED led_41 (.in(in[8]));
  LED led_42 (.in(in[9]));
  LED led_43 (.in(in[10]));
  LED led_44 (.in(in[11]));
  LED led_45 (.in(out[11]));
  LED led_46 (.in(out[10]));
  LED led_47 (.in(out[9]));
  LED led_48 (.in(out[8]));
  Multiplexer #(.Bits(32)) multiplexer_3 (
    .sel(shamt[4]), .in_0(multiplexer_2_out), .in_1({{16{multiplexer_1_out[31]}}, multiplexer_2_out[31:16]}),
    .out(multiplexer_3_out));
  LED led_49 (.in(in[4]));
  LED led_50 (.in(in[5]));
  LED led_51 (.in(in[6]));
  LED led_52 (.in(in[7]));
  LED led_53 (.in(out[7]));
  LED led_54 (.in(out[6]));
  LED led_55 (.in(out[5]));
  LED led_56 (.in(out[4]));
  LED led_57 (.in(in[0]));
  LED led_58 (.in(in[1]));
  LED led_59 (.in(in[2]));
  LED led_60 (.in(in[3]));
  LED led_61 (.in(out[3]));
  LED led_62 (.in(out[2]));
  LED led_63 (.in(out[1]));
  LED led_64 (.in(out[0]));
  Multiplexer #(.Bits(32)) multiplexer_4 (
    .sel(shamt[3]), .in_0(multiplexer_3_out), .in_1({{8{multiplexer_1_out[31]}}, multiplexer_3_out[31:8]}),
    .out(multiplexer_4_out));
  Multiplexer #(.Bits(32)) multiplexer_5 (
    .sel(shamt[2]), .in_0(multiplexer_4_out), .in_1({{4{multiplexer_1_out[31]}}, multiplexer_4_out[31:4]}),
    .out(multiplexer_5_out));
  Multiplexer #(.Bits(32)) multiplexer_6 (
    .sel(shamt[1]), .in_0(multiplexer_5_out), .in_1({{2{multiplexer_1_out[31]}}, multiplexer_5_out[31:2]}),
    .out({multiplexer_1_out[30:0], multiplexer_6_out[0]}));
  Multiplexer #(.Bits(32)) multiplexer_7 (
    .sel(shamt[0]), .in_0({multiplexer_1_out[30:0], multiplexer_6_out[0]}), .in_1(multiplexer_1_out),
    .out(multiplexer_7_out));
  Multiplexer #(.Bits(32)) multiplexer_8 (
    .sel(not_1_out), .in_0(multiplexer_7_out),
    .in_1({multiplexer_7_out[0], multiplexer_7_out[1], multiplexer_7_out[2], multiplexer_7_out[3], multiplexer_7_out[4], multiplexer_7_out[5], multiplexer_7_out[6], multiplexer_7_out[7], multiplexer_7_out[8], multiplexer_7_out[9], multiplexer_7_out[10], multiplexer_7_out[11], multiplexer_7_out[12], multiplexer_7_out[13], multiplexer_7_out[14], multiplexer_7_out[15], multiplexer_7_out[16], multiplexer_7_out[17], multiplexer_7_out[18], multiplexer_7_out[19], multiplexer_7_out[20], multiplexer_7_out[21], multiplexer_7_out[22], multiplexer_7_out[23], multiplexer_7_out[24], multiplexer_7_out[25], multiplexer_7_out[26], multiplexer_7_out[27], multiplexer_7_out[28], multiplexer_7_out[29], multiplexer_7_out[30], multiplexer_7_out[31]}),
    .out(out));

  // Notes on the sheet:
  //   00   SLL
  //   10   SRL
  //   11   SRA
endmodule
