// Digital circuit Branch.Unit.dig as structural Verilog
module Branch_Unit (
  input  [31:0] Imm,
  input  [31:0] PC,
  input  Branch,
  input  [1:0] BR_ctrl,
  input  ALU_zero,
  input  ALU_SLT,
  output BR_taken,
  output [31:0] BR_addr
);

  wire and_1_out, and_2_out, and_3_out, and_4_out, or_1_out, or_2_out;

  and and_1 (and_1_out, ~BR_ctrl[1], ALU_zero);  // And
  and and_2 (and_2_out, ALU_SLT, BR_ctrl[1]);
  BasicAdder basicadder_1 (.A(Imm), .B(PC), .Y(BR_addr));
  or or_1 (or_1_out, and_1_out, and_2_out);
  and and_3 (and_3_out, ~BR_ctrl[0], or_1_out);  // And
  and and_4 (and_4_out, ~or_1_out, BR_ctrl[0]);  // And
  or or_2 (or_2_out, and_3_out, and_4_out);
  and and_5 (BR_taken, or_2_out, Branch);
endmodule
