// Digital circuit FowardUnit.dig as structural Verilog
module FowardUnit (
  input  [4:0] ID_Rs1,
  input  [4:0] ID_Rs2,
  input  [4:0] Exe_rd,
  input  Exe_we,
  input  [4:0] Mem_rd,
  input  Mem_we,
  input  Exe_Memrd,
  input  [4:0] ID_stall,
  output [1:0] A_mux,
  output [1:0] B_mux
);

  wire A0_out, A1_out, A2_out, A3_out, A4_out, and_1_out, and_4_out, and_6_out, and_8_out, and_9_out,
       and_10_out, and_11_out, B0_out, B1_out, B2_out, B3_out, B4_out, comparator_1_eq, comparator_2_eq,
       comparator_3_eq, comparator_4_eq, or_1_out, or_2_out, xnor_1_out, xnor_2_out, xnor_3_out, xnor_4_out,
       xnor_5_out;

  nor nor_1 (ID_stall[0], and_6_out, and_4_out);
  Comparator #(.Bits(5)) comparator_1 (.a(Exe_rd), .b(ID_Rs1), .eq(comparator_1_eq));  // open: gt, lt
  Comparator #(.Bits(5)) comparator_2 (.a(Exe_rd), .b(ID_Rs2), .eq(comparator_2_eq));  // open: gt, lt
  and and_1 (and_1_out, Exe_we, or_1_out);
  and and_2 (A_mux[0], and_1_out, comparator_1_eq);
  and and_3 (B_mux[0], and_1_out, comparator_2_eq);
  or or_1 (or_1_out, Exe_rd[0], Exe_rd[1], Exe_rd[2], Exe_rd[3], Exe_rd[4]);
  and and_4 (and_4_out, A_mux[0], Exe_Memrd);
  and and_5 (A_mux[1], and_9_out, ~A_mux[0]);  // And
  and and_6 (and_6_out, B_mux[0], Exe_Memrd);
  and and_7 (B_mux[1], and_10_out, ~B_mux[0]);  // And
  Comparator #(.Bits(5)) comparator_3 (.a(Mem_rd), .b(ID_Rs1), .eq(comparator_3_eq));  // open: gt, lt
  Comparator #(.Bits(5)) comparator_4 (.a(Mem_rd), .b(ID_Rs2), .eq(comparator_4_eq));  // open: gt, lt
  and and_8 (and_8_out, Mem_we, or_2_out);
  and and_9 (and_9_out, and_8_out, comparator_3_eq);
  and and_10 (and_10_out, and_8_out, comparator_4_eq);
  or or_2 (or_2_out, Mem_rd[0], Mem_rd[1], Mem_rd[2], Mem_rd[3], Mem_rd[4]);
  DipSwitch A0 (.out(A0_out));
  DipSwitch B0 (.out(B0_out));
  DipSwitch A1 (.out(A1_out));
  DipSwitch B1 (.out(B1_out));
  DipSwitch A2 (.out(A2_out));
  DipSwitch B2 (.out(B2_out));
  DipSwitch A3 (.out(A3_out));
  DipSwitch B3 (.out(B3_out));
  DipSwitch A4 (.out(A4_out));
  DipSwitch B4 (.out(B4_out));
  xnor xnor_1 (xnor_1_out, A0_out, B0_out);
  xnor xnor_2 (xnor_2_out, A1_out, B1_out);
  xnor xnor_3 (xnor_3_out, A2_out, B2_out);
  xnor xnor_4 (xnor_4_out, A3_out, B3_out);
  xnor xnor_5 (xnor_5_out, A4_out, B4_out);
  and and_11 (and_11_out, xnor_1_out, xnor_2_out, xnor_3_out, xnor_4_out, xnor_5_out);
  // Pins of 1 and 5 bits meet at ID_stall

  // Notes on the sheet:
  //   A_mux
  //   B_mux
  //   Exe_rd != 0
  //   A_stall
  //   Exe has higher priority
  //   B_stall
  //   Mem_rd != 0
  //   Comparator (5bit)
  //   A=B
endmodule
