// Digital circuit Imm.Decoder.dig as structural Verilog
module Imm_Decoder (
  input  [2:0] Ctrl,
  input  [31:0] Inst,
  output [31:0] Imm
);

  wire B_type, I_type, J_type, R_type__unused, S_type, U_type;

  Decoder #(.Selector_Bits(3)) decoder_1 (
    .sel(Ctrl), .out_0(R_type__unused), .out_1(I_type), .out_2(S_type), .out_3(B_type), .out_4(U_type),
    .out_5(J_type));  // open: out_6, out_7
  assign Imm = I_type ? {{21{Inst[31]}}, Inst[30:20]} : 32'bz;  // Driver driver_1
  assign Imm = S_type ? {{21{Inst[31]}}, Inst[30:25], Inst[11:7]} : 32'bz;  // Driver driver_2
  assign Imm = B_type ? {{20{Inst[31]}}, Inst[7], Inst[30:25], Inst[11:8], 1'b0} : 32'bz;  // Driver driver_3
  LED led_1 (.in(Imm[31]));
  LED led_2 (.in(Imm[30]));
  LED led_3 (.in(Imm[29]));
  LED led_4 (.in(Imm[28]));
  LED led_5 (.in(Imm[27]));
  LED led_6 (.in(Imm[26]));
  LED led_7 (.in(Imm[25]));
  LED led_8 (.in(Imm[24]));
  LED led_9 (.in(Imm[23]));
  LED led_10 (.in(Imm[22]));
  LED led_11 (.in(Imm[21]));
  LED led_12 (.in(Imm[20]));
  LED led_13 (.in(Imm[19]));
  LED led_14 (.in(Imm[18]));
  assign Imm = U_type ? {Inst[31:12], {12{1'b0}}} : 32'bz;  // Driver driver_4
  LED led_15 (.in(Imm[17]));
  LED led_16 (.in(Imm[16]));
  LED led_17 (.in(Imm[15]));
  LED led_18 (.in(Imm[14]));
  LED led_19 (.in(Imm[13]));
  LED led_20 (.in(Imm[12]));
  LED led_21 (.in(Imm[11]));
  LED led_22 (.in(Imm[10]));
  LED led_23 (.in(Imm[9]));
  LED led_24 (.in(Imm[8]));
  LED led_25 (.in(Imm[7]));
  LED led_26 (.in(Imm[6]));
  LED led_27 (.in(Imm[5]));
  LED led_28 (.in(Imm[4]));
  LED led_29 (.in(Imm[3]));
  LED led_30 (.in(Imm[2]));
  assign Imm = J_type ? {{12{Inst[31]}}, Inst[19:12], Inst[20], Inst[30:21], 1'b0} : 32'bz;  // Driver driver_5
  LED led_31 (.in(Imm[1]));
  LED led_32 (.in(Imm[0]));
  PullDown #(.Bits(32)) pulldown_1 (.out(Imm));

  // Other names for the same wires on the sheet: inst_7 = Inst[7]; inst_8_11[3:0] = Inst[11:8];
  //   inst_12_19[7:0] = Inst[19:12]; inst_20 = Inst[20]; inst_21_24[3:0] = Inst[24:21]; inst_25_30[5:0] = Inst[30:25];
  //   inst_31 = Inst[31]

  // Notes on the sheet:
  //   I-type
  //   Imm_Ctrl
  //   000   R-type
  //   001   I-type
  //   010   S-type
  //   011   B-type
  //   100   U-type
  //   101   J-type
  //   110   (unused)
  //   111   (unused)
  //   S-type
  //   B-type
  //   U-type
  //   J-type
endmodule
