// Digital circuit Instr.Decoder.dig as structural Verilog
module Instr_Decoder (
  input  [31:0] Inst,
  output [4:0] WB_reg,
  output WB_we,
  output [4:0] Rs1,
  output [4:0] Rs2,
  output [2:0] Imm_ctrl,
  output B_mux,
  output [4:0] ALU_ctrl,
  output Mem_wr,
  output [1:0] Mem_mux,
  output Mem_rd,
  output [2:0] Mem_sz,
  output A_mux,
  output Valid,
  output Jump,
  output Branch,
  output [1:0] J_ctrl,
  output [1:0] BR_ctrl
);

  wire and_1_out, and_2_out, and_3_out, Debug_out, dipswitch_16_out, instr_decoder_rvc_1_illegal_instr,
       instr_decoder_rvc_1_rvc_instr, rs1_en, rs2_en, uCRom___Logic_out, WB_mux;
  wire [6:0] func7;
  wire [24:0] inst_t;
  wire [31:0] dipswitch_1_out, driverinvsel_1_out;

  DipSwitch dipswitch_1 (.out(dipswitch_1_out[31]));
  DipSwitch dipswitch_2 (.out(dipswitch_1_out[30]));
  DipSwitch dipswitch_3 (.out(dipswitch_1_out[29]));
  DipSwitch dipswitch_4 (.out(dipswitch_1_out[28]));
  DipSwitch dipswitch_5 (.out(dipswitch_1_out[27]));
  DipSwitch dipswitch_6 (.out(dipswitch_1_out[26]));
  DipSwitch dipswitch_7 (.out(dipswitch_1_out[25]));
  DipSwitch dipswitch_8 (.out(dipswitch_1_out[24]));
  DipSwitch dipswitch_9 (.out(dipswitch_1_out[23]));
  DipSwitch dipswitch_10 (.out(dipswitch_1_out[22]));
  DipSwitch dipswitch_11 (.out(dipswitch_1_out[21]));
  and and_1 (and_1_out, inst_t[0], inst_t[1]);
  DipSwitch dipswitch_12 (.out(dipswitch_1_out[20]));
  DipSwitch dipswitch_13 (.out(dipswitch_1_out[19]));
  DipSwitch dipswitch_14 (.out(dipswitch_1_out[18]));
  DipSwitch dipswitch_15 (.out(dipswitch_1_out[17]));
  assign driverinvsel_1_out = ~Debug_out ? Inst : 32'bz;  // DriverInvSel driverinvsel_1
  DipSwitch #(.dipDefault("true")) dipswitch_16 (.out(dipswitch_16_out));
  PullDown pulldown_1 (.out(A_mux));
  DipSwitch dipswitch_17 (.out(dipswitch_1_out[16]));
  DipSwitch dipswitch_18 (.out(dipswitch_1_out[15]));
  DipSwitch dipswitch_19 (.out(dipswitch_1_out[14]));
  DipSwitch dipswitch_20 (.out(dipswitch_1_out[13]));
  DipSwitch Debug (.out(Debug_out));
  assign driverinvsel_1_out = Debug_out ? dipswitch_1_out : 32'bz;  // Driver driver_1
  Instr_Decoder_RVC instr_decoder_rvc_1 (
    .in(driverinvsel_1_out), .enable(dipswitch_16_out),
    .out({func7, inst_t[24:15], BR_ctrl[1], Mem_sz[1], BR_ctrl[0], inst_t[11:0]}),
    .RVC_instr(instr_decoder_rvc_1_rvc_instr), .illegal_instr(instr_decoder_rvc_1_illegal_instr));
  DipSwitch uCRom___Logic (.out(uCRom___Logic_out));
  and and_2 (and_2_out, ~uCRom___Logic_out, and_1_out);  // And
  and and_3 (and_3_out, uCRom___Logic_out, and_1_out);
  PullDown pulldown_2 (.out(rs2_en));
  PullDown pulldown_3 (.out(rs1_en));
  PullDown #(.Bits(3)) pulldown_4 (.out(Imm_ctrl));
  PullDown pulldown_5 (.out(B_mux));
  DipSwitch dipswitch_21 (.out(dipswitch_1_out[12]));
  DipSwitch dipswitch_22 (.out(dipswitch_1_out[11]));
  DipSwitch dipswitch_23 (.out(dipswitch_1_out[10]));
  DipSwitch dipswitch_24 (.out(dipswitch_1_out[9]));
  Instr_Decoder_uCRom instr_decoder_ucrom_1 (
    .sel(and_2_out), .opcode(inst_t[6:2]), .func3({BR_ctrl[1], Mem_sz[1], BR_ctrl[0]}), .func7(func7),
    .rd(inst_t[11:7]), .rs1(inst_t[19:15]), .rs2(inst_t[24:20]), .A_mux(A_mux), .B_mux(B_mux),
    .Imm_ctrl(Imm_ctrl), .rs1_en(rs1_en), .rs2_en(rs2_en), .rd_en(WB_we), .Mem_rd(Mem_rd), .Mem_wr(Mem_wr),
    .Mem_mux(Mem_mux), .ALU_ctrl(ALU_ctrl), .J_JAL(J_ctrl[0]), .J_JALR(J_ctrl[1]), .Branch(Branch),
    .Valid_instr(Valid));
  Instr_Decoder_Logic instr_decoder_logic_1 (
    .sel(and_3_out), .opcode(inst_t[6:2]), .func3({BR_ctrl[1], Mem_sz[1], BR_ctrl[0]}), .func7(func7),
    .rd(inst_t[11:7]), .rs1(inst_t[19:15]), .rs2(inst_t[24:20]), .A_mux(A_mux), .B_mux(B_mux),
    .Imm_ctrl(Imm_ctrl), .rs1_en(rs1_en), .rs2_en(rs2_en), .rd_en(WB_we), .Mem_rd(Mem_rd), .Mem_wr(Mem_wr),
    .Mem_mux(Mem_mux), .ALU_ctrl(ALU_ctrl), .J_JAL(J_ctrl[0]), .J_JALR(J_ctrl[1]), .Branch(Branch),
    .Valid_instr(Valid));
  PullDown pulldown_6 (.out(Mem_wr));
  PullDown pulldown_7 (.out(Mem_rd));
  PullDown pulldown_8 (.out(WB_mux));
  PullDown pulldown_9 (.out(WB_we));
  DipSwitch dipswitch_25 (.out(dipswitch_1_out[8]));
  DipSwitch dipswitch_26 (.out(dipswitch_1_out[7]));
  DipSwitch dipswitch_27 (.out(dipswitch_1_out[6]));
  DipSwitch dipswitch_28 (.out(dipswitch_1_out[5]));
  LED led_1 (.in(instr_decoder_rvc_1_rvc_instr));
  LED led_2 (.in(instr_decoder_rvc_1_illegal_instr));
  PullDown #(.Bits(5)) pulldown_10 (.out(ALU_ctrl));
  PullDown #(.Bits(2)) pulldown_11 (.out(Mem_mux));
  PullDown pulldown_12 (.out(J_ctrl[0]));
  PullDown pulldown_13 (.out(J_ctrl[1]));
  DipSwitch dipswitch_29 (.out(dipswitch_1_out[4]));
  DipSwitch dipswitch_30 (.out(dipswitch_1_out[3]));
  DipSwitch dipswitch_31 (.out(dipswitch_1_out[2]));
  DipSwitch #(.dipDefault("true")) dipswitch_32 (.out(dipswitch_1_out[1]));
  PullDown pulldown_14 (.out(Valid));
  PullDown pulldown_15 (.out(Branch));
  DipSwitch #(.dipDefault("true")) dipswitch_33 (.out(dipswitch_1_out[0]));
  or or_1 (Jump, J_ctrl[0], J_ctrl[1]);
  assign Rs1 = rs1_en ? inst_t[19:15] : 5'bz;  // Driver driver_2
  assign Rs2 = rs2_en ? inst_t[24:20] : 5'bz;  // Driver driver_3
  assign WB_reg = WB_we ? inst_t[11:7] : 5'bz;  // Driver driver_4
  PullDown #(.Bits(5)) pulldown_16 (.out(Rs1));
  PullDown #(.Bits(5)) pulldown_17 (.out(Rs2));
  PullDown #(.Bits(5)) pulldown_18 (.out(WB_reg));

  assign {Mem_sz[2], Mem_sz[0]} = BR_ctrl;

  // Other names for the same wires on the sheet: opcode_nonrvc[1:0] = inst_t[1:0]; opcode[4:0] = inst_t[6:2];
  //   rd[4:0] = inst_t[11:7]; func3[2:0] = {BR_ctrl[1], Mem_sz[1], BR_ctrl[0]};
  //   inst_t (some bits) = {func7, BR_ctrl[1], Mem_sz[1], BR_ctrl[0]}; rs1_t[4:0] = inst_t[19:15];
  //   rs2_t[4:0] = inst_t[24:20]; J_JAL = J_ctrl[0]; J_JALR = J_ctrl[1]; rd_en = WB_we; Valid_instr = Valid

  // Notes on the sheet:
  //   Debug / RVC-Decoding
  //   Instruction-Decoder
  //   func7
  //   rs2
  //   rs1
  //   func3
  //   rd
  //   opcode
  //   11
  //   Jump-Unit
  //   Stage: Instruction-Decode / Register-Fetch (ID)
  //   Branch-Unit
  //   Stage: Execute (EXE)
  //   ALU-Operation
  //   Stage: Memory (MEM)
  //   Stage: Write-Back (WB)
  //   0-x0-00   ADD
  //   0-x1-00   SUB
  //   0-00-01   XOR
  //   0-01-01   OR
  //   0-10-01   AND
  //   0-x0-11   SLT
  //   0-x1-11   SLTU
  //   0-00-10   SLL
  //   0-10-10   SRL
  //   0-11-10   SRA
  //   MUL/DIV-Operation
  //   1-xx-xx   TODO...
  //   A_mux
  //   0   Rs1_data
  //   1   PC
  //   B_mux
  //   0   Rs2_data
  //   1   Imm
  //   Imm_ctrl
  //   000   R-type
  //   001   I-type
  //   010   S-type
  //   011   B-type
  //   100   U-type
  //   101   J-type
  //   110   (unused)
  //   111   (unused)
  //   Mem_mux
  //   00   ALU_Result
  //   01   Mem_data
  //   10   PC_next
  //   11   (unused)
  //   Mem_sz
  //   x-00   B
  //   x-01   H
  //   x-10   W
  //   1-0x   U
endmodule
