// Digital circuit Instr.Display.dig as structural Verilog
module Instr_Display (
  input  [31:0] Inst,
  output opLOAD,
  output opLOAD_FP,
  output opCUST0,
  output opMISC_MEM,
  output opOP_IMM,
  output opAUIPC,
  output opOP_IMM_32,
  output op48BIT1,
  output opSTORE,
  output opSTORE_FP,
  output opCUST1,
  output opAMO,
  output opOP,
  output opLUI,
  output opOP_32,
  output op64BIT,
  output opMADD,
  output opMSUB,
  output opNMSUB,
  output opNMADD,
  output opOP_FP,
  output opRES0,
  output opCUST2,
  output op48BIT2,
  output opBRANCH,
  output opJALR,
  output opRES1,
  output opJAL,
  output opSYSTEM,
  output opRES2,
  output opCUST3,
  output op80BIT,
  output Illegal,
  output iJAL,
  output iJALR,
  output iBEQ,
  output iBNE,
  output iBLT,
  output iBGE,
  output iBLTU,
  output iBGEU,
  output iLUI,
  output iAUIPC,
  output iLB,
  output iLH,
  output iLW,
  output iLBU,
  output iLHU,
  output iSB,
  output iSH,
  output iSW,
  output iSLLI,
  output iSRLI,
  output iSRAI,
  output iXORI,
  output iORI,
  output iANDI,
  output iSLTI,
  output iSLTIU,
  output iADDI,
  output iFENCE,
  output iFENCE_TSO,
  output iECALL,
  output iEBREAK,
  output iNOP,
  output iSLL,
  output iSRL,
  output iSRA,
  output iXOR,
  output iOR,
  output iAND,
  output iSLT,
  output iSLTU,
  output iADD,
  output iSUB,
  output iCSRRW,
  output iCSRRS,
  output iCSRRC,
  output iMUL,
  output iMULH,
  output iMULHSU,
  output iMULHU,
  output iDIV,
  output iDIVU,
  output iREM,
  output iREMU,
  output iCSRRWI,
  output iCSRRSI,
  output iCSRRCI,
  output iFENCE_I,
  output iCSRaddr0,
  output iCSRaddr1,
  output iCSRaddr2,
  output iCSRaddr3,
  output iCSRaddr4,
  output iCSRaddr5,
  output iCSRaddr6,
  output iCSRaddr7,
  output iCSRaddr8,
  output iCSRaddr9,
  output iCSRaddr10,
  output iCSRaddr11
);

  wire and_7_out, and_8_out, and_10_out, and_11_out, and_12_out, and_13_out, and_27_out, and_28_out,
       Debug_out, demultiplexer_1_out_2, demultiplexer_1_out_3, demultiplexer_2_out_3, demultiplexer_2_out_6,
       demultiplexer_2_out_7, demultiplexer_3_out_3, demultiplexer_3_out_4, demultiplexer_3_out_5,
       demultiplexer_3_out_6, demultiplexer_3_out_7, demultiplexer_4_out_4, demultiplexer_5_out_0,
       demultiplexer_5_out_1, demultiplexer_5_out_2, demultiplexer_5_out_3, demultiplexer_11_out_0,
       demultiplexer_11_out_1, demultiplexer_11_out_2, demultiplexer_11_out_3, demultiplexer_11_out_4,
       demultiplexer_11_out_5, demultiplexer_11_out_6, demultiplexer_11_out_7, demultiplexer_12_out_0,
       demultiplexer_12_out_1, demultiplexer_12_out_2, demultiplexer_12_out_3, demultiplexer_12_out_4,
       demultiplexer_12_out_5, demultiplexer_12_out_6, demultiplexer_12_out_7, diodeforward_22_out,
       diodeforward_27_out, diodeforward_32_out, diodeforward_34_out, diodeforward_37_out, func3_n,
       func7_0100000, func7_1000001, func7_n, nand_1_out, not_3_out, not_4_out, not_5_out, not_6_out,
       not_8_out, not_9_out, not_10_out, not_11_out, not_12_out, not_13_out, not_14_out, not_15_out,
       or_1_out, rd_n, rs1_n, rs2_00001, rs2_10011, rs2_n;
  wire [2:0] func3;
  wire [6:0] func7;
  wire [24:0] inst_t;
  wire [31:0] dipswitch_32_out;

  DipSwitch dipswitch_1 (.out(dipswitch_32_out[31]));
  DipSwitch dipswitch_2 (.out(dipswitch_32_out[30]));
  DipSwitch dipswitch_3 (.out(dipswitch_32_out[29]));
  DipSwitch dipswitch_4 (.out(dipswitch_32_out[28]));
  DipSwitch dipswitch_5 (.out(dipswitch_32_out[27]));
  DipSwitch dipswitch_6 (.out(dipswitch_32_out[26]));
  DipSwitch dipswitch_7 (.out(dipswitch_32_out[25]));
  DipSwitch dipswitch_8 (.out(dipswitch_32_out[24]));
  DipSwitch dipswitch_9 (.out(dipswitch_32_out[23]));
  DipSwitch dipswitch_10 (.out(dipswitch_32_out[22]));
  DipSwitch dipswitch_11 (.out(dipswitch_32_out[21]));
  DiodeForward diodeforward_1 (.in(opLOAD_FP), .out(Illegal));
  DiodeForward diodeforward_2 (.in(opOP_IMM_32), .out(Illegal));
  DiodeForward diodeforward_3 (.in(opSTORE_FP), .out(Illegal));
  DiodeForward diodeforward_4 (.in(opAMO), .out(Illegal));
  DiodeForward diodeforward_5 (.in(opOP_32), .out(Illegal));
  DiodeForward diodeforward_6 (.in(opMADD), .out(Illegal));
  DiodeForward diodeforward_7 (.in(opMSUB), .out(Illegal));
  DiodeForward diodeforward_8 (.in(opNMSUB), .out(Illegal));
  DiodeForward diodeforward_9 (.in(opNMADD), .out(Illegal));
  DiodeForward diodeforward_10 (.in(opOP_FP), .out(Illegal));
  DiodeForward diodeforward_11 (.in(opCUST0), .out(Illegal));
  PullDown pulldown_1 (.out(Illegal));
  DiodeForward diodeforward_12 (.in(opCUST1), .out(Illegal));
  DiodeForward diodeforward_13 (.in(opCUST2), .out(Illegal));
  DiodeForward diodeforward_14 (.in(opCUST3), .out(Illegal));
  DiodeForward diodeforward_15 (.in(opRES0), .out(Illegal));
  DiodeForward diodeforward_16 (.in(opRES1), .out(Illegal));
  DiodeForward diodeforward_17 (.in(opRES2), .out(Illegal));
  DiodeForward diodeforward_18 (.in(op48BIT1), .out(Illegal));
  DiodeForward diodeforward_19 (.in(op48BIT2), .out(Illegal));
  DiodeForward diodeforward_20 (.in(op64BIT), .out(Illegal));
  DiodeForward diodeforward_21 (.in(op80BIT), .out(Illegal));
  DiodeForward diodeforward_22 (.in(inst_t[7]), .out(diodeforward_22_out));
  DiodeForward diodeforward_23 (.in(inst_t[8]), .out(diodeforward_22_out));
  DiodeForward diodeforward_24 (.in(inst_t[9]), .out(diodeforward_22_out));
  DiodeForward diodeforward_25 (.in(inst_t[10]), .out(diodeforward_22_out));
  DiodeForward diodeforward_26 (.in(inst_t[11]), .out(diodeforward_22_out));
  PullDown pulldown_2 (.out(diodeforward_22_out));
  DiodeForward diodeforward_27 (.in(inst_t[15]), .out(diodeforward_27_out));
  DiodeForward diodeforward_28 (.in(inst_t[16]), .out(diodeforward_27_out));
  DiodeForward diodeforward_29 (.in(inst_t[17]), .out(diodeforward_27_out));
  DiodeForward diodeforward_30 (.in(inst_t[18]), .out(diodeforward_27_out));
  DiodeForward diodeforward_31 (.in(inst_t[19]), .out(diodeforward_27_out));
  PullDown pulldown_3 (.out(diodeforward_27_out));
  DiodeForward diodeforward_32 (.in(inst_t[22]), .out(diodeforward_32_out));
  DiodeForward diodeforward_33 (.in(inst_t[23]), .out(diodeforward_32_out));
  PullDown pulldown_4 (.out(diodeforward_32_out));
  DiodeForward diodeforward_34 (.in(func3[0]), .out(diodeforward_34_out));
  DiodeForward diodeforward_35 (.in(func3[1]), .out(diodeforward_34_out));
  DiodeForward diodeforward_36 (.in(func3[2]), .out(diodeforward_34_out));
  PullDown pulldown_5 (.out(diodeforward_34_out));
  DiodeForward diodeforward_37 (.in(func7[1]), .out(diodeforward_37_out));
  DiodeForward diodeforward_38 (.in(func7[2]), .out(diodeforward_37_out));
  DiodeForward diodeforward_39 (.in(func7[3]), .out(diodeforward_37_out));
  DiodeForward diodeforward_40 (.in(func7[4]), .out(diodeforward_37_out));
  PullDown pulldown_6 (.out(diodeforward_37_out));
  DipSwitch dipswitch_12 (.out(dipswitch_32_out[20]));
  DipSwitch dipswitch_13 (.out(dipswitch_32_out[19]));
  DipSwitch dipswitch_14 (.out(dipswitch_32_out[18]));
  DipSwitch dipswitch_15 (.out(dipswitch_32_out[17]));
  assign {func7, inst_t[24:15], func3, inst_t[11:0]} = ~Debug_out ? Inst : 32'bz;  // DriverInvSel driverinvsel_1
  LED led_1 (.in(Debug_out));
  not not_1 (rd_n, diodeforward_22_out);
  not not_2 (rs1_n, diodeforward_27_out);
  not not_3 (not_3_out, inst_t[20]);
  not not_4 (not_4_out, inst_t[21]);
  not not_5 (not_5_out, diodeforward_32_out);
  not not_6 (not_6_out, inst_t[24]);
  not not_7 (func3_n, diodeforward_34_out);
  not not_8 (not_8_out, func7[0]);
  not not_9 (not_9_out, diodeforward_37_out);
  not not_10 (not_10_out, func7[5]);
  not not_11 (not_11_out, func7[6]);
  DipSwitch dipswitch_16 (.out(dipswitch_32_out[14]));
  DipSwitch dipswitch_17 (.out(dipswitch_32_out[13]));
  DipSwitch dipswitch_18 (.out(dipswitch_32_out[16]));
  DipSwitch dipswitch_19 (.out(dipswitch_32_out[15]));
  assign {func7, inst_t[24:15], func3, inst_t[11:0]} = Debug_out ? dipswitch_32_out : 32'bz;  // Driver driver_1
  DipSwitch dipswitch_20 (.out(dipswitch_32_out[12]));
  DipSwitch dipswitch_21 (.out(dipswitch_32_out[11]));
  DipSwitch dipswitch_22 (.out(dipswitch_32_out[10]));
  DipSwitch dipswitch_23 (.out(dipswitch_32_out[9]));
  DipSwitch Debug (.out(Debug_out));
  and and_1 (rs2_n, not_3_out, not_4_out, not_5_out, not_6_out);
  and and_2 (rs2_00001, inst_t[20], not_4_out, not_5_out, not_6_out);
  and and_3 (rs2_10011, inst_t[20], inst_t[21], not_5_out, inst_t[24]);
  and and_4 (func7_n, not_8_out, not_9_out, not_10_out, not_11_out);
  and and_5 (func7_0100000, not_8_out, not_9_out, func7[5], not_11_out);
  and and_6 (func7_1000001, func7[0], not_9_out, not_10_out, func7[6]);
  DipSwitch dipswitch_24 (.out(dipswitch_32_out[6]));
  DipSwitch dipswitch_25 (.out(dipswitch_32_out[5]));
  DipSwitch dipswitch_26 (.out(dipswitch_32_out[8]));
  DipSwitch dipswitch_27 (.out(dipswitch_32_out[7]));
  DipSwitch dipswitch_28 (.out(dipswitch_32_out[4]));
  DipSwitch dipswitch_29 (.out(dipswitch_32_out[3]));
  DipSwitch dipswitch_30 (.out(dipswitch_32_out[2]));
  DipSwitch #(.dipDefault("true")) dipswitch_31 (.out(dipswitch_32_out[1]));
  DipSwitch #(.dipDefault("true")) dipswitch_32 (.out(dipswitch_32_out[0]));
  nand nand_1 (nand_1_out, inst_t[0], inst_t[1]);
  Demultiplexer #(.Selector_Bits(3)) demultiplexer_1 (
    .sel(func3), .in(opBRANCH), .out_0(iBEQ), .out_1(iBNE), .out_2(demultiplexer_1_out_2),
    .out_3(demultiplexer_1_out_3), .out_4(iBLT), .out_5(iBGE), .out_6(iBLTU), .out_7(iBGEU));
  Demultiplexer #(.Selector_Bits(3)) demultiplexer_2 (
    .sel(func3), .in(opLOAD), .out_0(iLB), .out_1(iLH), .out_2(iLW), .out_3(demultiplexer_2_out_3),
    .out_4(iLBU), .out_5(iLHU), .out_6(demultiplexer_2_out_6), .out_7(demultiplexer_2_out_7));
  Demultiplexer #(.Selector_Bits(3)) demultiplexer_3 (
    .sel(func3), .in(opSTORE), .out_0(iSB), .out_1(iSH), .out_2(iSW), .out_3(demultiplexer_3_out_3),
    .out_4(demultiplexer_3_out_4), .out_5(demultiplexer_3_out_5), .out_6(demultiplexer_3_out_6),
    .out_7(demultiplexer_3_out_7));
  Demultiplexer #(.Selector_Bits(3)) demultiplexer_4 (
    .sel(func3), .in(opSYSTEM), .out_1(iCSRRW), .out_2(iCSRRS), .out_3(iCSRRC),
    .out_4(demultiplexer_4_out_4), .out_5(iCSRRWI), .out_6(iCSRRSI), .out_7(iCSRRCI));  // open: out_0
  not not_12 (not_12_out, nand_1_out);
  Demultiplexer #(.Selector_Bits(2)) demultiplexer_5 (
    .sel(inst_t[6:5]), .in(not_12_out), .out_0(demultiplexer_5_out_0), .out_1(demultiplexer_5_out_1),
    .out_2(demultiplexer_5_out_2), .out_3(demultiplexer_5_out_3));
  DiodeForward diodeforward_41 (.in(demultiplexer_1_out_2), .out(Illegal));
  DiodeForward diodeforward_42 (.in(demultiplexer_1_out_3), .out(Illegal));
  DiodeForward diodeforward_43 (.in(demultiplexer_2_out_3), .out(Illegal));
  DiodeForward diodeforward_44 (.in(demultiplexer_2_out_6), .out(Illegal));
  DiodeForward diodeforward_45 (.in(demultiplexer_2_out_7), .out(Illegal));
  DiodeForward diodeforward_46 (.in(demultiplexer_3_out_3), .out(Illegal));
  DiodeForward diodeforward_47 (.in(demultiplexer_3_out_4), .out(Illegal));
  DiodeForward diodeforward_48 (.in(demultiplexer_3_out_5), .out(Illegal));
  DiodeForward diodeforward_49 (.in(demultiplexer_3_out_6), .out(Illegal));
  DiodeForward diodeforward_50 (.in(demultiplexer_3_out_7), .out(Illegal));
  not not_13 (not_13_out, func3[1]);
  not not_14 (not_14_out, func3[2]);
  DiodeForward diodeforward_51 (.in(demultiplexer_4_out_4), .out(Illegal));
  and and_7 (and_7_out, func7_1000001, opOP);
  LED RVC_Instruction (.in(nand_1_out));
  Demultiplexer #(.Selector_Bits(3)) demultiplexer_6 (
    .sel(inst_t[4:2]), .in(demultiplexer_5_out_0), .out_0(opLOAD), .out_1(opLOAD_FP), .out_2(opCUST0),
    .out_3(opMISC_MEM), .out_4(opOP_IMM), .out_5(iAUIPC), .out_6(opOP_IMM_32), .out_7(op48BIT1));
  LED LOAD (.in(opLOAD));
  Demultiplexer #(.Selector_Bits(3)) demultiplexer_7 (
    .sel(inst_t[4:2]), .in(demultiplexer_5_out_1), .out_0(opSTORE), .out_1(opSTORE_FP), .out_2(opCUST1),
    .out_3(opAMO), .out_4(opOP), .out_5(iLUI), .out_6(opOP_32), .out_7(op64BIT));
  LED STORE (.in(opSTORE));
  Demultiplexer #(.Selector_Bits(3)) demultiplexer_8 (
    .sel(inst_t[4:2]), .in(demultiplexer_5_out_2), .out_0(opMADD), .out_1(opMSUB), .out_2(opNMSUB),
    .out_3(opNMADD), .out_4(opOP_FP), .out_5(opRES0), .out_6(opCUST2), .out_7(op48BIT2));
  LED MADD (.in(opMADD));
  Demultiplexer #(.Selector_Bits(3)) demultiplexer_9 (
    .sel(inst_t[4:2]), .in(demultiplexer_5_out_3), .out_0(opBRANCH), .out_1(iJALR), .out_2(opRES1),
    .out_3(iJAL), .out_4(opSYSTEM), .out_5(opRES2), .out_6(opCUST3), .out_7(op80BIT));
  LED BRANCH (.in(opBRANCH));
  and and_8 (and_8_out, func3[0], not_13_out, not_14_out);
  Demultiplexer #(.Selector_Bits(3)) demultiplexer_10 (
    .sel(func3), .in(and_7_out), .out_0(iMUL), .out_1(iMULH), .out_2(iMULHSU), .out_3(iMULHU), .out_4(iDIV),
    .out_5(iDIVU), .out_6(iREM), .out_7(iREMU));
  and and_9 (iFENCE_I, opMISC_MEM, and_8_out);
  LED LOAD_FP (.in(opLOAD_FP));
  LED STORE_FP (.in(opSTORE_FP));
  LED MSUB (.in(opMSUB));
  LED JALR (.in(iJALR));
  Demultiplexer #(.Selector_Bits(3)) demultiplexer_11 (
    .sel(func3), .in(opOP_IMM), .out_0(demultiplexer_11_out_0), .out_1(demultiplexer_11_out_1),
    .out_2(demultiplexer_11_out_2), .out_3(demultiplexer_11_out_3), .out_4(demultiplexer_11_out_4),
    .out_5(demultiplexer_11_out_5), .out_6(demultiplexer_11_out_6), .out_7(demultiplexer_11_out_7));
  LED custom_0 (.in(opCUST0));
  LED custom_1 (.in(opCUST1));
  LED NMSUB (.in(opNMSUB));
  LED res1 (.in(opRES1));
  and and_10 (and_10_out, rd_n, rs1_n, rs2_n);
  and and_11 (and_11_out, opSYSTEM, func7_n, func3_n);
  and and_12 (and_12_out, rd_n, rs1_n);
  and and_13 (and_13_out, not_15_out, opSYSTEM);
  not not_15 (not_15_out, func3_n);
  assign {iCSRaddr11, iCSRaddr10, iCSRaddr9, iCSRaddr8, iCSRaddr7, iCSRaddr6, iCSRaddr5, iCSRaddr4, iCSRaddr3, iCSRaddr2, iCSRaddr1, iCSRaddr0} = and_13_out ? {func7, inst_t[24:20]} : 12'bz;  // Driver driver_2
  LED MISC_MEM (.in(opMISC_MEM));
  LED AMO (.in(opAMO));
  LED NMADD (.in(opNMADD));
  LED JAL (.in(iJAL));
  and and_14 (iADDI, func7_n, demultiplexer_11_out_0);
  and and_15 (iSLLI, func7_n, demultiplexer_11_out_1);
  and and_16 (iSLTI, func7_n, demultiplexer_11_out_2);
  and and_17 (iSLTIU, func7_n, demultiplexer_11_out_3);
  and and_18 (iXORI, func7_n, demultiplexer_11_out_4);
  and and_19 (iSRLI, func7_n, demultiplexer_11_out_5);
  and and_20 (iSRAI, func7_0100000, demultiplexer_11_out_5);
  and and_21 (iORI, func7_n, demultiplexer_11_out_6);
  and and_22 (iANDI, func7_n, demultiplexer_11_out_7);
  and and_23 (iNOP, iADDI, func7_n, and_10_out);
  and and_24 (iECALL, and_11_out, and_12_out, rs2_n);
  and and_25 (iEBREAK, and_11_out, and_12_out, rs2_00001);
  PullDown #(.Bits(12)) pulldown_7 (.out({iCSRaddr11, iCSRaddr10, iCSRaddr9, iCSRaddr8, iCSRaddr7, iCSRaddr6, iCSRaddr5, iCSRaddr4, iCSRaddr3, iCSRaddr2, iCSRaddr1, iCSRaddr0}));
  LED OP_IMM (.in(opOP_IMM));
  LED OP (.in(opOP));
  LED OP_FP (.in(opOP_FP));
  LED SYSTEM (.in(opSYSTEM));
  LED AUIPC (.in(iAUIPC));
  LED LUI (.in(iLUI));
  LED res0 (.in(opRES0));
  LED res2 (.in(opRES2));
  Demultiplexer #(.Selector_Bits(3)) demultiplexer_12 (
    .sel(func3), .in(opOP), .out_0(demultiplexer_12_out_0), .out_1(demultiplexer_12_out_1),
    .out_2(demultiplexer_12_out_2), .out_3(demultiplexer_12_out_3), .out_4(demultiplexer_12_out_4),
    .out_5(demultiplexer_12_out_5), .out_6(demultiplexer_12_out_6), .out_7(demultiplexer_12_out_7));
  or or_1 (or_1_out, func3[1], func3[2]);
  LED OP_IMM_32 (.in(opOP_IMM_32));
  LED OP_32 (.in(opOP_32));
  LED custom_2_rv129 (.in(opCUST2));
  LED custom_3_rv129 (.in(opCUST3));
  and and_26 (iFENCE, opMISC_MEM, func3_n);
  and and_27 (and_27_out, iFENCE, func7_1000001, rd_n);
  and and_28 (and_28_out, opMISC_MEM, or_1_out);
  and and_29 (iADD, func7_n, demultiplexer_12_out_0);
  and and_30 (iSUB, func7_0100000, demultiplexer_12_out_0);
  and and_31 (iSLL, func7_n, demultiplexer_12_out_1);
  and and_32 (iSLT, func7_n, demultiplexer_12_out_2);
  and and_33 (iSLTU, func7_n, demultiplexer_12_out_3);
  and and_34 (iXOR, func7_n, demultiplexer_12_out_4);
  and and_35 (iSRL, func7_n, demultiplexer_12_out_5);
  and and_36 (iSRA, func7_0100000, demultiplexer_12_out_5);
  and and_37 (iOR, func7_n, demultiplexer_12_out_6);
  and and_38 (iAND, func7_n, demultiplexer_12_out_7);
  and and_39 (iFENCE_TSO, and_27_out, rs1_n, rs2_10011);
  DiodeForward diodeforward_52 (.in(and_28_out), .out(Illegal));
  LED _48bit (.in(op48BIT1));
  LED _64bit (.in(op64BIT));
  LED _48bit_2 (.in(op48BIT2));
  LED gt__eq_80b (.in(op80BIT));
  LED JAL_2 (.in(iJAL));
  LED JALR_2 (.in(iJALR));
  LED BEQ (.in(iBEQ));
  LED BNE (.in(iBNE));
  LED BLT (.in(iBLT));
  LED BGE (.in(iBGE));
  LED BLTU (.in(iBLTU));
  LED BGEU (.in(iBGEU));
  LED LUI_2 (.in(iLUI));
  LED AUIPC_2 (.in(iAUIPC));
  LED FENCE_I (.in(iFENCE_I));
  LED CSRRW (.in(iCSRRW));
  LED CSRRS (.in(iCSRRS));
  LED CSRRC (.in(iCSRRC));
  LED MUL (.in(iMUL));
  LED MULH (.in(iMULH));
  LED MULHSU (.in(iMULHSU));
  LED MULHU (.in(iMULHU));
  LED LB (.in(iLB));
  LED LH (.in(iLH));
  LED LW (.in(iLW));
  LED LBU (.in(iLBU));
  LED LHU (.in(iLHU));
  LED SB (.in(iSB));
  LED SH (.in(iSH));
  LED SW (.in(iSW));
  LED CSRRWI (.in(iCSRRWI));
  LED CSRRSI (.in(iCSRRSI));
  LED CSRRCI (.in(iCSRRCI));
  LED DIV (.in(iDIV));
  LED DIVU (.in(iDIVU));
  LED REM (.in(iREM));
  LED REMU (.in(iREMU));
  LED SLLI (.in(iSLLI));
  LED SRLI (.in(iSRLI));
  LED SRAI (.in(iSRAI));
  LED XORI (.in(iXORI));
  LED ORI (.in(iORI));
  LED ANDI (.in(iANDI));
  LED SLTI (.in(iSLTI));
  LED SLTIU (.in(iSLTIU));
  LED ADDI (.in(iADDI));
  LED SLL (.in(iSLL));
  LED SRL (.in(iSRL));
  LED SRA (.in(iSRA));
  LED XOR (.in(iXOR));
  LED OR_2 (.in(iOR));
  LED AND_40 (.in(iAND));
  LED SLT (.in(iSLT));
  LED SLTU (.in(iSLTU));
  LED ADD (.in(iADD));
  LED SUB (.in(iSUB));
  LED led_2 (.in(Illegal));
  PullDown pulldown_8 (.out(Illegal));
  LED FENCE (.in(iFENCE));
  LED FENCE_TSO (.in(iFENCE_TSO));
  LED ECALL (.in(iECALL));
  LED EBREAK (.in(iEBREAK));
  LED NOP (.in(iNOP));

  assign opAUIPC = iAUIPC;
  assign opJAL = iJAL;
  assign opJALR = iJALR;
  assign opLUI = iLUI;

  // Other names for the same wires on the sheet: rvc[1:0] = inst_t[1:0]; opcode[4:0] = inst_t[6:2];
  //   rd[4:0] = inst_t[11:7]; inst_t (some bits) = {func7, func3}; rs1[4:0] = inst_t[19:15]; rs2[4:0] = inst_t[24:20];
  //   OP_48bit1 = op48BIT1; OP_48bit2 = op48BIT2; OP_64bit = op64BIT; OP_80bit = op80BIT; OP_AMO = opAMO;
  //   OP_AUIPC = iAUIPC; OP_BRANCH = opBRANCH; OP_cust0 = opCUST0; OP_cust1 = opCUST1; OP_cust2 = opCUST2;
  //   OP_cust3 = opCUST3; OP_JAL = iJAL; OP_JALR = iJALR; OP_LOAD = opLOAD; OP_LOADFP = opLOAD_FP; OP_LUI = iLUI;
  //   OP_MADD = opMADD; OP_MISCMEM = opMISC_MEM; OP_MSUB = opMSUB; OP_NMADD = opNMADD; OP_NMSUB = opNMSUB;
  //   OP_OP = opOP; OP_OP32 = opOP_32; OP_OPFP = opOP_FP; OP_OPIMM = opOP_IMM; OP_OPIMM32 = opOP_IMM_32;
  //   OP_res0 = opRES0; OP_res1 = opRES1; OP_res2 = opRES2; OP_STORE = opSTORE; OP_STOREFP = opSTORE_FP;
  //   OP_SYSTEM = opSYSTEM; opADD = iADD; opADDI = iADDI; opAND = iAND; opANDI = iANDI; opBEQ = iBEQ; opBGE = iBGE;
  //   opBGEU = iBGEU; opBLT = iBLT; opBLTU = iBLTU; opBNE = iBNE; opCSRRC = iCSRRC; opCSRRCI = iCSRRCI;
  //   opCSRRS = iCSRRS; opCSRRSI = iCSRRSI; opCSRRW = iCSRRW; opCSRRWI = iCSRRWI; opDIV = iDIV; opDIVU = iDIVU;
  //   opEBREAK = iEBREAK; opECALL = iECALL; opFENCE = iFENCE; opFENCE_I = iFENCE_I; opFENCE_TSO = iFENCE_TSO;
  //   opILLEGAL = Illegal; opLB = iLB; opLBU = iLBU; opLH = iLH; opLHU = iLHU; opLW = iLW; opMUL = iMUL;
  //   opMULH = iMULH; opMULHSU = iMULHSU; opMULHU = iMULHU; opNOP = iNOP; opOR = iOR; opORI = iORI; opREM = iREM;
  //   opREMU = iREMU; opSB = iSB; opSH = iSH; opSLL = iSLL; opSLLI = iSLLI; opSLT = iSLT; opSLTI = iSLTI;
  //   opSLTIU = iSLTIU; opSLTU = iSLTU; opSRA = iSRA; opSRAI = iSRAI; opSRL = iSRL; opSRLI = iSRLI; opSUB = iSUB;
  //   opSW = iSW; opXOR = iXOR; opXORI = iXORI

  // Notes on the sheet:
  //   TODOs:
  //   Illegal instruction decoding
  //   - OP_OP (func7)
  //   - OP_SYSTEM
  //   - FENCE/FENCE.TSO instruction
  //   - CSRxx decode
  //   Debug
  //   func7
  //   Basic decoding
  //   rs2
  //   rs1
  //   func3
  //   rd
  //   opcode
  //   11
  //   Major opcodes
  //   RV32I Base Instructions
  //   Zifencei Standard Extension
  //   Zicsr Standard Extension
  //   RV32M Standard Extension
  //   00
  //   01
  //   10
  //   000
  //   001
  //   Special encoding of ADDI
  //   010
  //   011
  //   100
  //   101
  //   Special encoding of FENCE
  //   110
  //   111
  //   Instruction types
  //   31
  //   30
  //   29
  //   imm[11:0]
  //   imm[11:5]
  //   imm[12,10:5]
  //   imm[31:12]
  //   imm[20,10:1,11,19:12]
  //   Instruction parts
  //   imm
  //   csr
  //   RV32A Standard Extension
  //   RV32F Standard Extension
  //   RV32D Standard Extension
  //   RV32Q Standard Extension
  //   28
  //   27
  //   26
  //   25
  //   24
  //   23
  //   22
  //   21
  //   20
  //   19
  //   18
  //   17
  //   0
  //   4
  //   uimm
  //   16
  //   15
  //   14
  //   13
  //   12
  //   9
  //   imm[4:0]
  //   imm[4:1,11]
  //   8
  //   7
  //   6
  //   5
  //   2
  //   3
  //   1
  //   R-type
  //   I-type
  //   S-type
  //   B-type
  //   U-type
  //   J-type
  //   rs2/shamt
endmodule
