// Digital circuit Jump.Unit.dig as structural Verilog
module Jump_Unit (
  input  [1:0] J_ctrl,
  input  [31:0] PC,
  input  [31:0] Rs1,
  input  [31:0] Imm,
  output [31:0] J_addr
);

  wire [0:0] basicadder_1_y;
  wire [31:0] multiplexer_1_out;

  Multiplexer #(.Bits(32)) multiplexer_1 (.sel(J_ctrl[1]), .in_0(PC), .in_1(Rs1), .out(multiplexer_1_out));
  BasicAdder basicadder_1 (.A(multiplexer_1_out), .B(Imm), .Y({J_addr[31:1], basicadder_1_y[0]}));

  assign J_addr[0] = 1'b0;
endmodule
