// Digital circuit Mem.Ext.dig as structural Verilog
module Mem_Ext (
  input  [2:0] size,
  input  [31:0] in,
  output [31:0] out
);

  wire \signed ;
  wire [31:31] LB_U, LH_U;

  not not_1 (\signed , size[2]);
  assign LB_U[31] = \signed  ? in[7] : 1'bz;  // Driver driver_1
  PullDown pulldown_1 (.out(LB_U[31]));
  assign LH_U[31] = \signed  ? in[15] : 1'bz;  // Driver driver_2
  PullDown pulldown_2 (.out(LH_U[31]));
  Multiplexer #(.Bits(32), .Selector_Bits(2)) multiplexer_1 (
    .sel(size[1:0]), .in_0({{24{LB_U[31]}}, in[7:0]}), .in_1({{16{LH_U[31]}}, in[15:0]}), .in_2({32{1'b0}}),
    .in_3(in), .out(out));

  // Other names for the same wires on the sheet: LH_U[30:0] = {{15{LH_U[31]}}, in[15:0]};
  //   LB_U[30:0] = {{23{LB_U[31]}}, in[7:0]}

  // Notes on the sheet:
  //   x-00 byte
  //   x-01 half word
  //   x-10 word
  //   1-xx unsigned
endmodule
