// Digital circuit PipeCtrl.dig as structural Verilog
module PipeCtrl (
  input  Valid__prev,
  input  Ready__next,
  input  Done__this,
  input  Clock,
  input  Reset,
  input  Flush,
  output Ready__prev,
  output Valid__this,
  output _1cc,
  output REG_Clear,
  output REG_Clock,
  output REG_OE,
  output LED_Valid,
  output LED_Busy,
  output LED_Waiting,
  output LED_Empty
);

  wire and_3_out, and_4_out, and_7_out, and_8_out, and_9_out, not_1_out, not_2_out, not_3_out, not_4_out,
       not_5_out, not_6_out, or_2_out, xor_1_out;

  PullUp pullup_1 (.out(Valid__prev));
  PullDown pulldown_1 (.out(Flush));
  and and_1 (REG_Clock, Clock, Ready__prev);
  not not_1 (not_1_out, REG_Clear);
  and and_2 (REG_Clear, Reset, not_2_out);
  not not_2 (not_2_out, and_3_out);
  and and_3 (and_3_out, xor_1_out, ~Clock);  // And
  xor xor_1 (xor_1_out, and_4_out, not_3_out);
  not not_3 (not_3_out, not_4_out);
  not not_4 (not_4_out, not_5_out);
  not not_5 (not_5_out, not_6_out);
  not not_6 (not_6_out, and_4_out);
  and and_4 (and_4_out, Flush, ~Clock);  // And
  D_FF_AS d_ff_as_1 (.Set(1'b0), .D(Valid__prev), .C(REG_Clock), .Clr(not_1_out), .Q(LED_Valid), .nQ(LED_Empty));
  or or_1 (Ready__prev, and_9_out, ~LED_Valid);  // Or
  and and_5 (Valid__this, Done__this, LED_Valid);
  and and_6 (LED_Busy, ~LED_Empty, ~Done__this);  // And
  and and_7 (and_7_out, Clock, Done__this, Valid__prev, Ready__next);
  and and_8 (and_8_out, ~Clock, _1cc);  // And
  and and_9 (and_9_out, Ready__next, Done__this);
  and and_10 (LED_Waiting, ~Ready__next, LED_Valid, ~LED_Busy);  // And
  RS_FF_AS rs_ff_as_1 (.S(and_7_out), .R(or_2_out), .Q(_1cc));  // open: nQ
  or or_2 (or_2_out, and_8_out, not_1_out);
  PullUp pullup_2 (.out(Done__this));
  PullUp pullup_3 (.out(Ready__next));

  assign REG_OE = LED_Empty;

  // Notes on the sheet:
  //   .
  //   Generate clear-pulse on the
  //   falling edge of clock.
endmodule
