// Digital circuit PipeReg_32bit.dig as structural Verilog
module PipeReg_32bit (
  input  [31:0] In,
  input  [31:0] Default,
  input  REG_Clock,
  input  REG_OE,
  input  REG_Clear,
  output [31:0] Out,
  output [31:0] Disp
);

  PipeReg_8bit pipereg_8bit_1 (
    .In(In[7:0]), .Default(Default[7:0]), .REG_Clock(REG_Clock), .REG_OE(REG_OE), .REG_Clear(REG_Clear),
    .Out(Out[7:0]), .Disp(Disp[7:0]));
  PipeReg_8bit pipereg_8bit_2 (
    .In(In[15:8]), .Default(Default[15:8]), .REG_Clock(REG_Clock), .REG_OE(REG_OE), .REG_Clear(REG_Clear),
    .Out(Out[15:8]), .Disp(Disp[15:8]));
  PipeReg_8bit pipereg_8bit_3 (
    .In(In[23:16]), .Default(Default[23:16]), .REG_Clock(REG_Clock), .REG_OE(REG_OE), .REG_Clear(REG_Clear),
    .Out(Out[23:16]), .Disp(Disp[23:16]));
  PipeReg_8bit pipereg_8bit_4 (
    .In(In[31:24]), .Default(Default[31:24]), .REG_Clock(REG_Clock), .REG_OE(REG_OE), .REG_Clear(REG_Clear),
    .Out(Out[31:24]), .Disp(Disp[31:24]));
endmodule
