// Digital circuit PipeReg_8bit.dig as structural Verilog
module PipeReg_8bit (
  input  [7:0] In,
  input  [7:0] Default,
  input  REG_Clock,
  input  REG_OE,
  input  REG_Clear,
  output [7:0] Out,
  output [7:0] Disp
);

  wire _74273_1_pin2, _74273_1_pin5, _74273_1_pin6, _74273_1_pin9, _74273_1_pin12, _74273_1_pin15,
       _74273_1_pin16, _74273_1_pin19, pfet_1_d, pfet_2_d, pfet_3_d, pfet_4_d, pfet_5_d, pfet_6_d, pfet_7_d,
       pfet_8_d, pullup_1_out, pullup_2_out, pullup_3_out, pullup_4_out, pullup_5_out, pullup_6_out,
       pullup_7_out, pullup_8_out;

  _74273 _74273_1 (
    .pin1(REG_Clear), .pin2(_74273_1_pin2), .pin3(In[0]), .pin4(In[2]), .pin5(_74273_1_pin5),
    .pin6(_74273_1_pin6), .pin7(In[4]), .pin8(In[6]), .pin9(_74273_1_pin9), .pin10(1'b0), .pin11(REG_Clock),
    .pin12(_74273_1_pin12), .pin13(In[7]), .pin14(In[5]), .pin15(_74273_1_pin15), .pin16(_74273_1_pin16),
    .pin17(In[3]), .pin18(In[1]), .pin19(_74273_1_pin19), .pin20(1'b1));
  LED led_1 (.in(_74273_1_pin12));
  LED led_2 (.in(_74273_1_pin9));
  LED led_3 (.in(_74273_1_pin15));
  LED led_4 (.in(_74273_1_pin6));
  LED led_5 (.in(_74273_1_pin16));
  LED led_6 (.in(_74273_1_pin5));
  LED led_7 (.in(_74273_1_pin19));
  PullUp pullup_1 (.out(pullup_1_out));
  PullUp pullup_2 (.out(pullup_2_out));
  NFET nfet_1 (.G(Default[0]), .D(pullup_1_out), .S(Out[0]));
  NFET nfet_2 (.G(Default[1]), .D(pullup_2_out), .S(Out[1]));
  PFET pfet_1 (.G(Default[0]), .S(Out[0]), .D(pfet_1_d));
  PFET pfet_2 (.G(Default[1]), .S(Out[1]), .D(pfet_2_d));
  PullDown pulldown_1 (.out(pfet_1_d));
  PullDown pulldown_2 (.out(pfet_2_d));
  _74245 _74245_1 (
    .pin1(1'b1), .pin2(_74273_1_pin2), .pin3(_74273_1_pin19), .pin4(_74273_1_pin5), .pin5(_74273_1_pin16),
    .pin6(_74273_1_pin6), .pin7(_74273_1_pin15), .pin8(_74273_1_pin9), .pin9(_74273_1_pin12), .pin10(1'b0),
    .pin11(Out[7]), .pin12(Out[6]), .pin13(Out[5]), .pin14(Out[4]), .pin15(Out[3]), .pin16(Out[2]),
    .pin17(Out[1]), .pin18(Out[0]), .pin19(REG_OE), .pin20(1'b1));
  LED led_8 (.in(_74273_1_pin2));
  PullUp pullup_3 (.out(pullup_3_out));
  PullUp pullup_4 (.out(pullup_4_out));
  NFET nfet_3 (.G(Default[2]), .D(pullup_3_out), .S(Out[2]));
  NFET nfet_4 (.G(Default[3]), .D(pullup_4_out), .S(Out[3]));
  PFET pfet_3 (.G(Default[2]), .S(Out[2]), .D(pfet_3_d));
  PFET pfet_4 (.G(Default[3]), .S(Out[3]), .D(pfet_4_d));
  PullDown pulldown_3 (.out(pfet_3_d));
  PullDown pulldown_4 (.out(pfet_4_d));
  PullUp pullup_5 (.out(pullup_5_out));
  PullUp pullup_6 (.out(pullup_6_out));
  NFET nfet_5 (.G(Default[4]), .D(pullup_5_out), .S(Out[4]));
  NFET nfet_6 (.G(Default[5]), .D(pullup_6_out), .S(Out[5]));
  PFET pfet_5 (.G(Default[4]), .S(Out[4]), .D(pfet_5_d));
  PFET pfet_6 (.G(Default[5]), .S(Out[5]), .D(pfet_6_d));
  PullDown pulldown_5 (.out(pfet_5_d));
  PullDown pulldown_6 (.out(pfet_6_d));
  PullUp pullup_7 (.out(pullup_7_out));
  PullUp pullup_8 (.out(pullup_8_out));
  NFET nfet_7 (.G(Default[6]), .D(pullup_7_out), .S(Out[6]));
  NFET nfet_8 (.G(Default[7]), .D(pullup_8_out), .S(Out[7]));
  PFET pfet_7 (.G(Default[6]), .S(Out[6]), .D(pfet_7_d));
  PFET pfet_8 (.G(Default[7]), .S(Out[7]), .D(pfet_8_d));
  PullDown pulldown_7 (.out(pfet_7_d));
  PullDown pulldown_8 (.out(pfet_8_d));
  _74245 _74245_2 (
    .pin1(1'b1), .pin2(Out[0]), .pin3(Out[1]), .pin4(Out[2]), .pin5(Out[3]), .pin6(Out[4]), .pin7(Out[5]),
    .pin8(Out[6]), .pin9(Out[7]), .pin10(1'b0), .pin11(Disp[7]), .pin12(Disp[6]), .pin13(Disp[5]),
    .pin14(Disp[4]), .pin15(Disp[3]), .pin16(Disp[2]), .pin17(Disp[1]), .pin18(Disp[0]), .pin19(1'b0),
    .pin20(1'b1));

  // Notes on the sheet:
  //   D7..0
endmodule
