// Digital circuit Pipe_MEM_WB.dig as structural Verilog
module Pipe_MEM_WB (
  input  [31:0] PC_in,
  input  REGin_Clear,
  input  REGin_Clock,
  input  REGin_OE,
  input  [31:0] PC_nextin,
  input  [31:0] Mem_data_in,
  output [31:0] PC_out,
  output [31:0] PC_disp,
  output REGout_Clock,
  output REGout_OE,
  output REGout_Clear,
  output [31:0] PC_nextout,
  output [31:0] PC_nextdisp,
  output [31:0] Mem_data_out,
  output [31:0] Mem_data_disp
);

  PipeReg_32bit PC (
    .In(PC_in), .Default({32{1'b0}}), .REG_Clock(REGin_Clock), .REG_OE(REGin_OE), .REG_Clear(REGin_Clear),
    .Out(PC_out), .Disp(PC_disp));
  PipeReg_32bit PC_next (
    .In(PC_nextin), .Default({32{1'b0}}), .REG_Clock(REGin_Clock), .REG_OE(REGin_OE),
    .REG_Clear(REGin_Clear), .Out(PC_nextout), .Disp(PC_nextdisp));
  PipeReg_32bit Mem_wdata (
    .In(Mem_data_in), .Default({32{1'b0}}), .REG_Clock(REGin_Clock), .REG_OE(REGin_OE),
    .REG_Clear(REGin_Clear), .Out(Mem_data_out), .Disp(Mem_data_disp));

  assign REGout_Clear = REGin_Clear;
  assign REGout_Clock = REGin_Clock;
  assign REGout_OE = REGin_OE;

  // Other names for the same wires on the sheet: Clear = REGin_Clear; Clock = REGin_Clock; OE = REGin_OE

  // Notes on the sheet:
  //   Control
  //   Register
endmodule
