// Digital circuit Pipe_PC.dig as structural Verilog
module Pipe_PC (
  input  [31:0] PC_in,
  input  REGin_Clear,
  input  REGin_Clock,
  input  REGin_OE,
  output [31:0] PC_out,
  output [31:0] PC_disp
);

  PipeReg_32bit PC (
    .In(PC_in), .Default({32{1'b0}}), .REG_Clock(REGin_Clock), .REG_OE(REGin_OE), .REG_Clear(REGin_Clear),
    .Out(PC_out), .Disp(PC_disp));

  // Other names for the same wires on the sheet: Clear = REGin_Clear; Clock = REGin_Clock; OE = REGin_OE

  // Notes on the sheet:
  //   Control
  //   Register
endmodule
