// Digital circuit RegFile_Reg32bit.dig as structural Verilog
module RegFile_Reg32bit (
  input  OEa,
  input  OEb,
  input  Reset,
  input  Clock,
  input  Write,
  input  [31:0] DataIn,
  input  [31:0] a,
  input  [31:0] b,
  input  [31:0] disp
);

  wire and_1_out;

  and and_1 (and_1_out, Write, Clock);
  _74273 _74273_1 (
    .pin1(Reset), .pin2(disp[31]), .pin3(DataIn[31]), .pin4(DataIn[29]), .pin5(disp[29]), .pin6(disp[27]),
    .pin7(DataIn[27]), .pin8(DataIn[25]), .pin9(disp[25]), .pin10(1'b0), .pin11(and_1_out), .pin12(disp[24]),
    .pin13(DataIn[24]), .pin14(DataIn[26]), .pin15(disp[26]), .pin16(disp[28]), .pin17(DataIn[28]),
    .pin18(DataIn[30]), .pin19(disp[30]), .pin20(1'b1));
  _74273 _74273_2 (
    .pin1(Reset), .pin2(disp[23]), .pin3(DataIn[23]), .pin4(DataIn[21]), .pin5(disp[21]), .pin6(disp[19]),
    .pin7(DataIn[19]), .pin8(DataIn[17]), .pin9(disp[17]), .pin10(1'b0), .pin11(and_1_out), .pin12(disp[16]),
    .pin13(DataIn[16]), .pin14(DataIn[18]), .pin15(disp[18]), .pin16(disp[20]), .pin17(DataIn[20]),
    .pin18(DataIn[22]), .pin19(disp[22]), .pin20(1'b1));
  _74273 _74273_3 (
    .pin1(Reset), .pin2(disp[15]), .pin3(DataIn[15]), .pin4(DataIn[13]), .pin5(disp[13]), .pin6(disp[11]),
    .pin7(DataIn[11]), .pin8(DataIn[9]), .pin9(disp[9]), .pin10(1'b0), .pin11(and_1_out), .pin12(disp[8]),
    .pin13(DataIn[8]), .pin14(DataIn[10]), .pin15(disp[10]), .pin16(disp[12]), .pin17(DataIn[12]),
    .pin18(DataIn[14]), .pin19(disp[14]), .pin20(1'b1));
  _74273 _74273_4 (
    .pin1(Reset), .pin2(disp[7]), .pin3(DataIn[7]), .pin4(DataIn[5]), .pin5(disp[5]), .pin6(disp[3]),
    .pin7(DataIn[3]), .pin8(DataIn[1]), .pin9(disp[1]), .pin10(1'b0), .pin11(and_1_out), .pin12(disp[0]),
    .pin13(DataIn[0]), .pin14(DataIn[2]), .pin15(disp[2]), .pin16(disp[4]), .pin17(DataIn[4]),
    .pin18(DataIn[6]), .pin19(disp[6]), .pin20(1'b1));
  _74245 _74245_1 (
    .pin1(1'b1), .pin2(disp[31]), .pin3(disp[30]), .pin4(disp[29]), .pin5(disp[28]), .pin6(disp[27]),
    .pin7(disp[26]), .pin8(disp[25]), .pin9(disp[24]), .pin10(1'b0), .pin11(a[24]), .pin12(a[25]),
    .pin13(a[26]), .pin14(a[27]), .pin15(a[28]), .pin16(a[29]), .pin17(a[30]), .pin18(a[31]), .pin19(OEa),
    .pin20(1'b1));
  _74245 _74245_2 (
    .pin1(1'b1), .pin2(disp[23]), .pin3(disp[22]), .pin4(disp[21]), .pin5(disp[20]), .pin6(disp[19]),
    .pin7(disp[18]), .pin8(disp[17]), .pin9(disp[16]), .pin10(1'b0), .pin11(a[16]), .pin12(a[17]),
    .pin13(a[18]), .pin14(a[19]), .pin15(a[20]), .pin16(a[21]), .pin17(a[22]), .pin18(a[23]), .pin19(OEa),
    .pin20(1'b1));
  _74245 _74245_3 (
    .pin1(1'b1), .pin2(disp[15]), .pin3(disp[14]), .pin4(disp[13]), .pin5(disp[12]), .pin6(disp[11]),
    .pin7(disp[10]), .pin8(disp[9]), .pin9(disp[8]), .pin10(1'b0), .pin11(a[8]), .pin12(a[9]), .pin13(a[10]),
    .pin14(a[11]), .pin15(a[12]), .pin16(a[13]), .pin17(a[14]), .pin18(a[15]), .pin19(OEa), .pin20(1'b1));
  _74245 _74245_4 (
    .pin1(1'b1), .pin2(disp[7]), .pin3(disp[6]), .pin4(disp[5]), .pin5(disp[4]), .pin6(disp[3]),
    .pin7(disp[2]), .pin8(disp[1]), .pin9(disp[0]), .pin10(1'b0), .pin11(a[0]), .pin12(a[1]), .pin13(a[2]),
    .pin14(a[3]), .pin15(a[4]), .pin16(a[5]), .pin17(a[6]), .pin18(a[7]), .pin19(OEa), .pin20(1'b1));
  _74245 _74245_5 (
    .pin1(1'b1), .pin2(disp[31]), .pin3(disp[30]), .pin4(disp[29]), .pin5(disp[28]), .pin6(disp[27]),
    .pin7(disp[26]), .pin8(disp[25]), .pin9(disp[24]), .pin10(1'b0), .pin11(b[24]), .pin12(b[25]),
    .pin13(b[26]), .pin14(b[27]), .pin15(b[28]), .pin16(b[29]), .pin17(b[30]), .pin18(b[31]), .pin19(OEb),
    .pin20(1'b1));
  _74245 _74245_6 (
    .pin1(1'b1), .pin2(disp[23]), .pin3(disp[22]), .pin4(disp[21]), .pin5(disp[20]), .pin6(disp[19]),
    .pin7(disp[18]), .pin8(disp[17]), .pin9(disp[16]), .pin10(1'b0), .pin11(b[16]), .pin12(b[17]),
    .pin13(b[18]), .pin14(b[19]), .pin15(b[20]), .pin16(b[21]), .pin17(b[22]), .pin18(b[23]), .pin19(OEb),
    .pin20(1'b1));
  _74245 _74245_7 (
    .pin1(1'b1), .pin2(disp[15]), .pin3(disp[14]), .pin4(disp[13]), .pin5(disp[12]), .pin6(disp[11]),
    .pin7(disp[10]), .pin8(disp[9]), .pin9(disp[8]), .pin10(1'b0), .pin11(b[8]), .pin12(b[9]), .pin13(b[10]),
    .pin14(b[11]), .pin15(b[12]), .pin16(b[13]), .pin17(b[14]), .pin18(b[15]), .pin19(OEb), .pin20(1'b1));
  _74245 _74245_8 (
    .pin1(1'b1), .pin2(disp[7]), .pin3(disp[6]), .pin4(disp[5]), .pin5(disp[4]), .pin6(disp[3]),
    .pin7(disp[2]), .pin8(disp[1]), .pin9(disp[0]), .pin10(1'b0), .pin11(b[0]), .pin12(b[1]), .pin13(b[2]),
    .pin14(b[3]), .pin15(b[4]), .pin16(b[5]), .pin17(b[6]), .pin18(b[7]), .pin19(OEb), .pin20(1'b1));

  // Notes on the sheet:
  //   D31..24
  //   D23..16
  //   D15..8
  //   D7..0
endmodule
