// Digital circuit Reset.Unit.dig as structural Verilog
module Reset_Unit (
  input  Reset_In,
  input  Clock,
  output Reset_Out
);

  wire _74193_1_pin13, nand_1_out, nand_2_out, nand_3_out, nand_4_out, nand_5_out, nand_6_out,
       polarityawareled_1_p1, polarityawareled_2_p1, polarityawareled_3_p1, polarityawareled_4_p1;
  wire [3:0] _74193_1_pin9;

  PullUp pullup_1 (.out(Reset_In));
  nand nand_1 (nand_1_out, Clock, nand_2_out);
  // PolarityAwareLED polarityawareled_1: pin names not known; wires that end beside it: polarityawareled_1_p1, 1'b0
  // PolarityAwareLED polarityawareled_2: pin names not known; wires that end beside it: polarityawareled_2_p1, 1'b0
  // PolarityAwareLED polarityawareled_3: pin names not known; wires that end beside it: polarityawareled_3_p1, 1'b0
  // PolarityAwareLED polarityawareled_4: pin names not known; wires that end beside it: polarityawareled_4_p1, 1'b0
  _74193 _74193_1 (
    .pin1(_74193_1_pin9[1]), .pin2(polarityawareled_3_p1), .pin3(polarityawareled_2_p1), .pin4(nand_1_out),
    .pin5(1'b1), .pin6(polarityawareled_4_p1), .pin7(polarityawareled_1_p1), .pin8(1'b0),
    .pin9(_74193_1_pin9[3]), .pin10(_74193_1_pin9[2]), .pin11(Reset_In), .pin13(_74193_1_pin13),
    .pin14(1'b0), .pin15(_74193_1_pin9[0]), .pin16(1'b1));  // open: pin12
  DipSwitch dipswitch_1 (.out(_74193_1_pin9[3]));
  DipSwitch dipswitch_2 (.out(_74193_1_pin9[2]));
  DipSwitch #(.dipDefault("true")) dipswitch_3 (.out(_74193_1_pin9[1]));
  DipSwitch #(.dipDefault("true")) dipswitch_4 (.out(_74193_1_pin9[0]));
  // Probe on _74193_1_pin9
  nand nand_2 (nand_2_out, Reset_In, nand_3_out);
  nand nand_3 (nand_3_out, nand_2_out, _74193_1_pin13);
  nand nand_4 (nand_4_out, nand_3_out, nand_5_out);
  nand nand_5 (nand_5_out, Clock, Clock);
  nand nand_6 (nand_6_out, Reset_In, Reset_Out);
  nand nand_7 (Reset_Out, nand_6_out, nand_4_out);
  // PolarityAwareLED polarityawareled_5: pin names not known; wires that end beside it: nand_6_out, Reset_Out, 1'b1
  _7400 _7400_1 (
    .pin1(1'b0), .pin2(1'b0), .pin4(1'b0), .pin5(1'b0), .pin7(1'b0), .pin9(1'b0), .pin10(1'b0), .pin12(1'b0),
    .pin13(1'b0), .pin14(1'b1));  // open: pin3, pin6, pin8, pin11
  _7400 _7400_2 (
    .pin1(1'b0), .pin2(1'b0), .pin4(1'b0), .pin5(1'b0), .pin7(1'b0), .pin9(1'b0), .pin10(1'b0), .pin12(1'b0),
    .pin13(1'b0), .pin14(1'b1));  // open: pin3, pin6, pin8, pin11
  // NAnd nand_8 has open pins: In_1=1'b0, In_2=1'b0, out=open

  // Notes on the sheet:
  //   Num of Clock-Cycles (-1)
  //   FF
  //   /SET
  //   /RESET
  //   /Q
  //   Q
  //   /Reset goes High on
  //   the falling edge of Clock
  //   Chips for the Gates
endmodule
