// Digital circuit _CPU.dig as structural Verilog
module CPU (
  input  Clk_Slow,
  input  Clk_Fast,
  input  Clk_Manual
);

  wire alu_1_z, and_2_out, and_3_out, BR_taken, Branch, counter_3_ovf, counter_4_ovf, CPU_Clock, CPU_Reset,
       Debug_out, delay_1_out, dipswitch_33_out, dipswitch_34_out, dipswitch_35_out, Exe_MemRd, Exe_rd,
       Exe_we, Fast_out, Halt_2_out, ID_stall, instr_decoder_1_b_mux, instr_decoder_1_branch,
       instr_decoder_1_mem_rd, instr_decoder_1_mem_wr, instr_decoder_1_valid, instr_decoder_1_wb_we,
       instr_display_1_iadd, instr_display_1_iaddi, instr_display_1_iand, instr_display_1_iandi,
       instr_display_1_iauipc, instr_display_1_ibeq, instr_display_1_ibge, instr_display_1_ibgeu,
       instr_display_1_iblt, instr_display_1_ibltu, instr_display_1_ibne, instr_display_1_icsraddr0,
       instr_display_1_icsraddr1, instr_display_1_icsraddr2, instr_display_1_icsraddr3,
       instr_display_1_icsraddr4, instr_display_1_icsraddr5, instr_display_1_icsraddr6,
       instr_display_1_icsraddr7, instr_display_1_icsraddr8, instr_display_1_icsraddr9,
       instr_display_1_icsraddr10, instr_display_1_icsraddr11, instr_display_1_icsrrc,
       instr_display_1_icsrrci, instr_display_1_icsrrs, instr_display_1_icsrrsi, instr_display_1_icsrrw,
       instr_display_1_icsrrwi, instr_display_1_idiv, instr_display_1_idivu, instr_display_1_iebreak,
       instr_display_1_iecall, instr_display_1_ifence, instr_display_1_ifence_i, instr_display_1_ifence_tso,
       instr_display_1_ijal, instr_display_1_ijalr, instr_display_1_ilb, instr_display_1_ilbu,
       instr_display_1_ilh, instr_display_1_ilhu, instr_display_1_ilui, instr_display_1_ilw,
       instr_display_1_imul, instr_display_1_imulh, instr_display_1_imulhsu, instr_display_1_imulhu,
       instr_display_1_inop, instr_display_1_ior, instr_display_1_iori, instr_display_1_irem,
       instr_display_1_iremu, instr_display_1_isb, instr_display_1_ish, instr_display_1_isll,
       instr_display_1_islli, instr_display_1_islt, instr_display_1_islti, instr_display_1_isltiu,
       instr_display_1_isltu, instr_display_1_isra, instr_display_1_israi, instr_display_1_isrl,
       instr_display_1_isrli, instr_display_1_isub, instr_display_1_isw, instr_display_1_ixor,
       instr_display_1_ixori, instr_display_1_op48bit1, instr_display_1_op48bit2, instr_display_1_op64bit,
       instr_display_1_op80bit, instr_display_1_opamo, instr_display_1_opauipc, instr_display_1_opbranch,
       instr_display_1_opcust0, instr_display_1_opcust1, instr_display_1_opcust2, instr_display_1_opcust3,
       instr_display_1_opjal, instr_display_1_opjalr, instr_display_1_opload, instr_display_1_opload_fp,
       instr_display_1_oplui, instr_display_1_opmadd, instr_display_1_opmisc_mem, instr_display_1_opmsub,
       instr_display_1_opnmadd, instr_display_1_opnmsub, instr_display_1_opop, instr_display_1_opop_32,
       instr_display_1_opop_fp, instr_display_1_opop_imm, instr_display_1_opop_imm_32,
       instr_display_1_opres0, instr_display_1_opres1, instr_display_1_opres2, instr_display_1_opstore,
       instr_display_1_opstore_fp, instr_display_1_opsystem, Jump, Manual_out, Mem_rd, Mem_we, nand_1_out,
       not_1_out, not_2_out, not_3_out, not_4_out, not_5_out, not_6_out, or_2_out, or_3_out,
       pipe_exe_mem_1_p5, pipe_exe_mem_1_p6, pipe_exe_mem_1_p7, pipe_exe_mem_1_p8, pipe_exe_mem_1_p9,
       pipe_id_exe_1_p6, pipe_id_exe_1_p7, pipe_id_exe_1_p8, pipe_id_exe_1_p9, pipe_id_exe_1_p10,
       pipe_id_exe_1_p12, pipe_id_exe_1_p13, pipe_mem_wb_1_p4, pipe_mem_wb_1_p5, pipe_mem_wb_1_p6,
       pipectrl_1__1cc, pipectrl_1_led_busy, pipectrl_1_led_empty, pipectrl_1_led_valid,
       pipectrl_1_led_waiting, pipectrl_1_reg_clear, pipectrl_1_reg_clock, pipectrl_1_reg_oe,
       pipectrl_1_valid__this, pipectrl_2_led_busy, pipectrl_2_led_empty, pipectrl_2_led_valid,
       pipectrl_2_led_waiting, pipectrl_2_ready__prev, pipectrl_2_reg_clear, pipectrl_2_reg_clock,
       pipectrl_2_reg_oe, pipectrl_2_valid__this, pipectrl_3__1cc, pipectrl_3_led_busy, pipectrl_3_led_empty,
       pipectrl_3_led_valid, pipectrl_3_led_waiting, pipectrl_3_ready__prev, pipectrl_3_valid__this,
       pipectrl_4__1cc, pipectrl_4_led_busy, pipectrl_4_led_empty, pipectrl_4_led_valid,
       pipectrl_4_led_waiting, pipectrl_4_ready__prev, pipectrl_4_valid__this, pipectrl_5__1cc,
       pipectrl_5_led_busy, pipectrl_5_led_empty, pipectrl_5_led_valid, pipectrl_5_led_waiting,
       pipectrl_5_ready__prev, pipectrl_5_valid__this, pipereg_mem_1_p5, pipereg_mem_1_p6, pipereg_mem_1_p8,
       pipereg_mem_2_p7, pipereg_mem_2_p8, pullup_1_out, pullup_2_out, PwrOn_Reset_out, Reset_out,
       rs_ff_as_1_q, RVC_enabled_out, Slow_out, WB_we;
  wire [0:0] instr_decoder_1_a_mux;
  wire [1:0] A_mux, B_mux, instr_decoder_1_br_ctrl, instr_decoder_1_j_ctrl, instr_decoder_1_mem_mux,
       pipereg_branch_1_p4, pipereg_mem_2_p5;
  wire [2:0] instr_decoder_1_imm_ctrl, instr_decoder_1_mem_sz, pipereg_mem_2_p6;
  wire [2:1] to_b_of_PC_adder;
  wire [3:0] multiplexer_7_out, pulldown_2_out;
  wire [4:0] ID_Rs1, ID_Rs2, instr_decoder_1_alu_ctrl, instr_decoder_1_wb_reg, pipereg_exe_1_p2, WB_reg;
  wire [29:0] regfile_1_disp_r0, regfile_1_disp_r1, regfile_1_disp_r2, regfile_1_disp_r3, regfile_1_disp_r4,
       regfile_1_disp_r5, regfile_1_disp_r6, regfile_1_disp_r7, regfile_1_disp_r8, regfile_1_disp_r9,
       regfile_1_disp_r10, regfile_1_disp_r11, regfile_1_disp_r12, regfile_1_disp_r13, regfile_1_disp_r14,
       regfile_1_disp_r15, regfile_1_disp_r16, regfile_1_disp_r17, regfile_1_disp_r18, regfile_1_disp_r19,
       regfile_1_disp_r20, regfile_1_disp_r21, regfile_1_disp_r22, regfile_1_disp_r23, regfile_1_disp_r24,
       regfile_1_disp_r25, regfile_1_disp_r26, regfile_1_disp_r27, regfile_1_disp_r28, regfile_1_disp_r29,
       regfile_1_disp_r30, regfile_1_disp_r31;
  wire [31:0] basicadder_1_y, BR_addr, counter_1_out, counter_2_out, counter_3_out, counter_4_out, Data_d,
       dipswitch_32_out, Exe_data, imm_decoder_1_imm, instr, J_addr, Mem_data, mem_ext_1_out,
       multiplexer_1_out, multiplexer_2_out, multiplexer_3_out, multiplexer_4_out, multiplexer_5_out,
       multiplexer_6_out, pipe_exe_mem_1_p10, pipe_exe_mem_1_p11, pipe_exe_mem_1_p12, pipe_id_exe_1_p11,
       pipe_id_exe_1_p14, pipe_if_id_1_instr_disp, pipe_if_id_1_instr_out, pipe_if_id_1_pc_disp,
       pipe_if_id_1_pc_nextdisp, pipe_if_id_1_pc_nextout, pipe_if_id_1_pc_out, pipe_pc_1_pc_disp,
       pipe_pc_1_pc_out, Progr_d, regfile_1_rd1, regfile_1_rd2, undriven, undriven_2, WB_data;

  DipSwitch dipswitch_1 (.out(dipswitch_32_out[31]));
  DipSwitch dipswitch_2 (.out(dipswitch_32_out[30]));
  DipSwitch dipswitch_3 (.out(dipswitch_32_out[29]));
  // Probe on {{29{1'b0}}, to_b_of_PC_adder, 1'b0}
  DipSwitch dipswitch_4 (.out(dipswitch_32_out[28]));
  DipSwitch dipswitch_5 (.out(dipswitch_32_out[27]));
  DipSwitch dipswitch_6 (.out(dipswitch_32_out[26]));
  DipSwitch dipswitch_7 (.out(dipswitch_32_out[25]));
  DipSwitch dipswitch_8 (.out(dipswitch_32_out[24]));
  DipSwitch dipswitch_9 (.out(dipswitch_32_out[23]));
  DipSwitch dipswitch_10 (.out(dipswitch_32_out[22]));
  DipSwitch dipswitch_11 (.out(dipswitch_32_out[21]));
  DipSwitch dipswitch_12 (.out(dipswitch_32_out[20]));
  DipSwitch dipswitch_13 (.out(dipswitch_32_out[19]));
  DipSwitch dipswitch_14 (.out(dipswitch_32_out[18]));
  DipSwitch dipswitch_15 (.out(dipswitch_32_out[17]));
  or or_1 (to_b_of_PC_adder[2], not_1_out, and_2_out);
  not not_1 (not_1_out, to_b_of_PC_adder[1]);
  and and_1 (to_b_of_PC_adder[1], RVC_enabled_out, not_2_out);
  DipSwitch RVC_enabled (.out(RVC_enabled_out));
  DipSwitch dipswitch_16 (.out(dipswitch_32_out[16]));
  DipSwitch dipswitch_17 (.out(dipswitch_32_out[15]));
  DipSwitch dipswitch_18 (.out(dipswitch_32_out[14]));
  DipSwitch dipswitch_19 (.out(dipswitch_32_out[13]));
  not not_2 (not_2_out, and_2_out);
  DipSwitch dipswitch_20 (.out(dipswitch_32_out[12]));
  DipSwitch dipswitch_21 (.out(dipswitch_32_out[11]));
  DipSwitch dipswitch_22 (.out(dipswitch_32_out[10]));
  DipSwitch dipswitch_23 (.out(dipswitch_32_out[9]));
  and and_2 (and_2_out, instr[0], instr[1]);
  DipSwitch dipswitch_24 (.out(dipswitch_32_out[8]));
  DipSwitch dipswitch_25 (.out(dipswitch_32_out[7]));
  DipSwitch dipswitch_26 (.out(dipswitch_32_out[6]));
  DipSwitch dipswitch_27 (.out(dipswitch_32_out[5]));
  DipSwitch dipswitch_28 (.out(dipswitch_32_out[4]));
  DipSwitch dipswitch_29 (.out(dipswitch_32_out[3]));
  DipSwitch dipswitch_30 (.out(dipswitch_32_out[2]));
  DipSwitch #(.dipDefault("true")) dipswitch_31 (.out(dipswitch_32_out[1]));
  // Probe on dipswitch_32_out
  LED led_1 (.in(1'b1));
  DipSwitch #(.dipDefault("true")) dipswitch_32 (.out(dipswitch_32_out[0]));
  LED led_2 (.in(1'b1));
  LED led_3 (.in(1'b1));
  LED led_4 (.in(1'b1));
  LED led_5 (.in(1'b1));
  // Probe on multiplexer_1_out
  // Probe on multiplexer_2_out
  LED led_6 (.in(1'b1));
  LED led_7 (.in(1'b1));
  LED led_8 (.in(1'b1));
  LED led_9 (.in(1'b1));
  LED led_10 (.in(1'b1));
  LED led_11 (.in(1'b1));
  LED led_12 (.in(1'b1));
  Multiplexer #(.Selector_Bits(2), .Bits(32)) multiplexer_1 (
    .sel({Jump, BR_taken}), .in_0(basicadder_1_y), .in_1(BR_addr), .in_2(J_addr), .in_3(BR_addr),
    .out(multiplexer_1_out));
  Multiplexer #(.Bits(32)) multiplexer_2 (
    .sel(rs_ff_as_1_q), .in_0(32'h100), .in_1(multiplexer_1_out), .out(multiplexer_2_out));
  Pipe_PC pipe_pc_1 (
    .PC_in(multiplexer_2_out), .PC_out(pipe_pc_1_pc_out), .PC_disp(pipe_pc_1_pc_disp),
    .REGin_Clear(pipectrl_1_reg_clear), .REGin_Clock(pipectrl_1_reg_clock), .REGin_OE(pipectrl_1_reg_oe));
  PipeCtrl pipectrl_1 (
    .Valid__this(pipectrl_1_valid__this), .Ready__next(pipectrl_2_ready__prev),
    .Done__this(dipswitch_33_out), ._1cc(pipectrl_1__1cc), .Clock(CPU_Clock), .Reset(CPU_Reset),
    .Flush(or_2_out), .REG_Clear(pipectrl_1_reg_clear), .REG_Clock(pipectrl_1_reg_clock),
    .REG_OE(pipectrl_1_reg_oe), .LED_Valid(pipectrl_1_led_valid), .LED_Busy(pipectrl_1_led_busy),
    .LED_Waiting(pipectrl_1_led_waiting), .LED_Empty(pipectrl_1_led_empty));  // open: Valid__prev, Ready__prev
  LED led_13 (.in(or_2_out));
  LED led_14 (.in(1'b1));
  LED led_15 (.in(1'b1));
  LED led_16 (.in(1'b1));
  LED led_17 (.in(1'b1));
  LED led_18 (.in(1'b1));
  LED led_19 (.in(1'b1));
  LED led_20 (.in(1'b1));
  LED led_21 (.in(1'b1));
  RS_FF_AS rs_ff_as_1 (.S(pipectrl_1_valid__this), .R(not_4_out), .Q(rs_ff_as_1_q));  // open: nQ
  LED Busy (.in(pipectrl_1_led_busy));
  LED Valid (.in(pipectrl_1_led_valid));
  or or_2 (or_2_out, BR_taken, Jump);
  Button #(.activeLow("true")) Manual (.out(Manual_out));
  Button #(.activeLow("true")) Slow (.out(Slow_out));
  Button #(.activeLow("true")) Fast (.out(Fast_out));
  LED Halt (.in(not_3_out));
  not not_3 (not_3_out, pullup_2_out);
  LED led_22 (.in(1'b1));
  LED led_23 (.in(1'b1));
  LED led_24 (.in(1'b1));
  LED led_25 (.in(1'b1));
  LED led_26 (.in(1'b1));
  LED led_27 (.in(1'b1));
  LED led_28 (.in(1'b1));
  LED led_29 (.in(1'b1));
  LED led_30 (.in(1'b1));
  LED led_31 (.in(1'b1));
  LED led_32 (.in(1'b1));
  LED led_33 (.in(1'b1));
  BasicAdder basicadder_1 (.A(pipe_pc_1_pc_out), .B(32'h4), .Y(basicadder_1_y));
  not not_4 (not_4_out, CPU_Reset);
  // Probe on pipe_pc_1_pc_disp
  LED Wait (.in(pipectrl_1_led_waiting));
  LED Empty (.in(pipectrl_1_led_empty));
  ClockCtrl clockctrl_1 (
    .Sel_Man(Manual_out), .Clk_Man(Clk_Manual), .Sel_Slow(Slow_out), .Clk_Slow(Clk_Slow),
    .Sel_Fast(Fast_out), .Clk_Fast(Clk_Fast), .Halt(pullup_2_out), .Reset(pullup_1_out), .Clk_Out(CPU_Clock));
  LED led_34 (.in(1'b1));
  LED led_35 (.in(1'b1));
  LED led_36 (.in(1'b1));
  LED led_37 (.in(1'b1));
  LED led_38 (.in(1'b1));
  LED led_39 (.in(1'b1));
  LED led_40 (.in(1'b1));
  LED led_41 (.in(1'b1));
  LED led_42 (.in(pipectrl_1__1cc));
  DipSwitch #(.dipDefault("true")) dipswitch_33 (.out(dipswitch_33_out));
  LED led_43 (.in(1'b1));
  LED led_44 (.in(1'b1));
  LED led_45 (.in(1'b1));
  LED led_46 (.in(1'b1));
  LED led_47 (.in(1'b1));
  LED led_48 (.in(1'b1));
  LED led_49 (.in(1'b1));
  LED led_50 (.in(1'b1));
  LED led_51 (.in(1'b1));
  LED led_52 (.in(1'b1));
  // PolarityAwareLED polarityawareled_1: pin names not known; wires that end beside it: CPU_Clock, 1'b0
  PullUp pullup_1 (.out(pullup_1_out));
  PullUp pullup_2 (.out(pullup_2_out));
  LED led_53 (.in(1'b1));
  LED led_54 (.in(1'b1));
  LED led_55 (.in(1'b1));
  LED led_56 (.in(1'b1));
  LED led_57 (.in(1'b1));
  LED led_58 (.in(1'b1));
  LED led_59 (.in(1'b1));
  LED led_60 (.in(1'b1));
  LED led_61 (.in(1'b1));
  LED led_62 (.in(1'b1));
  ROM #(.AddrBits(16), .Bits(32)) Progr (.A(pipe_pc_1_pc_out[17:2]), .sel(1'b1), .D(Progr_d));
  Reset_Unit reset_unit_1 (.Clock(CPU_Clock), .Reset_In(pullup_1_out), .Reset_Out(CPU_Reset));
  PFET pfet_1 (.G(PwrOn_Reset_out), .S(1'b0), .D(pullup_1_out));
  PFET pfet_2 (.G(Reset_out), .S(1'b0), .D(pullup_1_out));
  PFET pfet_3 (.G(Halt_2_out), .S(1'b0), .D(pullup_2_out));
  LED led_63 (.in(1'b1));
  LED led_64 (.in(1'b1));
  LED led_65 (.in(1'b1));
  LED led_66 (.in(1'b1));
  LED led_67 (.in(1'b1));
  LED led_68 (.in(1'b1));
  LED led_69 (.in(1'b1));
  LED led_70 (.in(1'b1));
  LED led_71 (.in(1'b1));
  Reset PwrOn_Reset (.out(PwrOn_Reset_out));
  Button #(.activeLow("true")) Reset (.out(Reset_out));
  Button #(.activeLow("true")) Halt_2 (.out(Halt_2_out));
  LED led_72 (.in(1'b1));
  LED led_73 (.in(1'b1));
  LED led_74 (.in(1'b1));
  LED led_75 (.in(1'b1));
  LED led_76 (.in(1'b1));
  LED led_77 (.in(1'b1));
  assign instr = ~Debug_out ? Progr_d : 32'bz;  // DriverInvSel driverinvsel_1
  assign instr = Debug_out ? dipswitch_32_out : 32'bz;  // Driver driver_1
  PullDown #(.Bits(32)) pulldown_1 (.out(instr));
  DipSwitch Debug (.out(Debug_out));
  // PolarityAwareLED polarityawareled_2: pin names not known; wires that end beside it: 1'b1, CPU_Reset
  Pipe_IF_ID pipe_if_id_1 (
    .PC_in(pipe_pc_1_pc_out), .Instr_in(instr), .PC_out(pipe_if_id_1_pc_out), .PC_disp(pipe_if_id_1_pc_disp),
    .Instr_out(pipe_if_id_1_instr_out), .Instr_disp(pipe_if_id_1_instr_disp),
    .REGin_Clear(pipectrl_2_reg_clear), .REGin_Clock(pipectrl_2_reg_clock), .REGin_OE(pipectrl_2_reg_oe),
    .PC_nextin(basicadder_1_y), .PC_nextout(pipe_if_id_1_pc_nextout), .PC_nextdisp(pipe_if_id_1_pc_nextdisp));  // open: REGout_Clock, REGout_OE, REGout_Clear
  PipeCtrl pipectrl_2 (
    .Valid__prev(pipectrl_1_valid__this), .Ready__prev(pipectrl_2_ready__prev),
    .Valid__this(pipectrl_2_valid__this), .Ready__next(pipectrl_3_ready__prev), .Done__this(ID_stall),
    .Clock(CPU_Clock), .Reset(CPU_Reset), .Flush(BR_taken), .REG_Clear(pipectrl_2_reg_clear),
    .REG_Clock(pipectrl_2_reg_clock), .REG_OE(pipectrl_2_reg_oe), .LED_Valid(pipectrl_2_led_valid),
    .LED_Busy(pipectrl_2_led_busy), .LED_Waiting(pipectrl_2_led_waiting), .LED_Empty(pipectrl_2_led_empty));  // open: _1cc
  LED Valid_2 (.in(pipectrl_2_led_valid));
  LED led_78 (.in(BR_taken));
  Instr_Display instr_display_1 (
    .opLOAD(instr_display_1_opload), .opLOAD_FP(instr_display_1_opload_fp),
    .opCUST0(instr_display_1_opcust0), .opMISC_MEM(instr_display_1_opmisc_mem),
    .opOP_IMM(instr_display_1_opop_imm), .opAUIPC(instr_display_1_opauipc),
    .opOP_IMM_32(instr_display_1_opop_imm_32), .op48BIT1(instr_display_1_op48bit1),
    .opSTORE(instr_display_1_opstore), .opSTORE_FP(instr_display_1_opstore_fp),
    .opCUST1(instr_display_1_opcust1), .opAMO(instr_display_1_opamo), .opOP(instr_display_1_opop),
    .opLUI(instr_display_1_oplui), .opOP_32(instr_display_1_opop_32), .op64BIT(instr_display_1_op64bit),
    .opMADD(instr_display_1_opmadd), .opMSUB(instr_display_1_opmsub), .opNMSUB(instr_display_1_opnmsub),
    .opNMADD(instr_display_1_opnmadd), .opOP_FP(instr_display_1_opop_fp), .opRES0(instr_display_1_opres0),
    .opCUST2(instr_display_1_opcust2), .op48BIT2(instr_display_1_op48bit2),
    .opBRANCH(instr_display_1_opbranch), .opJALR(instr_display_1_opjalr), .opRES1(instr_display_1_opres1),
    .opJAL(instr_display_1_opjal), .opSYSTEM(instr_display_1_opsystem), .opRES2(instr_display_1_opres2),
    .opCUST3(instr_display_1_opcust3), .op80BIT(instr_display_1_op80bit), .Inst(pipe_if_id_1_instr_out),
    .iJAL(instr_display_1_ijal), .iJALR(instr_display_1_ijalr), .iBEQ(instr_display_1_ibeq),
    .iBNE(instr_display_1_ibne), .iBLT(instr_display_1_iblt), .iBGE(instr_display_1_ibge),
    .iBLTU(instr_display_1_ibltu), .iBGEU(instr_display_1_ibgeu), .iLUI(instr_display_1_ilui),
    .iAUIPC(instr_display_1_iauipc), .iLB(instr_display_1_ilb), .iLH(instr_display_1_ilh),
    .iLW(instr_display_1_ilw), .iLBU(instr_display_1_ilbu), .iLHU(instr_display_1_ilhu),
    .iSB(instr_display_1_isb), .iSH(instr_display_1_ish), .iSW(instr_display_1_isw),
    .iSLLI(instr_display_1_islli), .iSRLI(instr_display_1_isrli), .iSRAI(instr_display_1_israi),
    .iXORI(instr_display_1_ixori), .iORI(instr_display_1_iori), .iANDI(instr_display_1_iandi),
    .iSLTI(instr_display_1_islti), .iSLTIU(instr_display_1_isltiu), .iADDI(instr_display_1_iaddi),
    .iFENCE(instr_display_1_ifence), .iFENCE_TSO(instr_display_1_ifence_tso),
    .iECALL(instr_display_1_iecall), .iEBREAK(instr_display_1_iebreak), .iNOP(instr_display_1_inop),
    .iSLL(instr_display_1_isll), .iSRL(instr_display_1_isrl), .iSRA(instr_display_1_isra),
    .iXOR(instr_display_1_ixor), .iOR(instr_display_1_ior), .iAND(instr_display_1_iand),
    .iSLT(instr_display_1_islt), .iSLTU(instr_display_1_isltu), .iADD(instr_display_1_iadd),
    .iSUB(instr_display_1_isub), .iCSRRW(instr_display_1_icsrrw), .iCSRRS(instr_display_1_icsrrs),
    .iCSRRC(instr_display_1_icsrrc), .iMUL(instr_display_1_imul), .iMULH(instr_display_1_imulh),
    .iMULHSU(instr_display_1_imulhsu), .iMULHU(instr_display_1_imulhu), .iDIV(instr_display_1_idiv),
    .iDIVU(instr_display_1_idivu), .iREM(instr_display_1_irem), .iREMU(instr_display_1_iremu),
    .iCSRRWI(instr_display_1_icsrrwi), .iCSRRSI(instr_display_1_icsrrsi), .iCSRRCI(instr_display_1_icsrrci),
    .iFENCE_I(instr_display_1_ifence_i), .iCSRaddr0(instr_display_1_icsraddr0),
    .iCSRaddr1(instr_display_1_icsraddr1), .iCSRaddr2(instr_display_1_icsraddr2),
    .iCSRaddr3(instr_display_1_icsraddr3), .iCSRaddr4(instr_display_1_icsraddr4),
    .iCSRaddr5(instr_display_1_icsraddr5), .iCSRaddr6(instr_display_1_icsraddr6),
    .iCSRaddr7(instr_display_1_icsraddr7), .iCSRaddr8(instr_display_1_icsraddr8),
    .iCSRaddr9(instr_display_1_icsraddr9), .iCSRaddr10(instr_display_1_icsraddr10),
    .iCSRaddr11(instr_display_1_icsraddr11));  // open: Illegal
  LED Busy_2 (.in(pipectrl_2_led_busy));
  LED Wait_2 (.in(pipectrl_2_led_waiting));
  LED led_79 (.in(instr_display_1_opload));
  LED led_80 (.in(instr_display_1_opstore));
  LED led_81 (.in(instr_display_1_opmadd));
  LED led_82 (.in(instr_display_1_opbranch));
  LED led_83 (.in(instr_display_1_ijal));
  LED led_84 (.in(instr_display_1_ijalr));
  LED led_85 (.in(instr_display_1_ibeq));
  LED led_86 (.in(instr_display_1_ibne));
  LED led_87 (.in(instr_display_1_iblt));
  LED led_88 (.in(instr_display_1_ibge));
  LED led_89 (.in(instr_display_1_ibltu));
  LED led_90 (.in(instr_display_1_ibgeu));
  LED led_91 (.in(instr_display_1_ilui));
  LED led_92 (.in(instr_display_1_iauipc));
  LED led_93 (.in(instr_display_1_ifence_i));
  LED led_94 (.in(instr_display_1_icsrrw));
  LED led_95 (.in(instr_display_1_icsrrs));
  LED led_96 (.in(instr_display_1_icsrrc));
  LED led_97 (.in(instr_display_1_imul));
  LED led_98 (.in(instr_display_1_imulh));
  LED led_99 (.in(instr_display_1_imulhsu));
  LED led_100 (.in(instr_display_1_imulhu));
  // Probe on pipe_if_id_1_pc_disp
  // Probe on pipe_if_id_1_pc_nextdisp
  // Probe on pipe_if_id_1_instr_disp
  LED Empty_2 (.in(pipectrl_2_led_empty));
  PFET pfet_4 (.G(nand_1_out), .S(1'b0), .D(pullup_2_out));
  LED led_101 (.in(instr_display_1_opload_fp));
  LED led_102 (.in(instr_display_1_opstore_fp));
  LED led_103 (.in(instr_display_1_opmsub));
  LED led_104 (.in(instr_display_1_opjalr));
  LED led_105 (.in(instr_display_1_ilb));
  LED led_106 (.in(instr_display_1_ilh));
  LED led_107 (.in(instr_display_1_ilw));
  LED led_108 (.in(instr_display_1_ilbu));
  LED led_109 (.in(instr_display_1_ilhu));
  LED led_110 (.in(instr_display_1_isb));
  LED led_111 (.in(instr_display_1_ish));
  LED led_112 (.in(instr_display_1_isw));
  LED led_113 (.in(instr_display_1_icsrrwi));
  LED led_114 (.in(instr_display_1_icsrrsi));
  LED led_115 (.in(instr_display_1_icsrrci));
  LED led_116 (.in(instr_display_1_idiv));
  LED led_117 (.in(instr_display_1_idivu));
  LED led_118 (.in(instr_display_1_irem));
  LED led_119 (.in(instr_display_1_iremu));
  Instr_Decoder instr_decoder_1 (
    .Inst(pipe_if_id_1_instr_out), .Valid(instr_decoder_1_valid), .J_ctrl(instr_decoder_1_j_ctrl),
    .Jump(Jump), .Rs1(ID_Rs1), .Rs2(ID_Rs2), .A_mux(instr_decoder_1_a_mux[0]), .B_mux(instr_decoder_1_b_mux),
    .Imm_ctrl(instr_decoder_1_imm_ctrl), .Branch(instr_decoder_1_branch), .BR_ctrl(instr_decoder_1_br_ctrl),
    .ALU_ctrl(instr_decoder_1_alu_ctrl), .Mem_mux(instr_decoder_1_mem_mux), .Mem_sz(instr_decoder_1_mem_sz),
    .Mem_rd(instr_decoder_1_mem_rd), .Mem_wr(instr_decoder_1_mem_wr), .WB_we(instr_decoder_1_wb_we),
    .WB_reg(instr_decoder_1_wb_reg));
  nand nand_1 (nand_1_out, ~instr_decoder_1_valid, pipectrl_2_valid__this);  // NAnd
  LED led_120 (.in(instr_display_1_opcust0));
  LED led_121 (.in(instr_display_1_opcust1));
  LED led_122 (.in(instr_display_1_opnmsub));
  LED led_123 (.in(instr_display_1_opres1));
  LED led_124 (.in(instr_display_1_islli));
  LED led_125 (.in(instr_display_1_isrli));
  LED led_126 (.in(instr_display_1_israi));
  LED led_127 (.in(instr_display_1_ixori));
  LED led_128 (.in(instr_display_1_iori));
  LED led_129 (.in(instr_display_1_iandi));
  LED led_130 (.in(instr_display_1_islti));
  LED led_131 (.in(instr_display_1_isltiu));
  LED led_132 (.in(instr_display_1_iaddi));
  LED led_133 (.in(instr_display_1_icsraddr11));
  LED led_134 (.in(instr_display_1_icsraddr9));
  LED led_135 (.in(instr_display_1_icsraddr8));
  LED led_136 (.in(instr_display_1_icsraddr7));
  LED led_137 (.in(instr_display_1_icsraddr10));
  RegFile regfile_1 (
    .Rs1(ID_Rs1), .Rs2(ID_Rs2), .Ws(WB_reg), .Rd1(regfile_1_rd1), .Rd2(regfile_1_rd2), .Clock(CPU_Clock),
    .Reset(CPU_Reset), .Data(WB_data), .We(WB_we), .Disp_R0(regfile_1_disp_r0), .Disp_R1(regfile_1_disp_r1),
    .Disp_R2(regfile_1_disp_r2), .Disp_R3(regfile_1_disp_r3), .Disp_R4(regfile_1_disp_r4),
    .Disp_R5(regfile_1_disp_r5), .Disp_R6(regfile_1_disp_r6), .Disp_R7(regfile_1_disp_r7),
    .Disp_R8(regfile_1_disp_r8), .Disp_R9(regfile_1_disp_r9), .Disp_R10(regfile_1_disp_r10),
    .Disp_R11(regfile_1_disp_r11), .Disp_R12(regfile_1_disp_r12), .Disp_R13(regfile_1_disp_r13),
    .Disp_R14(regfile_1_disp_r14), .Disp_R15(regfile_1_disp_r15), .Disp_R16(regfile_1_disp_r16),
    .Disp_R17(regfile_1_disp_r17), .Disp_R18(regfile_1_disp_r18), .Disp_R19(regfile_1_disp_r19),
    .Disp_R20(regfile_1_disp_r20), .Disp_R21(regfile_1_disp_r21), .Disp_R22(regfile_1_disp_r22),
    .Disp_R23(regfile_1_disp_r23), .Disp_R24(regfile_1_disp_r24), .Disp_R25(regfile_1_disp_r25),
    .Disp_R26(regfile_1_disp_r26), .Disp_R27(regfile_1_disp_r27), .Disp_R28(regfile_1_disp_r28),
    .Disp_R29(regfile_1_disp_r29), .Disp_R30(regfile_1_disp_r30), .Disp_R31(regfile_1_disp_r31));
  Imm_Decoder imm_decoder_1 (.Ctrl(instr_decoder_1_imm_ctrl), .Inst(pipe_if_id_1_instr_out), .Imm(imm_decoder_1_imm));
  // FowardUnit Forwarding_Unit: pin names not known; wires that end beside it: ID_stall, ID_Rs1, ID_Rs2, A_mux, B_mux, Exe_rd, Exe_we, Exe_MemRd, Mem_rd, Mem_we
  LED led_138 (.in(instr_display_1_opmisc_mem));
  LED led_139 (.in(instr_display_1_opamo));
  LED led_140 (.in(instr_display_1_opnmadd));
  LED led_141 (.in(instr_display_1_opjal));
  LED led_142 (.in(instr_display_1_isll));
  LED led_143 (.in(instr_display_1_isrl));
  LED led_144 (.in(instr_display_1_isra));
  LED led_145 (.in(instr_display_1_ixor));
  LED led_146 (.in(instr_display_1_ior));
  LED led_147 (.in(instr_display_1_iand));
  LED led_148 (.in(instr_display_1_islt));
  LED led_149 (.in(instr_display_1_isltu));
  LED led_150 (.in(instr_display_1_iadd));
  LED led_151 (.in(instr_display_1_isub));
  LED led_152 (.in(instr_display_1_icsraddr6));
  LED led_153 (.in(instr_display_1_icsraddr5));
  LED led_154 (.in(instr_display_1_icsraddr4));
  LED led_155 (.in(instr_display_1_icsraddr3));
  LED led_156 (.in(instr_display_1_opop_imm));
  LED led_157 (.in(instr_display_1_opop));
  LED led_158 (.in(instr_display_1_opop_fp));
  LED led_159 (.in(instr_display_1_opsystem));
  LED led_160 (.in(instr_display_1_ifence));
  LED led_161 (.in(instr_display_1_ifence_tso));
  LED led_162 (.in(instr_display_1_iecall));
  LED led_163 (.in(instr_display_1_iebreak));
  LED led_164 (.in(instr_display_1_inop));
  LED led_165 (.in(instr_display_1_icsraddr2));
  LED led_166 (.in(instr_display_1_icsraddr1));
  LED led_167 (.in(instr_display_1_icsraddr0));
  LED led_168 (.in(instr_display_1_opauipc));
  LED led_169 (.in(instr_display_1_oplui));
  LED led_170 (.in(instr_display_1_opres0));
  LED led_171 (.in(instr_display_1_opres2));
  // Probe on regfile_1_disp_r0
  // Probe on regfile_1_disp_r1
  // Probe on regfile_1_disp_r2
  // Probe on regfile_1_disp_r3
  // Probe on regfile_1_disp_r4
  // Probe on regfile_1_disp_r5
  // Probe on regfile_1_disp_r6
  // Probe on regfile_1_disp_r7
  // Probe on regfile_1_disp_r8
  // Probe on regfile_1_disp_r9
  // Probe on regfile_1_disp_r10
  // Probe on regfile_1_disp_r11
  // Probe on regfile_1_disp_r12
  // Probe on regfile_1_disp_r13
  // Probe on regfile_1_disp_r14
  // Probe on regfile_1_disp_r15
  LED led_172 (.in(instr_display_1_opop_imm_32));
  LED led_173 (.in(instr_display_1_opop_32));
  LED led_174 (.in(instr_display_1_opcust2));
  LED led_175 (.in(instr_display_1_opcust3));
  not not_5 (not_5_out, ID_stall);
  // Probe on regfile_1_disp_r16
  // Probe on regfile_1_disp_r17
  // Probe on regfile_1_disp_r18
  // Probe on regfile_1_disp_r19
  // Probe on regfile_1_disp_r20
  // Probe on regfile_1_disp_r21
  // Probe on regfile_1_disp_r22
  // Probe on regfile_1_disp_r23
  // Probe on regfile_1_disp_r24
  // Probe on regfile_1_disp_r25
  // Probe on regfile_1_disp_r26
  // Probe on regfile_1_disp_r27
  // Probe on regfile_1_disp_r28
  // Probe on regfile_1_disp_r29
  // Probe on regfile_1_disp_r30
  // Probe on regfile_1_disp_r31
  LED MemRead_in_EXE (.in(not_5_out));
  LED Stage__EXE (.in(A_mux[0]));
  LED Stage__MEM (.in(A_mux[1]));
  LED Stage__EXE_2 (.in(B_mux[0]));
  LED Stage__MEM_2 (.in(B_mux[1]));
  LED led_176 (.in(instr_display_1_op48bit1));
  LED led_177 (.in(instr_display_1_op64bit));
  LED led_178 (.in(instr_display_1_op48bit2));
  LED led_179 (.in(instr_display_1_op80bit));
  Jump_Unit jump_unit_1 (
    .J_addr(J_addr), .J_ctrl(instr_decoder_1_j_ctrl), .Imm(imm_decoder_1_imm), .Rs1(multiplexer_3_out),
    .PC(pipe_if_id_1_pc_out));
  Multiplexer #(.Selector_Bits(2), .Bits(32)) multiplexer_3 (
    .sel(A_mux), .in_0(regfile_1_rd1), .in_1(Exe_data), .in_2(Mem_data), .in_3({32{1'b0}}),
    .out(multiplexer_3_out));
  Multiplexer #(.Selector_Bits(2), .Bits(32)) multiplexer_4 (
    .sel(B_mux), .in_0(regfile_1_rd2), .in_1(Exe_data), .in_2(Mem_data), .in_3({32{1'b0}}),
    .out(multiplexer_4_out));
  Multiplexer #(.Selector_Bits(2), .Bits(32)) multiplexer_5 (
    .sel({Jump, instr_decoder_1_a_mux[0]}), .in_0(multiplexer_3_out), .in_1(pipe_if_id_1_pc_out),
    .in_2(pipe_if_id_1_pc_nextout), .in_3({32{1'b0}}), .out(multiplexer_5_out));
  Multiplexer #(.Bits(32)) multiplexer_6 (
    .sel(instr_decoder_1_b_mux), .in_0(multiplexer_4_out), .in_1(imm_decoder_1_imm), .out(multiplexer_6_out));
  // PipeReg_Branch pipereg_branch_1: pin names not known; wires that end beside it: instr_decoder_1_branch, instr_decoder_1_br_ctrl, Branch, pipereg_branch_1_p4
  // PipeReg_EXE pipereg_exe_1: pin names not known; wires that end beside it: instr_decoder_1_alu_ctrl, pipereg_exe_1_p2
  // PipeReg_MEM pipereg_mem_1: pin names not known; wires that end beside it: instr_decoder_1_mem_mux, instr_decoder_1_mem_sz, instr_decoder_1_mem_rd, instr_decoder_1_mem_wr, pipereg_mem_1_p5, pipereg_mem_1_p6, Exe_MemRd, pipereg_mem_1_p8
  // PipeReg_WB pipereg_wb_1: pin names not known; wires that end beside it: instr_decoder_1_wb_we, instr_decoder_1_wb_reg, Exe_we, Exe_rd
  // Pipe_ID_EXE pipe_id_exe_1: pin names not known; wires that end beside it: pipe_if_id_1_pc_out, pipe_if_id_1_pc_nextout, multiplexer_4_out, multiplexer_5_out, multiplexer_6_out, pipe_id_exe_1_p6, pipe_id_exe_1_p7, pipe_id_exe_1_p8, pipe_id_exe_1_p9, pipe_id_exe_1_p10, pipe_id_exe_1_p11, pipe_id_exe_1_p12, pipe_id_exe_1_p13, pipe_id_exe_1_p14
  PipeCtrl pipectrl_3 (
    .Valid__prev(pipectrl_2_valid__this), .Ready__prev(pipectrl_3_ready__prev),
    .Valid__this(pipectrl_3_valid__this), .Ready__next(pipectrl_4_ready__prev),
    .Done__this(dipswitch_34_out), ._1cc(pipectrl_3__1cc), .Clock(CPU_Clock), .Reset(CPU_Reset),
    .LED_Valid(pipectrl_3_led_valid), .LED_Busy(pipectrl_3_led_busy), .LED_Waiting(pipectrl_3_led_waiting),
    .LED_Empty(pipectrl_3_led_empty));  // open: Flush, REG_Clear, REG_Clock, REG_OE
  LED Valid_3 (.in(pipectrl_3_led_valid));
  LED Busy_3 (.in(pipectrl_3_led_busy));
  LED Wait_3 (.in(pipectrl_3_led_waiting));
  // Probe on pipe_id_exe_1_p6
  // Probe on pipe_id_exe_1_p7
  // Probe on pipe_id_exe_1_p8
  // Probe on pipe_id_exe_1_p9
  // Probe on pipe_id_exe_1_p10
  // Probe on nothing
  LED led_180 (.in(pipectrl_3__1cc));
  LED Empty_3 (.in(pipectrl_3_led_empty));
  PullDown #(.Bits(4)) pulldown_2 (.out(pulldown_2_out));
  DipSwitch #(.dipDefault("true")) dipswitch_34 (.out(dipswitch_34_out));
  Multiplexer #(.Bits(4)) multiplexer_7 (
    .sel(pipereg_exe_1_p2[4]), .in_0(pipereg_exe_1_p2[3:0]), .in_1(pulldown_2_out), .out(multiplexer_7_out));
  ALU alu_1 (.ALU_ctrl(multiplexer_7_out), .A(pipe_id_exe_1_p14), .B(undriven), .Y(Exe_data), .Z(alu_1_z));
  Branch_Unit branch_unit_1 (
    .Imm(undriven_2), .PC(pipe_id_exe_1_p11), .Branch(Branch), .BR_ctrl(pipereg_branch_1_p4),
    .ALU_zero(alu_1_z), .ALU_SLT(Exe_data[0]), .BR_addr(BR_addr), .BR_taken(BR_taken));
  // PipeReg_MEM pipereg_mem_2: pin names not known; wires that end beside it: pipereg_mem_1_p5, pipereg_mem_1_p6, Exe_MemRd, pipereg_mem_1_p8, pipereg_mem_2_p5, pipereg_mem_2_p6, pipereg_mem_2_p7, pipereg_mem_2_p8
  // PipeReg_WB pipereg_wb_2: pin names not known; wires that end beside it: Exe_we, Exe_rd, Mem_we, Mem_rd
  // Pipe_EXE_MEM pipe_exe_mem_1: pin names not known; wires that end beside it: pipe_id_exe_1_p11, pipe_id_exe_1_p12, pipe_id_exe_1_p13, Exe_data, pipe_exe_mem_1_p5, pipe_exe_mem_1_p6, pipe_exe_mem_1_p7, pipe_exe_mem_1_p8, pipe_exe_mem_1_p9, pipe_exe_mem_1_p10, pipe_exe_mem_1_p11, pipe_exe_mem_1_p12, pipereg_mem_2_p6
  PipeCtrl pipectrl_4 (
    .Valid__prev(pipectrl_3_valid__this), .Ready__prev(pipectrl_4_ready__prev),
    .Valid__this(pipectrl_4_valid__this), .Ready__next(pipectrl_5_ready__prev),
    .Done__this(dipswitch_35_out), ._1cc(pipectrl_4__1cc), .Clock(CPU_Clock), .Reset(CPU_Reset),
    .LED_Valid(pipectrl_4_led_valid), .LED_Busy(pipectrl_4_led_busy), .LED_Waiting(pipectrl_4_led_waiting),
    .LED_Empty(pipectrl_4_led_empty));  // open: Flush, REG_Clear, REG_Clock, REG_OE
  LED Valid_4 (.in(pipectrl_4_led_valid));
  LED Busy_4 (.in(pipectrl_4_led_busy));
  LED Wait_4 (.in(pipectrl_4_led_waiting));
  // Probe on pipe_exe_mem_1_p5
  // Probe on pipe_exe_mem_1_p6
  // Probe on pipe_exe_mem_1_p7
  // Probe on pipe_exe_mem_1_p8
  LED led_181 (.in(pipectrl_4__1cc));
  LED Empty_4 (.in(pipectrl_4_led_empty));
  DipSwitch #(.dipDefault("true")) dipswitch_35 (.out(dipswitch_35_out));
  Delay #(.delayTime(2)) delay_1 (.in(pipereg_mem_2_p8), .out(delay_1_out));
  RAMDualPort #(.AddrBits(14), .Bits(32)) Data (
    .A(pipe_exe_mem_1_p12[13:0]), .Din(pipe_exe_mem_1_p11), .str(pipereg_mem_2_p8), .C(delay_1_out),
    .ld(pipereg_mem_2_p7), .D(Data_d));
  Mem_Ext mem_ext_1 (.size(pipereg_mem_2_p6), .in(Data_d), .out(mem_ext_1_out));
  // Probe on counter_1_out
  // Probe on counter_3_out
  // Probe on counter_2_out
  // Probe on counter_4_out
  Multiplexer #(.Selector_Bits(2), .Bits(32)) multiplexer_8 (
    .sel(pipereg_mem_2_p5), .in_0(pipe_exe_mem_1_p12), .in_1(mem_ext_1_out), .in_2(pipe_exe_mem_1_p10),
    .in_3({32{1'b0}}), .out(Mem_data));
  Counter #(.Bits(32)) counter_1 (
    .en(counter_3_ovf), .C(CPU_Clock), .clr(not_6_out), .out(counter_1_out));  // open: ovf
  Counter #(.Bits(32)) counter_2 (.en(counter_4_ovf), .C(or_3_out), .clr(not_6_out), .out(counter_2_out));  // open: ovf
  // PipeReg_WB pipereg_wb_3: pin names not known; wires that end beside it: Mem_we, Mem_rd, WB_we, WB_reg
  // Pipe_MEM_WB pipe_mem_wb_1: pin names not known; wires that end beside it: pipe_exe_mem_1_p9, pipe_exe_mem_1_p10, Mem_data, pipe_mem_wb_1_p4, pipe_mem_wb_1_p5, pipe_mem_wb_1_p6, WB_data
  PipeCtrl pipectrl_5 (
    .Valid__prev(pipectrl_4_valid__this), .Ready__prev(pipectrl_5_ready__prev),
    .Valid__this(pipectrl_5_valid__this), ._1cc(pipectrl_5__1cc), .Clock(CPU_Clock), .Reset(CPU_Reset),
    .LED_Valid(pipectrl_5_led_valid), .LED_Busy(pipectrl_5_led_busy), .LED_Waiting(pipectrl_5_led_waiting),
    .LED_Empty(pipectrl_5_led_empty));  // open: Ready__next, Done__this, Flush, REG_Clear, REG_Clock, REG_OE
  LED Valid_5 (.in(pipectrl_5_led_valid));
  LED Busy_5 (.in(pipectrl_5_led_busy));
  LED Wait_5 (.in(pipectrl_5_led_waiting));
  Counter #(.Bits(32)) counter_3 (.en(1'b1), .C(CPU_Clock), .clr(not_6_out), .out(counter_3_out), .ovf(counter_3_ovf));
  Counter #(.Bits(32)) counter_4 (
    .en(pipectrl_5_valid__this), .C(or_3_out), .clr(not_6_out), .out(counter_4_out), .ovf(counter_4_ovf));
  // Probe on pipe_mem_wb_1_p4
  // Probe on pipe_mem_wb_1_p5
  // Probe on pipe_mem_wb_1_p6
  LED Empty_5 (.in(pipectrl_5_led_empty));
  not not_6 (not_6_out, CPU_Reset);
  and and_3 (and_3_out, CPU_Clock, not_6_out);
  or or_3 (or_3_out, pipectrl_5__1cc, and_3_out);

  // Notes on the sheet:
  //   Clk_Slow: Hz: 2
  //   Clk_Fast: Hz: 2147483647
  //   func7
  //   TODO:
  //   - Rework Clock Unit
  //   - Memory interface
  //   - Instruction cache
  //   - Check Addr of Instr before MemWrite
  //   Later:
  //   - User/Superviser/Machine mode
  //   - Interupts
  //   - Exceptions
  //   - CSR's
  //   - Memory Protection
  //   - Memory Management
  //   - RVC Decoding
  //   Rework:
  //   - Clear pulse in PipeCtrl
  //   RVC-PC-Increment (for later use)
  //   rs2
  //   rs1
  //   func3
  //   rd
  //   opcode
  //   11
  //   Imm
  //   Jump/Branch-Unit
  //   Reset-Vector
  //   Clock / Reset / Halt
  //   func7 / func12
  //   Instruction-Fetch
  //   contents of Progr (hex, n*v repeats v):
  //   64*0,1000593,613
  //   Branch-Unit
  //   Instruction-Decode / Register-Fetch
  //   Forwarding-Unit
  //   Stall
  //   Rs1 forward from:
  //   Rs2 forward from:
  //   Jump-Unit
  //   A_mux
  //   00: Rs1
  //   01: PC
  //   10: PC_next
  //   B_mux
  //   0: Rs2
  //   1: Imm
  //   Execute
  //   MUL/DIV-mode
  //   Memory
  //   Mem_sz
  //   Basic Cycle Counter
  //   Basic Instr. Counter
  //   Mem_mux
  //   00: ALU
  //   01: Mem
  //   10: PC_next
  //   Write-Back
endmodule
