// Digital circuit ClockCtrl.dig as structural Verilog
module ClockCtrl (
  input  Sel_Man,
  input  Clk_Man,
  input  Sel_Slow,
  input  Clk_Slow,
  input  Sel_Fast,
  input  Clk_Fast,
  input  Halt,
  input  Reset,
  output Clk_Out
);

  wire _74193_1_pin1, _74193_1_pin9, _74193_1_pin10, _74193_1_pin11, _74193_1_pin15, and_1_out, and_2_out,
       and_3_out, and_4_out, and_8_out, and_9_out, and_10_out, d_ff_1_q, nand_1_out, nand_2_out, nand_3_out,
       nand_4_out;
  wire [1:0] d_ff_2_q;

  _7400 _7400_1 (
    .pin1(1'b0), .pin2(1'b0), .pin4(1'b0), .pin5(1'b0), .pin7(1'b0), .pin9(1'b0), .pin10(1'b0), .pin12(1'b0),
    .pin13(1'b0), .pin14(1'b1));  // open: pin3, pin6, pin8, pin11
  and and_1 (and_1_out, Halt, Clk_Slow);
  and and_2 (and_2_out, Clk_Man, Halt);
  and and_3 (and_3_out, Reset, Halt);
  and and_4 (and_4_out, and_3_out, Sel_Man);
  _74193 _74193_1 (
    .pin1(_74193_1_pin1), .pin4(Clk_Fast), .pin5(1'b1), .pin8(1'b0), .pin9(_74193_1_pin9),
    .pin10(_74193_1_pin10), .pin11(_74193_1_pin11), .pin13(_74193_1_pin11), .pin14(1'b0),
    .pin15(_74193_1_pin15), .pin16(1'b1));  // open: pin2, pin3, pin6, pin7, pin12
  _7408 _7408_1 (
    .pin1(1'b0), .pin2(1'b0), .pin4(1'b0), .pin5(1'b0), .pin7(1'b0), .pin9(1'b0), .pin10(1'b0), .pin12(1'b0),
    .pin13(1'b0), .pin14(1'b1));  // open: pin3, pin6, pin8, pin11
  _7408 _7408_2 (
    .pin1(1'b0), .pin2(1'b0), .pin4(1'b0), .pin5(1'b0), .pin7(1'b0), .pin8(1'b0), .pin10(1'b0), .pin11(1'b0),
    .pin12(1'b0), .pin13(1'b0), .pin14(1'b0));  // open: pin3, pin6, pin9
  // And and_5 has open pins: In_1=1'b0, In_2=1'b0, out=open
  // And and_6 has open pins: In_1=1'b0, In_2=1'b0, out=open
  // And and_7 has open pins: In_1=1'b0, In_2=1'b0, out=open
  nand nand_1 (nand_1_out, and_3_out, d_ff_1_q);
  nand nand_2 (nand_2_out, and_10_out, and_9_out);
  nand nand_3 (nand_3_out, and_8_out, and_10_out);
  nand nand_4 (nand_4_out, and_8_out, and_9_out);
  D_FF d_ff_1 (.D(nand_1_out), .C(_74193_1_pin11), .Q(d_ff_1_q));  // open: nQ
  and and_8 (and_8_out, nand_2_out, and_4_out);
  and and_9 (and_9_out, nand_3_out, Sel_Slow);
  and and_10 (and_10_out, nand_4_out, Sel_Fast);
  DipSwitch dipswitch_1 (.out(_74193_1_pin1));
  DipSwitch dipswitch_2 (.out(_74193_1_pin10));
  DipSwitch dipswitch_3 (.out(_74193_1_pin9));
  _74153 _74153_1 (
    .pin1(1'b0), .pin2(1'b0), .pin3(1'b0), .pin4(1'b0), .pin5(1'b0), .pin6(1'b0), .pin8(1'b0), .pin9(1'b0),
    .pin10(1'b0), .pin11(1'b0), .pin12(1'b0), .pin13(1'b0), .pin14(1'b0), .pin15(1'b0), .pin16(1'b0));  // open: pin7
  Multiplexer #(.Selector_Bits(2)) multiplexer_1 (
    .sel(2'b00), .in_0(1'b0), .in_1(1'b0), .in_2(1'b0), .in_3(1'b0));  // open: out
  DipSwitch #(.dipDefault("true")) dipswitch_4 (.out(_74193_1_pin15));
  D_FF d_ff_2 (.D(and_8_out), .C(d_ff_1_q), .Q(d_ff_2_q[0]));  // open: nQ
  D_FF d_ff_3 (.D(and_9_out), .C(d_ff_1_q), .Q(d_ff_2_q[1]));  // open: nQ
  Multiplexer #(.Selector_Bits(2)) multiplexer_2 (
    .sel(d_ff_2_q), .in_0(1'b0), .in_1(and_1_out), .in_2(and_2_out), .in_3(d_ff_1_q), .out(Clk_Out));
  _74574 _74574_1 (
    .pin1(1'b0), .pin2(1'b0), .pin3(1'b0), .pin4(1'b0), .pin5(1'b0), .pin6(1'b0), .pin7(1'b0), .pin8(1'b0),
    .pin9(1'b0), .pin10(1'b0), .pin11(1'b0), .pin20(1'b1));  // open: pin12, pin13, pin14, pin15, pin16, pin17, pin18, pin19
  D_FF d_ff_4 (.D(1'b0), .C(1'b0));  // open: Q, nQ
  D_FF d_ff_5 (.D(1'b0), .C(1'b0));  // open: Q, nQ
  D_FF d_ff_6 (.D(1'b0), .C(1'b0));  // open: Q, nQ
  D_FF d_ff_7 (.D(1'b0), .C(1'b0));  // open: Q, nQ
  D_FF d_ff_8 (.D(1'b0), .C(1'b0));  // open: Q, nQ

  // Notes on the sheet:
  //   Sel_Man: default 1
  //   Sel_Slow: default 1
  //   Sel_Fast: default 1
  //   Clk_Fast: Hz: 10
  //   Halt: default 1
endmodule
