// Digital circuit Instr.Decoder.Logic.dig as structural Verilog
module Instr_Decoder_Logic (
  input  sel,
  input  [4:0] opcode,
  input  [2:0] func3,
  input  [6:0] func7,
  input  [4:0] rd,
  input  [4:0] rs1,
  input  [4:0] rs2,
  output B_mux,
  output [2:0] Imm_ctrl,
  output rs1_en,
  output rs2_en,
  output rd_en,
  output Mem_rd,
  output Mem_wr,
  output [1:0] Mem_mux,
  output [4:0] ALU_ctrl,
  output Valid_instr,
  output A_mux,
  output J_JAL,
  output J_JALR,
  output Branch
);

  wire [6:4] driver_3_out;
  wire [7:0] pulldown_1_out, pulldown_2_out, pulldown_3_out;

  PullDown #(.Bits(8)) pulldown_1 (.out(pulldown_1_out));
  PullDown #(.Bits(8)) pulldown_2 (.out(pulldown_2_out));
  PullDown #(.Bits(8)) pulldown_3 (.out(pulldown_3_out));
  assign {rd_en, rs2_en, rs1_en, Imm_ctrl, B_mux, A_mux} = sel ? pulldown_1_out : 8'bz;  // Driver driver_1
  assign {ALU_ctrl[3:0], Mem_wr, Mem_rd, Mem_mux} = sel ? pulldown_2_out : 8'bz;  // Driver driver_2
  assign {Valid_instr, driver_3_out, Branch, J_JALR, J_JAL, ALU_ctrl[4]} = sel ? pulldown_3_out : 8'bz;  // Driver driver_3

  // Notes on the sheet:
  //   Instruction.Decoder with discrete logic:
  //   TODO...
  //   TODO...
  //   TODO...
  //   TODO...
  //   TODO...
endmodule
