// Digital circuit Instr.Decoder.RVC.dig as structural Verilog
module Instr_Decoder_RVC (
  input  [31:0] in,
  input  enable,
  output [31:0] out,
  output illegal_instr,
  output RVC_instr
);

  wire nand_1_out;

  nand nand_1 (nand_1_out, in[0], in[1]);
  and and_1 (RVC_instr, nand_1_out, enable);
  and and_2 (illegal_instr, enable, 1'b0);

  assign out = in;

  // Notes on the sheet:
  //   enable: default 1
endmodule
