// Digital circuit Instr.Decoder.uCRom.dig as structural Verilog
module Instr_Decoder_uCRom (
  input  sel,
  input  [4:0] opcode,
  input  [2:0] func3,
  input  [6:0] func7,
  input  [4:0] rd,
  input  [4:0] rs1,
  input  [4:0] rs2,
  output B_mux,
  output [2:0] Imm_ctrl,
  output rs1_en,
  output rs2_en,
  output rd_en,
  output Mem_rd,
  output Mem_wr,
  output [1:0] Mem_mux,
  output [4:0] ALU_ctrl,
  output Valid_instr,
  output A_mux,
  output J_JAL,
  output J_JALR,
  output Branch
);

  wire funct7b1_4_nzero, rd_nzero, rs1_nzero, rs2b1_4_nzero;
  wire [6:4] driver_3_out;
  wire [7:0] \µCRom0_d , \µCRom1_d , \µCRom2_d ;

  DiodeForward diodeforward_1 (.in(func7[1]), .out(funct7b1_4_nzero));
  DiodeForward diodeforward_2 (.in(func7[2]), .out(funct7b1_4_nzero));
  PullDown pulldown_1 (.out(funct7b1_4_nzero));
  DiodeForward diodeforward_3 (.in(func7[3]), .out(funct7b1_4_nzero));
  DiodeForward diodeforward_4 (.in(func7[4]), .out(funct7b1_4_nzero));
  DiodeForward diodeforward_5 (.in(rd[0]), .out(rd_nzero));
  DiodeForward diodeforward_6 (.in(rd[1]), .out(rd_nzero));
  PullDown pulldown_2 (.out(rd_nzero));
  DiodeForward diodeforward_7 (.in(rd[2]), .out(rd_nzero));
  DiodeForward diodeforward_8 (.in(rd[3]), .out(rd_nzero));
  DiodeForward diodeforward_9 (.in(rd[4]), .out(rd_nzero));
  DiodeForward diodeforward_10 (.in(rs1[0]), .out(rs1_nzero));
  DiodeForward diodeforward_11 (.in(rs1[1]), .out(rs1_nzero));
  PullDown pulldown_3 (.out(rs1_nzero));
  DiodeForward diodeforward_12 (.in(rs1[2]), .out(rs1_nzero));
  DiodeForward diodeforward_13 (.in(rs1[3]), .out(rs1_nzero));
  DiodeForward diodeforward_14 (.in(rs1[4]), .out(rs1_nzero));
  DiodeForward diodeforward_15 (.in(rs2[1]), .out(rs2b1_4_nzero));
  DiodeForward diodeforward_16 (.in(rs2[2]), .out(rs2b1_4_nzero));
  PullDown pulldown_4 (.out(rs2b1_4_nzero));
  DiodeForward diodeforward_17 (.in(rs2[3]), .out(rs2b1_4_nzero));
  DiodeForward diodeforward_18 (.in(rs2[4]), .out(rs2b1_4_nzero));
  ROM #(.AddrBits(16), .Bits(8)) \u_µCRom0  (
    .A({rs2b1_4_nzero, rs2[0], rs1_nzero, rd_nzero, func7[6:5], funct7b1_4_nzero, func7[0], func3, opcode}),
    .sel(sel), .D(\µCRom0_d ));
  ROM #(.AddrBits(16), .Bits(8)) \u_µCRom1  (
    .A({rs2b1_4_nzero, rs2[0], rs1_nzero, rd_nzero, func7[6:5], funct7b1_4_nzero, func7[0], func3, opcode}),
    .sel(sel), .D(\µCRom1_d ));
  ROM #(.AddrBits(16), .Bits(8)) \u_µCRom2  (
    .A({rs2b1_4_nzero, rs2[0], rs1_nzero, rd_nzero, func7[6:5], funct7b1_4_nzero, func7[0], func3, opcode}),
    .sel(sel), .D(\µCRom2_d ));
  assign {rd_en, rs2_en, rs1_en, Imm_ctrl, B_mux, A_mux} = sel ? \µCRom0_d  : 8'bz;  // Driver driver_1
  assign {ALU_ctrl[3:0], Mem_wr, Mem_rd, Mem_mux} = sel ? \µCRom1_d  : 8'bz;  // Driver driver_2
  assign {Valid_instr, driver_3_out, Branch, J_JALR, J_JAL, ALU_ctrl[4]} = sel ? \µCRom2_d  : 8'bz;  // Driver driver_3

  // Other names for the same wires on the sheet: µCRom_Addr[15:0] = {rs2b1_4_nzero, rs2[0], rs1_nzero, rd_nzero, func7[6:5], funct7b1_4_nzero, func7[0], func3, opcode};
  //   funct7b0 = func7[0]; funct7b5 = func7[5]; funct7b6 = func7[6]; rs2b0 = rs2[0]

  // Notes on the sheet:
  //   Instruction.Decoder with MicrocodeROM's:
  //   µCRom0 loads ucode-rom0.bin
  //   µCRom1 loads ucode-rom1.bin
  //   µCRom2 loads ucode-rom2.bin
endmodule
