// Digital circuit Instr.Display.dig as structural Verilog
module Instr_Display (
);

  wire demultiplexer_1_out_0, demultiplexer_1_out_1, demultiplexer_1_out_2, demultiplexer_1_out_3,
       demultiplexer_2_out_0, demultiplexer_2_out_1, demultiplexer_2_out_2, demultiplexer_2_out_3,
       demultiplexer_2_out_4, demultiplexer_2_out_5, demultiplexer_2_out_6, demultiplexer_2_out_7,
       demultiplexer_3_out_0, demultiplexer_3_out_1, demultiplexer_3_out_2, demultiplexer_3_out_3,
       demultiplexer_3_out_4, demultiplexer_3_out_5, demultiplexer_3_out_6, demultiplexer_3_out_7,
       demultiplexer_4_out_0, demultiplexer_4_out_1, demultiplexer_4_out_2, demultiplexer_4_out_3,
       demultiplexer_4_out_4, demultiplexer_4_out_5, demultiplexer_4_out_6, demultiplexer_4_out_7,
       demultiplexer_5_out_0, demultiplexer_5_out_1, demultiplexer_5_out_2, demultiplexer_5_out_3,
       demultiplexer_5_out_4, demultiplexer_5_out_5, demultiplexer_5_out_6, demultiplexer_5_out_7,
       nand_1_out, not_1_out;
  wire [2:0] func3;
  wire [6:0] func7;
  wire [24:0] inst;

  nand nand_1 (nand_1_out, inst[0], inst[1]);
  not not_1 (not_1_out, nand_1_out);
  Demultiplexer #(.Selector_Bits(2)) demultiplexer_1 (
    .sel(inst[6:5]), .in(not_1_out), .out_0(demultiplexer_1_out_0), .out_1(demultiplexer_1_out_1),
    .out_2(demultiplexer_1_out_2), .out_3(demultiplexer_1_out_3));
  DipSwitch dipswitch_1 (.out(func7[6]));
  LED RVC_Instruction (.in(nand_1_out));
  Demultiplexer #(.Selector_Bits(3)) demultiplexer_2 (
    .sel(inst[4:2]), .in(demultiplexer_1_out_0), .out_0(demultiplexer_2_out_0),
    .out_1(demultiplexer_2_out_1), .out_2(demultiplexer_2_out_2), .out_3(demultiplexer_2_out_3),
    .out_4(demultiplexer_2_out_4), .out_5(demultiplexer_2_out_5), .out_6(demultiplexer_2_out_6),
    .out_7(demultiplexer_2_out_7));
  LED LOAD (.in(demultiplexer_2_out_0));
  Demultiplexer #(.Selector_Bits(3)) demultiplexer_3 (
    .sel(inst[4:2]), .in(demultiplexer_1_out_1), .out_0(demultiplexer_3_out_0),
    .out_1(demultiplexer_3_out_1), .out_2(demultiplexer_3_out_2), .out_3(demultiplexer_3_out_3),
    .out_4(demultiplexer_3_out_4), .out_5(demultiplexer_3_out_5), .out_6(demultiplexer_3_out_6),
    .out_7(demultiplexer_3_out_7));
  LED STORE (.in(demultiplexer_3_out_0));
  Demultiplexer #(.Selector_Bits(3)) demultiplexer_4 (
    .sel(inst[4:2]), .in(demultiplexer_1_out_2), .out_0(demultiplexer_4_out_0),
    .out_1(demultiplexer_4_out_1), .out_2(demultiplexer_4_out_2), .out_3(demultiplexer_4_out_3),
    .out_4(demultiplexer_4_out_4), .out_5(demultiplexer_4_out_5), .out_6(demultiplexer_4_out_6),
    .out_7(demultiplexer_4_out_7));
  LED MADD (.in(demultiplexer_4_out_0));
  Demultiplexer #(.Selector_Bits(3)) demultiplexer_5 (
    .sel(inst[4:2]), .in(demultiplexer_1_out_3), .out_0(demultiplexer_5_out_0),
    .out_1(demultiplexer_5_out_1), .out_2(demultiplexer_5_out_2), .out_3(demultiplexer_5_out_3),
    .out_4(demultiplexer_5_out_4), .out_5(demultiplexer_5_out_5), .out_6(demultiplexer_5_out_6),
    .out_7(demultiplexer_5_out_7));
  LED BRANCH (.in(demultiplexer_5_out_0));
  DipSwitch dipswitch_2 (.out(func7[5]));
  DipSwitch dipswitch_3 (.out(func7[4]));
  DipSwitch dipswitch_4 (.out(func7[3]));
  DipSwitch dipswitch_5 (.out(func7[2]));
  DipSwitch dipswitch_6 (.out(func7[1]));
  DipSwitch dipswitch_7 (.out(func7[0]));
  DipSwitch dipswitch_8 (.out(inst[24]));
  DipSwitch dipswitch_9 (.out(inst[23]));
  LED LOAD_FP (.in(demultiplexer_2_out_1));
  LED STORE_FP (.in(demultiplexer_3_out_1));
  LED MSUB (.in(demultiplexer_4_out_1));
  LED JALR (.in(demultiplexer_5_out_1));
  DipSwitch dipswitch_10 (.out(inst[22]));
  DipSwitch dipswitch_11 (.out(inst[21]));
  DipSwitch dipswitch_12 (.out(inst[20]));
  DipSwitch dipswitch_13 (.out(inst[19]));
  DipSwitch dipswitch_14 (.out(inst[18]));
  DipSwitch dipswitch_15 (.out(inst[17]));
  DipSwitch dipswitch_16 (.out(inst[16]));
  DipSwitch dipswitch_17 (.out(inst[15]));
  LED custom_0 (.in(demultiplexer_2_out_2));
  LED custom_1 (.in(demultiplexer_3_out_2));
  LED NMSUB (.in(demultiplexer_4_out_2));
  LED reserved (.in(demultiplexer_5_out_2));
  DipSwitch dipswitch_18 (.out(func3[2]));
  DipSwitch dipswitch_19 (.out(func3[1]));
  DipSwitch dipswitch_20 (.out(func3[0]));
  DipSwitch dipswitch_21 (.out(inst[11]));
  DipSwitch dipswitch_22 (.out(inst[10]));
  DipSwitch dipswitch_23 (.out(inst[9]));
  DipSwitch dipswitch_24 (.out(inst[8]));
  DipSwitch dipswitch_25 (.out(inst[7]));
  LED MISC_MEM (.in(demultiplexer_2_out_3));
  LED AMO (.in(demultiplexer_3_out_3));
  LED NMADD (.in(demultiplexer_4_out_3));
  LED JAL (.in(demultiplexer_5_out_3));
  DipSwitch dipswitch_26 (.out(inst[6]));
  DipSwitch dipswitch_27 (.out(inst[5]));
  DipSwitch dipswitch_28 (.out(inst[4]));
  DipSwitch dipswitch_29 (.out(inst[3]));
  DipSwitch dipswitch_30 (.out(inst[2]));
  DipSwitch #(.dipDefault("true")) dipswitch_31 (.out(inst[1]));
  DipSwitch #(.dipDefault("true")) dipswitch_32 (.out(inst[0]));
  LED OP_IMM (.in(demultiplexer_2_out_4));
  LED OP (.in(demultiplexer_3_out_4));
  LED OP_FP (.in(demultiplexer_4_out_4));
  LED SYSTEM (.in(demultiplexer_5_out_4));
  LED AUIPC (.in(demultiplexer_2_out_5));
  LED LUI (.in(demultiplexer_3_out_5));
  LED reserved_2 (.in(demultiplexer_4_out_5));
  LED reserved_3 (.in(demultiplexer_5_out_5));
  LED OP_IMM_33 (.in(demultiplexer_2_out_6));
  LED OP_33 (.in(demultiplexer_3_out_6));
  LED custom_2_rv129 (.in(demultiplexer_4_out_6));
  LED custom_3_rv129 (.in(demultiplexer_5_out_6));
  LED _48bit (.in(demultiplexer_2_out_7));
  LED _64bit (.in(demultiplexer_3_out_7));
  LED _48bit_2 (.in(demultiplexer_4_out_7));
  LED gt__eq_80b (.in(demultiplexer_5_out_7));
  LED JAL_2 (.in(1'b0));
  LED JALR_2 (.in(1'b0));
  LED BEQ (.in(1'b0));
  LED BNE (.in(1'b0));
  LED BLT (.in(1'b0));
  LED BGE (.in(1'b0));
  LED BLTU (.in(1'b0));
  LED BGEU (.in(1'b0));
  LED LUI_2 (.in(1'b0));
  LED AUIPC_2 (.in(1'b0));
  LED FENCE_I (.in(1'b0));
  LED CSRRW (.in(1'b0));
  LED CSRRS (.in(1'b0));
  LED CSRRC (.in(1'b0));
  LED MUL (.in(1'b0));
  LED MULH (.in(1'b0));
  LED MULHSU (.in(1'b0));
  LED MULHU (.in(1'b0));
  LED LB (.in(1'b0));
  LED LH (.in(1'b0));
  LED LW (.in(1'b0));
  LED LBU (.in(1'b0));
  LED LHU (.in(1'b0));
  LED SB (.in(1'b0));
  LED SH (.in(1'b0));
  LED SW (.in(1'b0));
  LED CSRRWI (.in(1'b0));
  LED CSRRSI (.in(1'b0));
  LED CSRRCI (.in(1'b0));
  LED DIV (.in(1'b0));
  LED DIVU (.in(1'b0));
  LED REM (.in(1'b0));
  LED REMU (.in(1'b0));
  LED SLLI (.in(1'b0));
  LED SRLI (.in(1'b0));
  LED SRAI (.in(1'b0));
  LED XORI (.in(1'b0));
  LED ORI (.in(1'b0));
  LED ANDI (.in(1'b0));
  LED SLTI (.in(1'b0));
  LED SLTIU (.in(1'b0));
  LED ADDI (.in(1'b0));
  LED SLL (.in(1'b0));
  LED SRL (.in(1'b0));
  LED SRA (.in(1'b0));
  LED XOR (.in(1'b0));
  LED OR (.in(1'b0));
  LED AND (.in(1'b0));
  LED SLT (.in(1'b0));
  LED SLTU (.in(1'b0));
  LED ADD (.in(1'b0));
  LED SUB (.in(1'b0));
  LED FENCE (.in(1'b0));
  LED FENCE_TSO (.in(1'b0));
  LED ECALL (.in(1'b0));
  LED EBREAK (.in(1'b0));
  LED NOP (.in(1'b0));

  // Other names for the same wires on the sheet: rd[4:0] = inst[11:7]; opcode[4:0] = inst[6:2]; rvc[1:0] = inst[1:0];
  //   inst (some bits) = {func7, func3}; rs1[4:0] = inst[19:15]; rs2[4:0] = inst[24:20]

  // Notes on the sheet:
  //   Major opcodes
  //   00
  //   01
  //   10
  //   11
  //   func7
  //   000
  //   rs2
  //   001
  //   rs1
  //   func3
  //   010
  //   rd
  //   011
  //   opcode
  //   100
  //   101
  //   110
  //   111
  //   Instruction types
  //   31
  //   30
  //   29
  //   imm[11:0]
  //   imm[11:5]
  //   imm[12,10:5]
  //   imm[31:12]
  //   imm[20,10:1,11,19:12]
  //   Instruction parts
  //   imm
  //   csr
  //   RV32I Base Instructions
  //   Zifencei Standard Extension
  //   Zicsr Standard Extension
  //   RV32M Standard Extension
  //   RV32A Standard Extension
  //   RV32F Standard Extension
  //   RV32D Standard Extension
  //   RV32Q Standard Extension
  //   28
  //   27
  //   26
  //   25
  //   24
  //   23
  //   22
  //   21
  //   20
  //   19
  //   18
  //   17
  //   0
  //   4
  //   uimm
  //   16
  //   15
  //   14
  //   13
  //   12
  //   9
  //   imm[4:0]
  //   imm[4:1,11]
  //   8
  //   7
  //   6
  //   5
  //   2
  //   3
  //   1
  //   R-type
  //   I-type
  //   S-type
  //   B-type
  //   U-type
  //   J-type
  //   rs2/shamt
endmodule
