// Digital circuit MUL_DIV.Unit.dig as structural Verilog
module MUL_DIV_Unit (
  input  Reset,
  input  Clock,
  input  [3:0] A,
  input  [3:0] B,
  input  Reset_2,
  input  Clock_2,
  input  [3:0] A_2,
  input  [3:0] B_2,
  input  Unsigned
);

  wire add_1_c_o, and_1_out, and_2_out, Carry_q, decoder_1_out_0, decoder_1_out_1, decoder_1_out_2,
       decoder_1_out_3, decoder_1_out_4, decoder_1_out_5, decoder_2_out_0, decoder_2_out_1, decoder_2_out_2,
       decoder_2_out_3, decoder_2_out_4, decoder_2_out_5, dipswitch_1_out, Falling_Pulse_nq, Falling_Pulse_q,
       multiplexer_4_out, multiplexer_7_out, multiplexer_8_out, multiplexer_11_out, not_1_out, not_3_out,
       not_4_out, or_1_out, Q_x_2_q, Q_x_q, Rising_Pulse_nq, Rising_Pulse_q, xnor_1_out, xnor_2_out;
  wire [2:0] counter_1_out, counter_2_out;
  wire [3:0] AC_2_q, AC_q, add_1_s, add_2_s, counter_3_out, M_2_q, M_q, multiplexer_2_out, multiplexer_3_out,
       multiplexer_5_out, multiplexer_6_out, multiplexer_9_out, multiplexer_10_out, multiplexer_12_out,
       multiplexer_13_out, not_2_out, not_5_out, Q_2_q, Q_q;
  wire [3:3] multiplexer_1_out;

  Multiplexer multiplexer_1 (.sel(Unsigned), .in_0(add_1_s[3]), .in_1(Carry_q), .out(multiplexer_1_out[3]));
  Counter #(.Bits(3)) counter_1 (.en(not_1_out), .C(Clock_2), .clr(Reset_2), .out(counter_1_out));  // open: ovf
  Multiplexer #(.Bits(4)) multiplexer_2 (
    .sel(decoder_1_out_0), .in_0({multiplexer_1_out[3], add_1_s[3:1]}), .in_1(4'b0000),
    .out(multiplexer_2_out));
  Multiplexer #(.Bits(4)) multiplexer_3 (
    .sel(decoder_1_out_0), .in_0({add_1_s[0], Q_q[3:1]}), .in_1(B_2), .out(multiplexer_3_out));
  Multiplexer multiplexer_4 (.sel(decoder_1_out_0), .in_0(Q_q[0]), .in_1(1'b0), .out(multiplexer_4_out));
  Decoder #(.Selector_Bits(3)) decoder_1 (
    .sel(counter_1_out), .out_0(decoder_1_out_0), .out_1(decoder_1_out_1), .out_2(decoder_1_out_2),
    .out_3(decoder_1_out_3), .out_4(decoder_1_out_4), .out_5(decoder_1_out_5));  // open: out_6, out_7
  // Probe on counter_1_out
  LED Init (.in(decoder_1_out_0));
  LED Step_5 (.in(decoder_1_out_1));
  LED Step_6 (.in(decoder_1_out_2));
  LED Step_7 (.in(decoder_1_out_3));
  LED Step_8 (.in(decoder_1_out_4));
  LED Done (.in(decoder_1_out_5));
  not not_1 (not_1_out, decoder_1_out_5);
  LED led_1 (.in(add_1_c_o));
  LED led_2 (.in(multiplexer_2_out[3]));
  LED led_3 (.in(multiplexer_2_out[2]));
  LED led_4 (.in(multiplexer_2_out[1]));
  LED led_5 (.in(multiplexer_2_out[0]));
  LED led_6 (.in(multiplexer_3_out[3]));
  LED led_7 (.in(multiplexer_3_out[2]));
  LED led_8 (.in(multiplexer_3_out[1]));
  LED led_9 (.in(multiplexer_3_out[0]));
  LED led_10 (.in(multiplexer_4_out));
  Register #(.Bits(4)) M (.D(A_2), .C(Clock_2), .en(not_1_out), .Q(M_q));
  Register Carry (.D(add_1_c_o), .C(Clock_2), .en(not_1_out), .Q(Carry_q));
  Register #(.Bits(4)) AC (.D(multiplexer_2_out), .C(Clock_2), .en(not_1_out), .Q(AC_q));
  Register #(.Bits(4)) Q (.D(multiplexer_3_out), .C(Clock_2), .en(not_1_out), .Q(Q_q));
  Register Q_x (.D(multiplexer_4_out), .C(Clock_2), .en(not_1_out), .Q(Q_x_q));
  LED led_11 (.in(M_q[3]));
  LED led_12 (.in(M_q[2]));
  LED led_13 (.in(Carry_q));
  LED led_14 (.in(AC_q[3]));
  LED led_15 (.in(AC_q[2]));
  LED led_16 (.in(Q_q[3]));
  LED led_17 (.in(Q_q[2]));
  LED led_18 (.in(Q_x_q));
  LED led_19 (.in(M_q[1]));
  LED led_20 (.in(M_q[0]));
  LED led_21 (.in(AC_q[1]));
  LED led_22 (.in(AC_q[0]));
  LED led_23 (.in(Q_q[1]));
  LED led_24 (.in(Q_q[0]));
  Multiplexer #(.Bits(4)) multiplexer_5 (.sel(xnor_1_out), .in_0(M_q), .in_1(4'b0000), .out(multiplexer_5_out));
  Multiplexer #(.Bits(4)) multiplexer_6 (
    .sel(and_1_out), .in_0(multiplexer_5_out), .in_1(not_2_out), .out(multiplexer_6_out));
  assign not_2_out = ~multiplexer_5_out;  // Not not_2, 4 bits wide
  Add #(.Bits(4)) add_1 (.a(multiplexer_6_out), .b(AC_q), .c_i(and_1_out), .s(add_1_s), .c_o(add_1_c_o));
  Multiplexer multiplexer_7 (.sel(Unsigned), .in_0(Q_q[0]), .in_1(1'b0), .out(multiplexer_7_out));
  Multiplexer multiplexer_8 (.sel(Unsigned), .in_0(Q_x_q), .in_1(Q_q[0]), .out(multiplexer_8_out));
  xnor xnor_1 (xnor_1_out, multiplexer_7_out, multiplexer_8_out);
  and and_1 (and_1_out, multiplexer_7_out, ~multiplexer_8_out);  // And
  DipSwitch dipswitch_1 (.out(dipswitch_1_out));
  LED led_25 (.in(multiplexer_7_out));
  LED led_26 (.in(multiplexer_8_out));
  LED led_27 (.in(add_1_s[3]));
  LED led_28 (.in(add_1_s[2]));
  not not_3 (not_3_out, dipswitch_1_out);
  LED led_29 (.in(add_1_s[1]));
  LED led_30 (.in(add_1_s[0]));
  D_FF_AS Rising_Pulse (
    .Set(1'b0), .D(Rising_Pulse_nq), .C(dipswitch_1_out), .Clr(Rising_Pulse_q), .Q(Rising_Pulse_q),
    .nQ(Rising_Pulse_nq));
  D_FF_AS Falling_Pulse (
    .Set(1'b0), .D(Falling_Pulse_nq), .C(not_3_out), .Clr(Falling_Pulse_q), .Q(Falling_Pulse_q),
    .nQ(Falling_Pulse_nq));
  or or_1 (or_1_out, Rising_Pulse_q, Falling_Pulse_q);
  Counter #(.Bits(3)) counter_2 (.en(not_4_out), .C(Clock), .clr(Reset), .out(counter_2_out));  // open: ovf
  Counter #(.Bits(4)) counter_3 (.en(1'b1), .C(or_1_out), .clr(1'b0), .out(counter_3_out));  // open: ovf
  Multiplexer #(.Bits(4)) multiplexer_9 (
    .sel(decoder_2_out_0), .in_0({{2{add_2_s[3]}}, add_2_s[2:1]}), .in_1(4'b0000), .out(multiplexer_9_out));
  Multiplexer #(.Bits(4)) multiplexer_10 (
    .sel(decoder_2_out_0), .in_0({add_2_s[0], Q_2_q[3:1]}), .in_1(B), .out(multiplexer_10_out));
  Multiplexer multiplexer_11 (.sel(decoder_2_out_0), .in_0(Q_2_q[0]), .in_1(1'b0), .out(multiplexer_11_out));
  Decoder #(.Selector_Bits(3)) decoder_2 (
    .sel(counter_2_out), .out_0(decoder_2_out_0), .out_1(decoder_2_out_1), .out_2(decoder_2_out_2),
    .out_3(decoder_2_out_3), .out_4(decoder_2_out_4), .out_5(decoder_2_out_5));  // open: out_6, out_7
  // Probe on counter_3_out
  LED Init_2 (.in(decoder_2_out_0));
  LED Step_1 (.in(decoder_2_out_1));
  LED Step_2 (.in(decoder_2_out_2));
  LED Step_3 (.in(decoder_2_out_3));
  LED Step_4 (.in(decoder_2_out_4));
  LED Done_2 (.in(decoder_2_out_5));
  not not_4 (not_4_out, decoder_2_out_5);
  // Probe on counter_2_out
  LED led_31 (.in(multiplexer_9_out[3]));
  LED led_32 (.in(multiplexer_9_out[2]));
  LED led_33 (.in(multiplexer_9_out[1]));
  LED led_34 (.in(multiplexer_10_out[3]));
  LED led_35 (.in(multiplexer_10_out[2]));
  LED led_36 (.in(multiplexer_10_out[1]));
  Register #(.Bits(4)) M_2 (.D(A), .C(Clock), .en(not_4_out), .Q(M_2_q));
  LED led_37 (.in(multiplexer_9_out[0]));
  Register #(.Bits(4)) AC_2 (.D(multiplexer_9_out), .C(Clock), .en(not_4_out), .Q(AC_2_q));
  LED led_38 (.in(multiplexer_10_out[0]));
  Register #(.Bits(4)) Q_2 (.D(multiplexer_10_out), .C(Clock), .en(not_4_out), .Q(Q_2_q));
  LED led_39 (.in(multiplexer_11_out));
  Register Q_x_2 (.D(multiplexer_11_out), .C(Clock), .en(not_4_out), .Q(Q_x_2_q));
  LED led_40 (.in(M_2_q[3]));
  LED led_41 (.in(AC_2_q[3]));
  LED led_42 (.in(Q_2_q[3]));
  LED led_43 (.in(Q_x_2_q));
  LED led_44 (.in(M_2_q[2]));
  LED led_45 (.in(M_2_q[1]));
  LED led_46 (.in(M_2_q[0]));
  LED led_47 (.in(AC_2_q[2]));
  LED led_48 (.in(AC_2_q[1]));
  LED led_49 (.in(AC_2_q[0]));
  LED led_50 (.in(Q_2_q[2]));
  LED led_51 (.in(Q_2_q[1]));
  LED led_52 (.in(Q_2_q[0]));
  Multiplexer #(.Bits(4)) multiplexer_12 (.sel(xnor_2_out), .in_0(M_2_q), .in_1(4'b0000), .out(multiplexer_12_out));
  assign not_5_out = ~multiplexer_12_out;  // Not not_5, 4 bits wide
  Multiplexer #(.Bits(4)) multiplexer_13 (
    .sel(and_2_out), .in_0(multiplexer_12_out), .in_1(not_5_out), .out(multiplexer_13_out));
  Add #(.Bits(4)) add_2 (.a(multiplexer_13_out), .b(AC_2_q), .c_i(and_2_out), .s(add_2_s));  // open: c_o
  xnor xnor_2 (xnor_2_out, Q_2_q[0], Q_x_2_q);
  and and_2 (and_2_out, Q_2_q[0], ~Q_x_2_q);  // And
  LED led_53 (.in(Q_2_q[0]));
  LED led_54 (.in(Q_x_2_q));
  LED led_55 (.in(add_2_s[3]));
  LED led_56 (.in(add_2_s[2]));
  LED led_57 (.in(add_2_s[1]));
  LED led_58 (.in(add_2_s[0]));

  // Notes on the sheet:
  //   Clock: Hz: 50000
  //   A: default 7
  //   B: default 3
  //   Clock_2: Hz: 50000
  //   A_2: default 7
  //   B_2: default 3
  //   4bit Signed-Multiplication (Booth-Algorithm) modified for unsigned
  //   Operation
  //   00 - ashr
  //   01 - add / ashr
  //   10 - sub / ashr
  //   11 - ashr
  //   4bit Signed-Multiplication (Booth-Algorithm)
  //   - * - = +
  //   - * + = -
  //   + * - = -
  //   + * + = +
  //   if only one operand is neg. then
  //   the result must be also neg.
  //   2*2=4   ->   10 * 10 = 0100
  //   1*1=1   ->   01 * 01 = 0001
  //   -1 * -1 = 1   ->   11 * 11 = 0001
endmodule
