// Digital circuit PipeReg_8bit_single.dig as structural Verilog
module PipeReg_8bit_single (
  input  In1,
  input  Default1,
  input  In2,
  input  Default2,
  input  In3,
  input  Default3,
  input  In4,
  input  Default4,
  input  In5,
  input  Default5,
  input  In6,
  input  Default6,
  input  In7,
  input  Default7,
  input  In8,
  input  Default8,
  input  REG_Clock,
  input  REG_OE,
  input  REG_Clear,
  output Out1,
  output Out2,
  output Out3,
  output Out4,
  output Out5,
  output Out6,
  output Out7,
  output Out8
);

  wire _74245_2_pin11, _74245_2_pin12, _74245_2_pin13, _74245_2_pin14, _74245_2_pin15, _74245_2_pin16,
       _74245_2_pin17, _74245_2_pin18, _74273_1_pin2, _74273_1_pin5, _74273_1_pin6, _74273_1_pin9,
       _74273_1_pin12, _74273_1_pin15, _74273_1_pin16, _74273_1_pin19, pfet_1_d, pfet_2_d, pfet_3_d,
       pfet_4_d, pfet_5_d, pfet_6_d, pfet_7_d, pfet_8_d, pullup_1_out, pullup_2_out, pullup_3_out,
       pullup_4_out, pullup_5_out, pullup_6_out, pullup_7_out, pullup_8_out;

  _74273 _74273_1 (
    .pin1(REG_Clear), .pin2(_74273_1_pin2), .pin3(In1), .pin4(In3), .pin5(_74273_1_pin5),
    .pin6(_74273_1_pin6), .pin7(In5), .pin8(In7), .pin9(_74273_1_pin9), .pin10(1'b0), .pin11(REG_Clock),
    .pin12(_74273_1_pin12), .pin13(In8), .pin14(In6), .pin15(_74273_1_pin15), .pin16(_74273_1_pin16),
    .pin17(In4), .pin18(In2), .pin19(_74273_1_pin19), .pin20(1'b1));
  LED led_1 (.in(_74273_1_pin2));
  LED led_2 (.in(_74273_1_pin5));
  LED led_3 (.in(_74273_1_pin19));
  LED led_4 (.in(_74273_1_pin9));
  LED led_5 (.in(_74273_1_pin6));
  LED led_6 (.in(_74273_1_pin15));
  LED led_7 (.in(_74273_1_pin16));
  PullUp pullup_1 (.out(pullup_1_out));
  PullUp pullup_2 (.out(pullup_2_out));
  NFET nfet_1 (.G(Default1), .D(pullup_1_out), .S(Out1));
  NFET nfet_2 (.G(Default2), .D(pullup_2_out), .S(Out2));
  PFET pfet_1 (.G(Default1), .S(Out1), .D(pfet_1_d));
  PFET pfet_2 (.G(Default2), .S(Out2), .D(pfet_2_d));
  PullDown pulldown_1 (.out(pfet_1_d));
  PullDown pulldown_2 (.out(pfet_2_d));
  _74245 _74245_1 (
    .pin1(1'b1), .pin2(_74273_1_pin2), .pin3(_74273_1_pin19), .pin4(_74273_1_pin5), .pin5(_74273_1_pin16),
    .pin6(_74273_1_pin6), .pin7(_74273_1_pin15), .pin8(_74273_1_pin9), .pin9(_74273_1_pin12), .pin10(1'b0),
    .pin11(Out8), .pin12(Out7), .pin13(Out6), .pin14(Out5), .pin15(Out4), .pin16(Out3), .pin17(Out2),
    .pin18(Out1), .pin19(REG_OE), .pin20(1'b1));
  LED led_8 (.in(_74273_1_pin12));
  PullUp pullup_3 (.out(pullup_3_out));
  PullUp pullup_4 (.out(pullup_4_out));
  NFET nfet_3 (.G(Default3), .D(pullup_3_out), .S(Out3));
  NFET nfet_4 (.G(Default4), .D(pullup_4_out), .S(Out4));
  PFET pfet_3 (.G(Default3), .S(Out3), .D(pfet_3_d));
  PFET pfet_4 (.G(Default4), .S(Out4), .D(pfet_4_d));
  PullDown pulldown_3 (.out(pfet_3_d));
  PullDown pulldown_4 (.out(pfet_4_d));
  PullUp pullup_5 (.out(pullup_5_out));
  PullUp pullup_6 (.out(pullup_6_out));
  NFET nfet_5 (.G(Default5), .D(pullup_5_out), .S(Out5));
  NFET nfet_6 (.G(Default6), .D(pullup_6_out), .S(Out6));
  PFET pfet_5 (.G(Default5), .S(Out5), .D(pfet_5_d));
  PFET pfet_6 (.G(Default6), .S(Out6), .D(pfet_6_d));
  PullDown pulldown_5 (.out(pfet_5_d));
  PullDown pulldown_6 (.out(pfet_6_d));
  PullUp pullup_7 (.out(pullup_7_out));
  PullUp pullup_8 (.out(pullup_8_out));
  NFET nfet_7 (.G(Default7), .D(pullup_7_out), .S(Out7));
  NFET nfet_8 (.G(Default8), .D(pullup_8_out), .S(Out8));
  PFET pfet_7 (.G(Default7), .S(Out7), .D(pfet_7_d));
  PFET pfet_8 (.G(Default8), .S(Out8), .D(pfet_8_d));
  PullDown pulldown_7 (.out(pfet_7_d));
  PullDown pulldown_8 (.out(pfet_8_d));
  _74245 _74245_2 (
    .pin1(1'b1), .pin2(Out1), .pin3(Out2), .pin4(Out3), .pin5(Out4), .pin6(Out5), .pin7(Out6), .pin8(Out7),
    .pin9(Out8), .pin10(1'b0), .pin11(_74245_2_pin11), .pin12(_74245_2_pin12), .pin13(_74245_2_pin13),
    .pin14(_74245_2_pin14), .pin15(_74245_2_pin15), .pin16(_74245_2_pin16), .pin17(_74245_2_pin17),
    .pin18(_74245_2_pin18), .pin19(1'b0), .pin20(1'b1));
  LED u_OUT7 (.in(_74245_2_pin18));
  LED u_OUT6 (.in(_74245_2_pin17));
  LED u_OUT5 (.in(_74245_2_pin16));
  LED u_OUT4 (.in(_74245_2_pin15));
  LED u_OUT3 (.in(_74245_2_pin14));
  LED u_OUT2 (.in(_74245_2_pin13));
  LED u_OUT1 (.in(_74245_2_pin12));
  LED OUT0 (.in(_74245_2_pin11));

  // Notes on the sheet:
  //   D7..0
endmodule
