// Digital circuit PipeReg_EXE.dig as structural Verilog
module PipeReg_EXE (
  input  [4:0] ALU_ctrl_in,
  input  REGin_Clear,
  input  REGin_Clock,
  input  REGin_OE,
  output [4:0] ALU_ctrl_out,
  output REGout_Clock,
  output REGout_OE,
  output REGout_Clear
);

  wire [7:5] pipereg_8bit_1_out, pulldown_1_out;

  PullDown #(.Bits(3)) pulldown_1 (.out(pulldown_1_out));
  PipeReg_8bit pipereg_8bit_1 (
    .In({pulldown_1_out, ALU_ctrl_in}), .Default({8{1'b0}}), .REG_Clock(REGin_Clock), .REG_OE(REGin_OE),
    .REG_Clear(REGin_Clear), .Out({pipereg_8bit_1_out, ALU_ctrl_out}));  // open: Disp

  assign REGout_Clear = REGin_Clear;
  assign REGout_Clock = REGin_Clock;
  assign REGout_OE = REGin_OE;

  // Other names for the same wires on the sheet: Clear = REGin_Clear; Clock = REGin_Clock; OE = REGin_OE

  // Notes on the sheet:
  //   Control
  //   Register
endmodule
