// Digital circuit PipeReg_MEM.dig as structural Verilog
module PipeReg_MEM (
  input  [1:0] MEM_mux_in,
  input  REGin_Clear,
  input  REGin_Clock,
  input  REGin_OE,
  input  [2:0] MEM_sz_in,
  input  MEM_rd_in,
  input  MEM_wr_in,
  output [1:0] MEM_mux_out,
  output REGout_Clock,
  output REGout_OE,
  output REGout_Clear,
  output [2:0] MEM_sz_out,
  output MEM_rd_out,
  output MEM_wr_out
);

  wire [7:7] pipereg_8bit_1_out, pulldown_1_out;

  PullDown pulldown_1 (.out(pulldown_1_out[7]));
  PipeReg_8bit pipereg_8bit_1 (
    .In({pulldown_1_out[7], MEM_wr_in, MEM_rd_in, MEM_sz_in, MEM_mux_in}), .Default({8{1'b0}}),
    .REG_Clock(REGin_Clock), .REG_OE(REGin_OE), .REG_Clear(REGin_Clear),
    .Out({pipereg_8bit_1_out[7], MEM_wr_out, MEM_rd_out, MEM_sz_out, MEM_mux_out}));  // open: Disp

  assign REGout_Clear = REGin_Clear;
  assign REGout_Clock = REGin_Clock;
  assign REGout_OE = REGin_OE;

  // Other names for the same wires on the sheet: Clear = REGin_Clear; Clock = REGin_Clock; OE = REGin_OE

  // Notes on the sheet:
  //   Control
  //   Register
endmodule
