// Digital circuit PipeReg_WB.dig as structural Verilog
module PipeReg_WB (
  input  WB_we_in,
  input  REGin_Clear,
  input  REGin_Clock,
  input  REGin_OE,
  input  [4:0] WB_reg_in,
  output WB_we_out,
  output REGout_Clock,
  output REGout_OE,
  output REGout_Clear,
  output [4:0] WB_reg_out
);

  wire [7:6] pipereg_8bit_1_out, pulldown_1_out;

  PullDown #(.Bits(2)) pulldown_1 (.out(pulldown_1_out));
  PipeReg_8bit pipereg_8bit_1 (
    .In({pulldown_1_out, WB_reg_in, WB_we_in}), .Default({8{1'b0}}), .REG_Clock(REGin_Clock),
    .REG_OE(REGin_OE), .REG_Clear(REGin_Clear), .Out({pipereg_8bit_1_out, WB_reg_out, WB_we_out}));  // open: Disp

  assign REGout_Clear = REGin_Clear;
  assign REGout_Clock = REGin_Clock;
  assign REGout_OE = REGin_OE;

  // Other names for the same wires on the sheet: Clear = REGin_Clear; Clock = REGin_Clock; OE = REGin_OE

  // Notes on the sheet:
  //   Control
  //   Register
endmodule
