// Digital circuit Pipe_ID_EXE.dig as structural Verilog
module Pipe_ID_EXE (
  input  [31:0] PC_in,
  input  REGin_Clear,
  input  REGin_Clock,
  input  REGin_OE,
  input  [31:0] PC_nextin,
  input  [31:0] wdata_in,
  input  [31:0] A_in,
  input  [31:0] B_in,
  input  [31:0] Imm_in,
  output [31:0] PC_out,
  output [31:0] PC_disp,
  output REGout_Clock,
  output REGout_OE,
  output REGout_Clear,
  output [31:0] PC_nextout,
  output [31:0] PC_nextdisp,
  output [31:0] wdata_out,
  output [31:0] wdata_disp,
  output [31:0] A_out,
  output [31:0] A_disp,
  output [31:0] B_out,
  output [31:0] B_disp,
  output [31:0] Imm_out,
  output [31:0] Imm_disp
);

  PipeReg_32bit PC (
    .In(PC_in), .Default({32{1'b0}}), .REG_Clock(REGin_Clock), .REG_OE(REGin_OE), .REG_Clear(REGin_Clear),
    .Out(PC_out), .Disp(PC_disp));
  PipeReg_32bit PC_next (
    .In(PC_nextin), .Default({32{1'b0}}), .REG_Clock(REGin_Clock), .REG_OE(REGin_OE),
    .REG_Clear(REGin_Clear), .Out(PC_nextout), .Disp(PC_nextdisp));
  PipeReg_32bit Mem_wdata (
    .In(wdata_in), .Default({32{1'b0}}), .REG_Clock(REGin_Clock), .REG_OE(REGin_OE), .REG_Clear(REGin_Clear),
    .Out(wdata_out), .Disp(wdata_disp));
  PipeReg_32bit A (
    .In(A_in), .Default({32{1'b0}}), .REG_Clock(REGin_Clock), .REG_OE(REGin_OE), .REG_Clear(REGin_Clear),
    .Out(A_out), .Disp(A_disp));
  PipeReg_32bit B (
    .In(B_in), .Default({32{1'b0}}), .REG_Clock(REGin_Clock), .REG_OE(REGin_OE), .REG_Clear(REGin_Clear),
    .Out(B_out), .Disp(B_disp));
  PipeReg_32bit Imm (
    .In(Imm_in), .Default({32{1'b0}}), .REG_Clock(REGin_Clock), .REG_OE(REGin_OE), .REG_Clear(REGin_Clear),
    .Out(Imm_out), .Disp(Imm_disp));

  assign REGout_Clear = REGin_Clear;
  assign REGout_Clock = REGin_Clock;
  assign REGout_OE = REGin_OE;

  // Other names for the same wires on the sheet: Clear = REGin_Clear; Clock = REGin_Clock; OE = REGin_OE

  // Notes on the sheet:
  //   Control
  //   Register
endmodule
