// Digital circuit RegFile.dig as structural Verilog
module RegFile (
  input  [4:0] Rs1,
  input  [4:0] Rs2,
  input  [4:0] Ws,
  input  Clock,
  input  Reset,
  input  [31:0] Data,
  input  We,
  output [31:0] Rd1,
  output [31:0] Rd2,
  output [31:0] Disp_R0,
  output [29:0] Disp_R1,
  output [29:0] Disp_R2,
  output [29:0] Disp_R3,
  output [29:0] Disp_R4,
  output [29:0] Disp_R5,
  output [29:0] Disp_R6,
  output [29:0] Disp_R7,
  output [29:0] Disp_R8,
  output [29:0] Disp_R9,
  output [29:0] Disp_R10,
  output [29:0] Disp_R11,
  output [29:0] Disp_R12,
  output [29:0] Disp_R13,
  output [29:0] Disp_R14,
  output [29:0] Disp_R15,
  output [29:0] Disp_R16,
  output [29:0] Disp_R17,
  output [29:0] Disp_R18,
  output [29:0] Disp_R19,
  output [29:0] Disp_R20,
  output [29:0] Disp_R21,
  output [29:0] Disp_R22,
  output [29:0] Disp_R23,
  output [29:0] Disp_R24,
  output [29:0] Disp_R25,
  output [29:0] Disp_R26,
  output [29:0] Disp_R27,
  output [29:0] Disp_R28,
  output [29:0] Disp_R29,
  output [29:0] Disp_R30,
  output [29:0] Disp_R31
);

  wire demultiplexer_1_out_0, demultiplexer_1_out_1, demultiplexer_1_out_2, demultiplexer_1_out_3,
       demultiplexer_1_out_4, demultiplexer_1_out_5, demultiplexer_1_out_6, demultiplexer_1_out_7,
       demultiplexer_1_out_8, demultiplexer_1_out_9, demultiplexer_1_out_10, demultiplexer_1_out_11,
       demultiplexer_1_out_12, demultiplexer_1_out_13, demultiplexer_1_out_14, demultiplexer_1_out_15,
       demultiplexer_1_out_16, demultiplexer_1_out_17, demultiplexer_1_out_18, demultiplexer_1_out_19,
       demultiplexer_1_out_20, demultiplexer_1_out_21, demultiplexer_1_out_22, demultiplexer_1_out_23,
       demultiplexer_1_out_24, demultiplexer_1_out_25, demultiplexer_1_out_26, demultiplexer_1_out_27,
       demultiplexer_1_out_28, demultiplexer_1_out_29, demultiplexer_1_out_30, demultiplexer_1_out_31,
       demultiplexer_2_out_0, demultiplexer_2_out_1, demultiplexer_2_out_2, demultiplexer_2_out_3,
       demultiplexer_2_out_4, demultiplexer_2_out_5, demultiplexer_2_out_6, demultiplexer_2_out_7,
       demultiplexer_2_out_8, demultiplexer_2_out_9, demultiplexer_2_out_10, demultiplexer_2_out_11,
       demultiplexer_2_out_12, demultiplexer_2_out_13, demultiplexer_2_out_14, demultiplexer_2_out_15,
       demultiplexer_2_out_16, demultiplexer_2_out_17, demultiplexer_2_out_18, demultiplexer_2_out_19,
       demultiplexer_2_out_20, demultiplexer_2_out_21, demultiplexer_2_out_22, demultiplexer_2_out_23,
       demultiplexer_2_out_24, demultiplexer_2_out_25, demultiplexer_2_out_26, demultiplexer_2_out_27,
       demultiplexer_2_out_28, demultiplexer_2_out_29, demultiplexer_2_out_30, demultiplexer_2_out_31,
       demultiplexer_3_out_0, demultiplexer_3_out_1, demultiplexer_3_out_2, demultiplexer_3_out_3,
       demultiplexer_3_out_4, demultiplexer_3_out_5, demultiplexer_3_out_6, demultiplexer_3_out_7,
       demultiplexer_3_out_8, demultiplexer_3_out_9, demultiplexer_3_out_10, demultiplexer_3_out_11,
       demultiplexer_3_out_12, demultiplexer_3_out_13, demultiplexer_3_out_14, demultiplexer_3_out_15,
       demultiplexer_3_out_16, demultiplexer_3_out_17, demultiplexer_3_out_18, demultiplexer_3_out_19,
       demultiplexer_3_out_20, demultiplexer_3_out_21, demultiplexer_3_out_22, demultiplexer_3_out_23,
       demultiplexer_3_out_24, demultiplexer_3_out_25, demultiplexer_3_out_26, demultiplexer_3_out_27,
       demultiplexer_3_out_28, demultiplexer_3_out_29, demultiplexer_3_out_30, demultiplexer_3_out_31,
       driver_1_out, driver_3_out, driver_5_out, driver_6_out, driver_8_out, not_1_out,
       regfile_reg32bit_8_p14, regfile_reg32bit_8_p15, regfile_reg32bit_16_p10, regfile_reg32bit_16_p11;
  wire [31:0] driver_2_out, driver_4_out, driver_7_out, regfile_reg32bit_8_p16, regfile_reg32bit_16_p12;

  assign driver_1_out = 1'b1 ? Reset : 1'bz;  // Driver driver_1
  assign driver_2_out = 1'b1 ? Data : 32'bz;  // Driver driver_2
  not not_1 (not_1_out, Clock);
  Demultiplexer #(.Selector_Bits(5)) demultiplexer_1 (
    .sel(Ws), .in(We), .out_0(demultiplexer_1_out_0), .out_1(demultiplexer_1_out_1),
    .out_2(demultiplexer_1_out_2), .out_3(demultiplexer_1_out_3), .out_4(demultiplexer_1_out_4),
    .out_5(demultiplexer_1_out_5), .out_6(demultiplexer_1_out_6), .out_7(demultiplexer_1_out_7),
    .out_8(demultiplexer_1_out_8), .out_9(demultiplexer_1_out_9), .out_10(demultiplexer_1_out_10),
    .out_11(demultiplexer_1_out_11), .out_12(demultiplexer_1_out_12), .out_13(demultiplexer_1_out_13),
    .out_14(demultiplexer_1_out_14), .out_15(demultiplexer_1_out_15), .out_16(demultiplexer_1_out_16),
    .out_17(demultiplexer_1_out_17), .out_18(demultiplexer_1_out_18), .out_19(demultiplexer_1_out_19),
    .out_20(demultiplexer_1_out_20), .out_21(demultiplexer_1_out_21), .out_22(demultiplexer_1_out_22),
    .out_23(demultiplexer_1_out_23), .out_24(demultiplexer_1_out_24), .out_25(demultiplexer_1_out_25),
    .out_26(demultiplexer_1_out_26), .out_27(demultiplexer_1_out_27), .out_28(demultiplexer_1_out_28),
    .out_29(demultiplexer_1_out_29), .out_30(demultiplexer_1_out_30), .out_31(demultiplexer_1_out_31));
  Demultiplexer #(.Selector_Bits(5), .Default(1)) demultiplexer_2 (
    .sel(Rs2), .in(1'b0), .out_0(demultiplexer_2_out_0), .out_1(demultiplexer_2_out_1),
    .out_2(demultiplexer_2_out_2), .out_3(demultiplexer_2_out_3), .out_4(demultiplexer_2_out_4),
    .out_5(demultiplexer_2_out_5), .out_6(demultiplexer_2_out_6), .out_7(demultiplexer_2_out_7),
    .out_8(demultiplexer_2_out_8), .out_9(demultiplexer_2_out_9), .out_10(demultiplexer_2_out_10),
    .out_11(demultiplexer_2_out_11), .out_12(demultiplexer_2_out_12), .out_13(demultiplexer_2_out_13),
    .out_14(demultiplexer_2_out_14), .out_15(demultiplexer_2_out_15), .out_16(demultiplexer_2_out_16),
    .out_17(demultiplexer_2_out_17), .out_18(demultiplexer_2_out_18), .out_19(demultiplexer_2_out_19),
    .out_20(demultiplexer_2_out_20), .out_21(demultiplexer_2_out_21), .out_22(demultiplexer_2_out_22),
    .out_23(demultiplexer_2_out_23), .out_24(demultiplexer_2_out_24), .out_25(demultiplexer_2_out_25),
    .out_26(demultiplexer_2_out_26), .out_27(demultiplexer_2_out_27), .out_28(demultiplexer_2_out_28),
    .out_29(demultiplexer_2_out_29), .out_30(demultiplexer_2_out_30), .out_31(demultiplexer_2_out_31));
  Demultiplexer #(.Selector_Bits(5), .Default(1)) demultiplexer_3 (
    .sel(Rs1), .in(1'b0), .out_0(demultiplexer_3_out_0), .out_1(demultiplexer_3_out_1),
    .out_2(demultiplexer_3_out_2), .out_3(demultiplexer_3_out_3), .out_4(demultiplexer_3_out_4),
    .out_5(demultiplexer_3_out_5), .out_6(demultiplexer_3_out_6), .out_7(demultiplexer_3_out_7),
    .out_8(demultiplexer_3_out_8), .out_9(demultiplexer_3_out_9), .out_10(demultiplexer_3_out_10),
    .out_11(demultiplexer_3_out_11), .out_12(demultiplexer_3_out_12), .out_13(demultiplexer_3_out_13),
    .out_14(demultiplexer_3_out_14), .out_15(demultiplexer_3_out_15), .out_16(demultiplexer_3_out_16),
    .out_17(demultiplexer_3_out_17), .out_18(demultiplexer_3_out_18), .out_19(demultiplexer_3_out_19),
    .out_20(demultiplexer_3_out_20), .out_21(demultiplexer_3_out_21), .out_22(demultiplexer_3_out_22),
    .out_23(demultiplexer_3_out_23), .out_24(demultiplexer_3_out_24), .out_25(demultiplexer_3_out_25),
    .out_26(demultiplexer_3_out_26), .out_27(demultiplexer_3_out_27), .out_28(demultiplexer_3_out_28),
    .out_29(demultiplexer_3_out_29), .out_30(demultiplexer_3_out_30), .out_31(demultiplexer_3_out_31));
  assign driver_3_out = 1'b1 ? driver_1_out : 1'bz;  // Driver driver_3
  assign driver_4_out = 1'b1 ? driver_2_out : 32'bz;  // Driver driver_4
  assign driver_5_out = 1'b1 ? not_1_out : 1'bz;  // Driver driver_5
  // RegFile_Reg32bit regfile_reg32bit_1: pin names not known; wires that end beside it: demultiplexer_1_out_0, demultiplexer_3_out_4, demultiplexer_2_out_4, driver_4_out, demultiplexer_1_out_4, driver_5_out, driver_3_out, Disp_R4, Rd1, Rd2
  // RegFile_Reg32bit regfile_reg32bit_2: pin names not known; wires that end beside it: demultiplexer_3_out_8, demultiplexer_2_out_8, driver_4_out, demultiplexer_1_out_8, driver_5_out, driver_3_out, Disp_R8, Rd1, Rd2
  // RegFile_Reg32bit regfile_reg32bit_3: pin names not known; wires that end beside it: demultiplexer_3_out_12, demultiplexer_2_out_12, driver_4_out, demultiplexer_1_out_12, driver_5_out, driver_3_out, Disp_R12, Rd1, Rd2
  // RegFile_Reg32bit regfile_reg32bit_4: pin names not known; wires that end beside it: demultiplexer_3_out_16, demultiplexer_2_out_16, driver_4_out, demultiplexer_1_out_16, driver_5_out, driver_3_out, Disp_R16, Rd1, Rd2
  // RegFile_Reg32bit regfile_reg32bit_5: pin names not known; wires that end beside it: demultiplexer_3_out_20, demultiplexer_2_out_20, driver_4_out, demultiplexer_1_out_20, driver_5_out, driver_3_out, Disp_R20, Rd1, Rd2
  // RegFile_Reg32bit regfile_reg32bit_6: pin names not known; wires that end beside it: demultiplexer_3_out_24, demultiplexer_2_out_24, driver_4_out, demultiplexer_1_out_24, driver_5_out, driver_3_out, Disp_R24, Rd1, Rd2
  // RegFile_Reg32bit regfile_reg32bit_7: pin names not known; wires that end beside it: demultiplexer_3_out_28, demultiplexer_2_out_28, driver_4_out, demultiplexer_1_out_28, driver_5_out, driver_3_out, Disp_R28, Rd1, Rd2, Rd1, Rd2
  PullDown #(.Bits(32)) pulldown_1 (.out(Disp_R0));
  PullDown #(.Bits(32)) pulldown_2 (.out(Rd2));
  PullDown #(.Bits(32)) pulldown_3 (.out(Rd1));
  assign driver_6_out = 1'b1 ? driver_1_out : 1'bz;  // Driver driver_6
  assign driver_7_out = 1'b1 ? driver_2_out : 32'bz;  // Driver driver_7
  assign driver_8_out = 1'b1 ? not_1_out : 1'bz;  // Driver driver_8
  // RegFile_Reg32bit regfile_reg32bit_8: pin names not known; wires that end beside it: demultiplexer_3_out_0, driver_6_out, driver_8_out, driver_7_out, demultiplexer_3_out_1, demultiplexer_2_out_1, driver_7_out, demultiplexer_1_out_1, driver_8_out, driver_6_out, Disp_R1, Rd1, Rd2, regfile_reg32bit_8_p14, regfile_reg32bit_8_p15, regfile_reg32bit_8_p16
  // RegFile_Reg32bit regfile_reg32bit_9: pin names not known; wires that end beside it: demultiplexer_3_out_5, demultiplexer_2_out_5, driver_7_out, demultiplexer_1_out_5, driver_8_out, driver_6_out, Disp_R5, Rd1, Rd2
  // RegFile_Reg32bit regfile_reg32bit_10: pin names not known; wires that end beside it: demultiplexer_3_out_9, demultiplexer_2_out_9, driver_7_out, demultiplexer_1_out_9, driver_8_out, driver_6_out, Disp_R9, Rd1, Rd2
  // RegFile_Reg32bit regfile_reg32bit_11: pin names not known; wires that end beside it: demultiplexer_3_out_13, demultiplexer_2_out_13, driver_7_out, demultiplexer_1_out_13, driver_8_out, driver_6_out, Disp_R13, Rd1, Rd2
  // RegFile_Reg32bit regfile_reg32bit_12: pin names not known; wires that end beside it: demultiplexer_3_out_17, demultiplexer_2_out_17, driver_7_out, demultiplexer_1_out_17, driver_8_out, driver_6_out, Disp_R17, Rd1, Rd2
  // RegFile_Reg32bit regfile_reg32bit_13: pin names not known; wires that end beside it: demultiplexer_3_out_21, demultiplexer_2_out_21, driver_7_out, demultiplexer_1_out_21, driver_8_out, driver_6_out, Disp_R21, Rd1, Rd2
  // RegFile_Reg32bit regfile_reg32bit_14: pin names not known; wires that end beside it: demultiplexer_3_out_25, demultiplexer_2_out_25, driver_7_out, demultiplexer_1_out_25, driver_8_out, driver_6_out, Disp_R25, Rd1, Rd2
  // RegFile_Reg32bit regfile_reg32bit_15: pin names not known; wires that end beside it: demultiplexer_3_out_29, demultiplexer_2_out_29, driver_7_out, demultiplexer_1_out_29, driver_8_out, driver_6_out, Disp_R29, Rd1, Rd2, Rd1, Rd2
  assign regfile_reg32bit_8_p15 = 1'b1 ? not_1_out : 1'bz;  // Driver driver_9
  assign regfile_reg32bit_8_p14 = 1'b1 ? driver_1_out : 1'bz;  // Driver driver_10
  assign regfile_reg32bit_8_p16 = 1'b1 ? driver_2_out : 32'bz;  // Driver driver_11
  // RegFile_Reg32bit regfile_reg32bit_16: pin names not known; wires that end beside it: demultiplexer_3_out_2, demultiplexer_2_out_2, regfile_reg32bit_8_p16, demultiplexer_1_out_2, regfile_reg32bit_8_p15, regfile_reg32bit_8_p14, Disp_R2, Rd1, Rd2, regfile_reg32bit_16_p10, regfile_reg32bit_16_p11, regfile_reg32bit_16_p12
  // RegFile_Reg32bit regfile_reg32bit_17: pin names not known; wires that end beside it: demultiplexer_3_out_6, demultiplexer_2_out_6, regfile_reg32bit_8_p16, demultiplexer_1_out_6, regfile_reg32bit_8_p15, regfile_reg32bit_8_p14, Disp_R6, Rd1, Rd2
  // RegFile_Reg32bit regfile_reg32bit_18: pin names not known; wires that end beside it: demultiplexer_3_out_10, demultiplexer_2_out_10, regfile_reg32bit_8_p16, demultiplexer_1_out_10, regfile_reg32bit_8_p15, regfile_reg32bit_8_p14, Disp_R10, Rd1, Rd2
  // RegFile_Reg32bit regfile_reg32bit_19: pin names not known; wires that end beside it: demultiplexer_3_out_14, demultiplexer_2_out_14, regfile_reg32bit_8_p16, demultiplexer_1_out_14, regfile_reg32bit_8_p15, regfile_reg32bit_8_p14, Disp_R14, Rd1, Rd2
  // RegFile_Reg32bit regfile_reg32bit_20: pin names not known; wires that end beside it: demultiplexer_3_out_18, demultiplexer_2_out_18, regfile_reg32bit_8_p16, demultiplexer_1_out_18, regfile_reg32bit_8_p15, regfile_reg32bit_8_p14, Disp_R18, Rd1, Rd2
  // RegFile_Reg32bit regfile_reg32bit_21: pin names not known; wires that end beside it: demultiplexer_3_out_22, demultiplexer_2_out_22, regfile_reg32bit_8_p16, demultiplexer_1_out_22, regfile_reg32bit_8_p15, regfile_reg32bit_8_p14, Disp_R22, Rd1, Rd2
  // RegFile_Reg32bit regfile_reg32bit_22: pin names not known; wires that end beside it: demultiplexer_3_out_26, demultiplexer_2_out_26, regfile_reg32bit_8_p16, demultiplexer_1_out_26, regfile_reg32bit_8_p15, regfile_reg32bit_8_p14, Disp_R26, Rd1, Rd2
  // RegFile_Reg32bit regfile_reg32bit_23: pin names not known; wires that end beside it: demultiplexer_3_out_30, demultiplexer_2_out_30, regfile_reg32bit_8_p16, demultiplexer_1_out_30, regfile_reg32bit_8_p15, regfile_reg32bit_8_p14, Disp_R30, Rd1, Rd2, Rd1, Rd2
  assign regfile_reg32bit_16_p11 = 1'b1 ? not_1_out : 1'bz;  // Driver driver_12
  assign regfile_reg32bit_16_p10 = 1'b1 ? driver_1_out : 1'bz;  // Driver driver_13
  assign regfile_reg32bit_16_p12 = 1'b1 ? driver_2_out : 32'bz;  // Driver driver_14
  // RegFile_Reg32bit regfile_reg32bit_24: pin names not known; wires that end beside it: demultiplexer_3_out_3, demultiplexer_2_out_3, regfile_reg32bit_16_p12, demultiplexer_1_out_3, regfile_reg32bit_16_p11, regfile_reg32bit_16_p10, Disp_R3, Rd1, Rd2
  // RegFile_Reg32bit regfile_reg32bit_25: pin names not known; wires that end beside it: demultiplexer_3_out_7, demultiplexer_2_out_7, regfile_reg32bit_16_p12, demultiplexer_1_out_7, regfile_reg32bit_16_p11, regfile_reg32bit_16_p10, Disp_R7, Rd1, Rd2
  // RegFile_Reg32bit regfile_reg32bit_26: pin names not known; wires that end beside it: demultiplexer_3_out_11, demultiplexer_2_out_11, regfile_reg32bit_16_p12, demultiplexer_1_out_11, regfile_reg32bit_16_p11, regfile_reg32bit_16_p10, Disp_R11, Rd1, Rd2
  // RegFile_Reg32bit regfile_reg32bit_27: pin names not known; wires that end beside it: demultiplexer_3_out_15, demultiplexer_2_out_15, regfile_reg32bit_16_p12, demultiplexer_1_out_15, regfile_reg32bit_16_p11, regfile_reg32bit_16_p10, Disp_R15, Rd1, Rd2
  // RegFile_Reg32bit regfile_reg32bit_28: pin names not known; wires that end beside it: demultiplexer_3_out_19, demultiplexer_2_out_19, regfile_reg32bit_16_p12, demultiplexer_1_out_19, regfile_reg32bit_16_p11, regfile_reg32bit_16_p10, Disp_R19, Rd1, Rd2
  // RegFile_Reg32bit regfile_reg32bit_29: pin names not known; wires that end beside it: demultiplexer_3_out_23, demultiplexer_2_out_23, regfile_reg32bit_16_p12, demultiplexer_1_out_23, regfile_reg32bit_16_p11, regfile_reg32bit_16_p10, Disp_R23, Rd1, Rd2
  // RegFile_Reg32bit regfile_reg32bit_30: pin names not known; wires that end beside it: demultiplexer_3_out_27, demultiplexer_2_out_27, regfile_reg32bit_16_p12, demultiplexer_1_out_27, regfile_reg32bit_16_p11, regfile_reg32bit_16_p10, Disp_R27, Rd1, Rd2
  // RegFile_Reg32bit regfile_reg32bit_31: pin names not known; wires that end beside it: driver_1_out, demultiplexer_3_out_31, demultiplexer_2_out_31, regfile_reg32bit_16_p12, demultiplexer_1_out_31, regfile_reg32bit_16_p11, regfile_reg32bit_16_p10, Disp_R31, Rd1, Rd2, Rd1, Rd2
  // Pins of 30 and 32 bits meet at Disp_R0

  // Notes on the sheet:
  //   Line-Driver: 32x
  //   Line-Driver: 1x
  //   R0 (Zero)
endmodule
