// Digital circuit Reset.dig as structural Verilog
module Reset (
  input  Clock,
  input  Reset_In,
  output Reset_Out
);

  wire _74193_1_pin2, _74193_1_pin3, _74193_1_pin6, _74193_1_pin7, _74193_1_pin13, nand_1_out, nand_2_out;
  wire [3:0] _74193_1_pin9;

  nand nand_1 (nand_1_out, Clock, nand_2_out);
  LED led_1 (.in(_74193_1_pin7));
  LED led_2 (.in(_74193_1_pin3));
  LED led_3 (.in(_74193_1_pin2));
  LED led_4 (.in(_74193_1_pin6));
  _74193 _74193_1 (
    .pin1(_74193_1_pin9[1]), .pin2(_74193_1_pin2), .pin3(_74193_1_pin3), .pin4(nand_1_out), .pin5(1'b1),
    .pin6(_74193_1_pin6), .pin7(_74193_1_pin7), .pin8(1'b0), .pin9(_74193_1_pin9[3]),
    .pin10(_74193_1_pin9[2]), .pin11(Reset_In), .pin13(_74193_1_pin13), .pin14(1'b0),
    .pin15(_74193_1_pin9[0]), .pin16(1'b1));  // open: pin12
  DipSwitch dipswitch_1 (.out(_74193_1_pin9[3]));
  DipSwitch dipswitch_2 (.out(_74193_1_pin9[2]));
  DipSwitch #(.dipDefault("true")) dipswitch_3 (.out(_74193_1_pin9[1]));
  DipSwitch #(.dipDefault("true")) dipswitch_4 (.out(_74193_1_pin9[0]));
  // Probe on _74193_1_pin9
  nand nand_2 (nand_2_out, Reset_In, Reset_Out);
  nand nand_3 (Reset_Out, nand_2_out, _74193_1_pin13);
  // PolarityAwareLED polarityawareled_1: pin names not known; wires that end beside it: Reset_Out, nand_2_out, 1'b1
  _7400 _7400_1 (
    .pin1(1'b0), .pin2(1'b0), .pin4(1'b0), .pin5(1'b0), .pin7(1'b0), .pin9(1'b0), .pin10(1'b0), .pin12(1'b0),
    .pin13(1'b0), .pin14(1'b1));  // open: pin3, pin6, pin8, pin11
  // NAnd nand_4 has open pins: In_1=1'b0, In_2=1'b0, out=open

  // Notes on the sheet:
  //   Num of Clock-Cycles
endmodule
